// Logisim project dunk.circ as structural Verilog
module main (
  input  SI_mode
);

  wire button_1_out, clock_1_out, control_box_1_clock_out, control_box_1_out_13, control_box_1_reset_out,
       control_unit_1_load, control_unit_1_pause, controlled_buffer_1_out, controlled_buffer_2_out,
       controlled_buffer_3_out, controlled_buffer_4_out, fast_printer_1_active, fast_printer_1_send,
       instruction_printer_1_clock_out, instruction_printer_1_reset_out, io_pins_4_1_out_11,
       io_pins_4_1_out_12, io_pins_4_1_out_13, io_pins_4_1_out_14, io_pins_4_1_out_15, io_pins_4_1_out_16,
       io_pins_4_1_out_17, io_pins_4_1_out_18, mem_ctrl_1_mem_write, mem_ctrl_1_reg_write, pause_out,
       reset_out, resume_out, run_instr_out, toggle_debug_out;
  wire [1:0] mem_ctrl_1_reg_select;
  wire [6:0] fast_printer_1_data_out, instruction_printer_1_ascii_out;
  wire [7:0] input_pins_8_1_out_9;
  wire [11:0] mem_ctrl_1_rom_addr_out;
  wire [15:0] addr_bus_controller_1_addr_bus_out, alu_1_p7, control_bus_controller_1_control_bus_1,
       control_bus_controller_1_control_bus_2, control_unit_1_addr_bus_out, control_unit_1_control_bus_1_out,
       control_unit_1_control_bus_2_out, control_unit_1_current_instr, control_unit_1_data_bus_out,
       control_unit_1_tmpc_out, control_unit_1_to_pk, data_bus_controller_1_data_bus_out,
       fast_printer_1_addr_out, firmware_data, io_pins_4_1_data_bus_out, mem_ctrl_1_data_bus_out,
       mem_ctrl_1_data_to_mem, mem_ctrl_1_data_to_reg, mem_ctrl_1_mem_addr_out, mmio_registers_1_out_7,
       mmio_registers_1_value_out, ram_1_dout, register_unit_1_addr_bus_out, register_unit_1_alu1_out,
       register_unit_1_alu2_out, register_unit_1_data_bus_out, special_registers_1_addr_bus_out,
       special_registers_1_data_bus_out, special_registers_1_offset_out, special_registers_1_program_kounter,
       special_registers_1_stack_pointer;

  Button run_instr (.out(run_instr_out));
  Button pause (.out(pause_out));
  Button resume (.out(resume_out));
  Button reset (.out(reset_out));
  Clock clock_1 (.out(clock_1_out));
  control_box control_box_1 (
    .instr(control_unit_1_current_instr), .clock_in(clock_1_out), .reset_in(reset_out),
    .quick_instruction(run_instr_out), .SI_mode(SI_mode),
    .program_kounter(special_registers_1_program_kounter), .pause(pause_out),
    .control_bus_1(control_bus_controller_1_control_bus_1), .ctl_unit_pause(control_unit_1_pause),
    .resume(resume_out), .out_13(control_box_1_out_13), .clock_out(control_box_1_clock_out),
    .reset_out(control_box_1_reset_out));
  LED led_1 (.in(control_box_1_out_13));
  Button toggle_debug (.out(toggle_debug_out));
  control_bus_controller control_bus_controller_1 (
    .control_1(control_unit_1_control_bus_1_out), .running(control_box_1_out_13),
    .control_2(control_unit_1_control_bus_2_out), .clock(control_box_1_clock_out),
    .reset(control_box_1_reset_out), .control_bus_1(control_bus_controller_1_control_bus_1),
    .control_bus_2(control_bus_controller_1_control_bus_2));
  data_bus_controller data_bus_controller_1 (
    .control_bus_2(control_bus_controller_1_control_bus_2), .clock(control_box_1_clock_out),
    .reset(control_box_1_reset_out), .control_bus_1(control_bus_controller_1_control_bus_1),
    .addr_bus_in(addr_bus_controller_1_addr_bus_out), .control_unit_in(control_unit_1_data_bus_out),
    .registers_in(register_unit_1_data_bus_out), .special_registers_in(alu_1_p7),
    .ALU_in(special_registers_1_data_bus_out), .memory_in(mem_ctrl_1_data_bus_out),
    .io_in(io_pins_4_1_data_bus_out), .data_bus_out(data_bus_controller_1_data_bus_out));
  addr_bus_controller addr_bus_controller_1 (
    .control_bus_1(control_bus_controller_1_control_bus_1),
    .control_bus_2(control_bus_controller_1_control_bus_2), .clock(control_box_1_clock_out),
    .reset(control_box_1_reset_out), .data_bus_in(data_bus_controller_1_data_bus_out),
    .control_unit_in(control_unit_1_addr_bus_out), .registers_in(register_unit_1_addr_bus_out),
    .special_registers_in(special_registers_1_addr_bus_out), .addr_bus_out(addr_bus_controller_1_addr_bus_out));
  instruction_printer instruction_printer_1 (
    .enable(toggle_debug_out), .data_bus(data_bus_controller_1_data_bus_out), .load(control_unit_1_load),
    .clk(control_box_1_clock_out), .reset(control_box_1_reset_out),
    .control_bus_1(control_bus_controller_1_control_bus_1),
    .control_bus_2(control_bus_controller_1_control_bus_2), .SI_mode(SI_mode),
    .pk(special_registers_1_program_kounter), .real_addr(mem_ctrl_1_mem_addr_out),
    .instr(control_unit_1_current_instr), .tmpc(control_unit_1_tmpc_out),
    .ascii_out(instruction_printer_1_ascii_out), .clock_out(instruction_printer_1_clock_out),
    .reset_out(instruction_printer_1_reset_out));
  TTY #(.rows(1)) tty_1 (
    .data(instruction_printer_1_ascii_out), .clk(instruction_printer_1_clock_out),
    .clr(instruction_printer_1_reset_out));  // open: we
  control_unit control_unit_1 (
    .stack_pointer(special_registers_1_stack_pointer), .addr_bus(addr_bus_controller_1_addr_bus_out),
    .control_bus_1(control_bus_controller_1_control_bus_1),
    .control_bus_2(control_bus_controller_1_control_bus_2), .clock(control_box_1_clock_out),
    .reset(control_box_1_reset_out), .RAM_direct(mem_ctrl_1_data_bus_out),
    .data_bus_in(data_bus_controller_1_data_bus_out), .pause_after_instruction(SI_mode),
    .stall(fast_printer_1_active), .interrupt_pins(input_pins_8_1_out_9),
    .control_bus_1_out(control_unit_1_control_bus_1_out),
    .control_bus_2_out(control_unit_1_control_bus_2_out), .current_instr(control_unit_1_current_instr),
    .tmpc_out(control_unit_1_tmpc_out), .data_bus_out(control_unit_1_data_bus_out),
    .addr_bus_out(control_unit_1_addr_bus_out), .to_pk(control_unit_1_to_pk), .pause(control_unit_1_pause),
    .load(control_unit_1_load));
  input_pins_8 input_pins_8_1 (
    .in_8(button_1_out), .out_9(input_pins_8_1_out_9));  // open: in_1, in_2, in_3, in_4, in_5, in_6, in_7
  Button button_1 (.out(button_1_out));
  register_unit register_unit_1 (
    .data_bus_in(data_bus_controller_1_data_bus_out), .clock(control_box_1_clock_out),
    .reset(control_box_1_reset_out), .control_bus_1(control_bus_controller_1_control_bus_1),
    .control_bus_2(control_bus_controller_1_control_bus_2), .data_bus_out(register_unit_1_data_bus_out),
    .addr_bus_out(register_unit_1_addr_bus_out), .alu1_out(register_unit_1_alu1_out),
    .alu2_out(register_unit_1_alu2_out));
  // ALU alu_1: pin names not known; wires that end beside it: control_bus_controller_1_control_bus_1, control_bus_controller_1_control_bus_2, register_unit_1_alu1_out, register_unit_1_alu2_out, control_box_1_clock_out, control_box_1_reset_out, alu_1_p7
  assign controlled_buffer_1_out = io_pins_4_1_out_12 ? io_pins_4_1_out_11 : 1'bz;  // Controlled_Buffer controlled_buffer_1
  assign controlled_buffer_2_out = io_pins_4_1_out_14 ? io_pins_4_1_out_13 : 1'bz;  // Controlled_Buffer controlled_buffer_2
  assign controlled_buffer_3_out = io_pins_4_1_out_16 ? io_pins_4_1_out_15 : 1'bz;  // Controlled_Buffer controlled_buffer_3
  special_registers special_registers_1 (
    .control_bus_1(control_bus_controller_1_control_bus_1),
    .control_bus_2(control_bus_controller_1_control_bus_2), .temp_register(control_unit_1_to_pk),
    .clock(control_box_1_clock_out), .reset(control_box_1_reset_out),
    .data_bus_in(data_bus_controller_1_data_bus_out), .program_kounter(special_registers_1_program_kounter),
    .data_bus_out(special_registers_1_data_bus_out), .addr_bus_out(special_registers_1_addr_bus_out),
    .stack_pointer(special_registers_1_stack_pointer), .offset_out(special_registers_1_offset_out));  // open: sp_reset_value
  io_pins_4 io_pins_4_1 (
    .in_8(controlled_buffer_3_out), .clock(control_box_1_clock_out), .reset(control_box_1_reset_out),
    .in_9(controlled_buffer_4_out), .control_bus(control_bus_controller_1_control_bus_1),
    .in_6(controlled_buffer_1_out), .data_bus_in(data_bus_controller_1_data_bus_out),
    .in_7(controlled_buffer_2_out), .addr_bus_in(addr_bus_controller_1_addr_bus_out),
    .out_15(io_pins_4_1_out_15), .out_16(io_pins_4_1_out_16), .out_17(io_pins_4_1_out_17),
    .out_18(io_pins_4_1_out_18), .data_bus_out(io_pins_4_1_data_bus_out), .out_11(io_pins_4_1_out_11),
    .out_12(io_pins_4_1_out_12), .out_13(io_pins_4_1_out_13), .out_14(io_pins_4_1_out_14));
  assign controlled_buffer_4_out = io_pins_4_1_out_18 ? io_pins_4_1_out_17 : 1'bz;  // Controlled_Buffer controlled_buffer_4
  mmio_registers mmio_registers_1 (
    .write(mem_ctrl_1_reg_write), .clock(control_box_1_clock_out), .reset(control_box_1_reset_out),
    .data_in(mem_ctrl_1_data_to_reg), .reg_select(mem_ctrl_1_reg_select), .out_7(mmio_registers_1_out_7),
    .value_out(mmio_registers_1_value_out));  // open: out_8, out_9, out_10
  RAM #(.addrWidth(16), .dataWidth(16), .enables("line")) ram_1 (
    .addr(mem_ctrl_1_mem_addr_out), .we(mem_ctrl_1_mem_write), .clk(control_box_1_clock_out),
    .din(mem_ctrl_1_data_to_mem), .dout(ram_1_dout));
  mem_ctrl mem_ctrl_1 (
    .data_bus_in(data_bus_controller_1_data_bus_out), .addr_in(addr_bus_controller_1_addr_bus_out),
    .offset_in(special_registers_1_offset_out), .pk_in(special_registers_1_program_kounter),
    .tmpc_in(control_unit_1_tmpc_out), .sp_in(special_registers_1_stack_pointer), .mem_in(ram_1_dout),
    .rom_in(firmware_data), .mmio_reg_in(mmio_registers_1_value_out),
    .control_bus_1(control_bus_controller_1_control_bus_1),
    .control_bus_2(control_bus_controller_1_control_bus_2), .clock(control_box_1_clock_out),
    .reset(control_box_1_reset_out), .override(fast_printer_1_active),
    .override_addr(fast_printer_1_addr_out), .mem_addr_out(mem_ctrl_1_mem_addr_out),
    .rom_addr_out(mem_ctrl_1_rom_addr_out), .reg_select(mem_ctrl_1_reg_select),
    .data_to_reg(mem_ctrl_1_data_to_reg), .reg_write(mem_ctrl_1_reg_write),
    .data_bus_out(mem_ctrl_1_data_bus_out), .data_to_mem(mem_ctrl_1_data_to_mem),
    .mem_write(mem_ctrl_1_mem_write));  // open: override_data
  ROM #(.addrWidth(12), .dataWidth(16)) firmware (.addr(mem_ctrl_1_rom_addr_out), .data(firmware_data));
  fast_printer fast_printer_1 (
    .clk(control_box_1_clock_out), .reset(control_box_1_reset_out), .enable(controlled_buffer_4_out),
    .addr(mmio_registers_1_out_7), .data_in(mem_ctrl_1_data_bus_out), .addr_out(fast_printer_1_addr_out),
    .active(fast_printer_1_active), .data_out(fast_printer_1_data_out), .send(fast_printer_1_send));
  TTY tty_2 (.data(fast_printer_1_data_out), .clk(fast_printer_1_send), .clr(control_box_1_reset_out));  // open: we

  // Notes on the sheet:
  //   David's Universal Number Kounter
  //   contents of firmware (hex, n*v repeats v):
  //   0 0 0 f009 f01d 4*0 8011 f010 9 25 30 1 f012 25 61 85d 4e ff 1129 113e 102d 0 1090 fffc 0 82 2927
  //   223d 2076 223e 186c 2 1076 8260 820d f021 2076 81 f009 207c 807c 820c f027 82 ff
endmodule

module instruction_printer (
  input  enable,
  input  SI_mode,
  input  load,
  input  clk,
  input  reset,
  input  [15:0] data_bus,
  input  [15:0] pk,
  input  [15:0] real_addr,
  input  [15:0] instr,
  input  [15:0] tmpc,
  input  [15:0] control_bus_1,
  input  [15:0] control_bus_2,
  output [6:0] ascii_out,
  output clock_out,
  output reset_out
);

  wire and_1_out, and_2_out, and_3_out, and_4_out, and_5_out, and_6_out, and_8_out, and_9_out, buffer_1_out,
       buffer_2_out, buffer_3_out, buffer_4_out, buffer_5_out, button_1_out, button_2_out, d_ff_1_q,
       d_ff_2_q, d_ff_3_q, d_ff_4_q, d_ff_5_q, d_ff_6_q, eight_bit_eq_cmp_1_out_3, eight_bit_eq_cmp_2_out_3,
       four_bit_eq_cmp_1_out_3, four_bit_eq_cmp_2_out_3, j_k_ff_1_q, l_1_out_2, l_2_out_2, or_1_out,
       or_2_out, or_3_out, or_4_out, or_6_out, or_7_out, or_8_out, parameter_printer_1_done,
       parameter_printer_2_done, parameter_printer_2_nothing_pass_up, parameter_printer_3_nothing_pass_up,
       pulsey_1_out_2, s_r_ff_1_q, sixt_bit_eq_cmp_1_out_3;
  wire [4:0] adder_1_out, and_7_out, register_1_q;
  wire [4:4] not_1_out;
  wire [5:0] rom_1_data, rom_1_data_2, rom_1_data_3;
  wire [6:0] or_9_out, or_10_out, parameter_printer_1_out_12, parameter_printer_2_out_12,
       parameter_printer_3_out_12;
  wire [7:0] sixt_bit_gatekeeper_1_out_3, sixt_bit_gatekeeper_1_out_3_2;
  wire [15:0] instr_addr_q, register_2_q, sixt_bit_gatekeeper_2_out_3, sixt_bit_gatekeeper_3_out_3,
       sixt_bit_gatekeeper_4_out_3, subtractor_1_out;

  or or_1 (or_1_out, enable, button_1_out);
  Button button_1 (.out(button_1_out));
  J_K_Flip_Flop j_k_ff_1 (.J(1'b1), .K(1'b1), .clk(or_1_out), .Q(j_k_ff_1_q));  // open: Qn, preset, reset
  not not_1 (not_1_out[4], j_k_ff_1_q);
  buf buffer_1 (buffer_1_out, not_1_out[4]);
  buf buffer_2 (buffer_2_out, buffer_1_out);
  D_Flip_Flop d_ff_1 (.D(load), .clk(clk), .Q(d_ff_1_q), .reset(reset));  // open: Qn, preset
  Button button_2 (.out(button_2_out));
  buf buffer_3 (buffer_3_out, buffer_2_out);
  buf buffer_4 (buffer_4_out, buffer_3_out);
  buf buffer_5 (buffer_5_out, buffer_4_out);
  and and_1 (and_1_out, buffer_5_out, or_1_out);
  D_Flip_Flop d_ff_2 (.D(d_ff_1_q), .clk(clk), .Q(d_ff_2_q), .reset(reset));  // open: Qn, preset
  or or_2 (or_2_out, button_2_out, and_1_out, or_4_out);
  and and_2 (and_2_out, ~not_1_out[4], or_1_out);  // AND_Gate
  L l_1 (.in_1(d_ff_2_q), .out_2(l_1_out_2));
  D_Flip_Flop d_ff_3 (.D(d_ff_2_q), .clk(clk), .Q(d_ff_3_q), .reset(reset));  // open: Qn, preset
  and and_3 (and_3_out, or_2_out, not_1_out[4]);
  pulsey pulsey_1 (.in_1(and_3_out), .out_3(clock_out), .out_2(pulsey_1_out_2));
  L l_2 (.in_1(d_ff_3_q), .out_2(l_2_out_2));
  D_Flip_Flop #(.trigger("falling")) d_ff_4 (.D(d_ff_3_q), .clk(clk), .Q(d_ff_4_q), .reset(reset));  // open: Qn, preset
  and and_4 (and_4_out, ~not_1_out[4], clock_out);  // AND_Gate
  or or_3 (or_3_out, pulsey_1_out_2, reset);
  Register #(.width(5)) register_1 (
    .D(adder_1_out), .en(not_1_out[4]), .clk(clock_out), .Q(register_1_q), .clr(or_6_out));
  or or_4 (or_4_out, d_ff_4_q, and_5_out);
  and and_5 (and_5_out, ~SI_mode, l_1_out_2, l_2_out_2, d_ff_6_q);  // AND_Gate
  Register #(.width(16)) instr_addr (.D(pk), .en(d_ff_1_q), .clk(clk), .Q(instr_addr_q), .clr(reset));
  or or_5 (reset_out, or_3_out, and_4_out, and_2_out);
  or or_6 (or_6_out, reset, or_3_out);
  Adder #(.width(5)) adder_1 (.a(register_1_q), .b(5'b00001), .out(adder_1_out));  // open: cin, cout
  Subtractor #(.width(16)) subtractor_1 (.a(real_addr), .b(instr_addr_q), .out(subtractor_1_out));  // open: bin, bout
  sixt_bit_eq_cmp sixt_bit_eq_cmp_1 (.in_1(subtractor_1_out), .in_2(16'h2), .out_3(sixt_bit_eq_cmp_1_out_3));
  ROM #(.addrWidth(13), .dataWidth(18)) rom_1 (
    .addr({sixt_bit_gatekeeper_1_out_3_2, register_1_q}), .data({rom_1_data_3, rom_1_data_2, rom_1_data}));
  sixt_bit_gatekeeper sixt_bit_gatekeeper_1 (
    .in_1(not_1_out[4]), .in_2(instr), .out_3({sixt_bit_gatekeeper_1_out_3, sixt_bit_gatekeeper_1_out_3_2}));
  D_Flip_Flop d_ff_5 (.D(and_6_out), .clk(clk), .Q(d_ff_5_q), .reset(reset));  // open: Qn, preset
  and and_6 (and_6_out, sixt_bit_eq_cmp_1_out_3, or_8_out);
  D_Flip_Flop d_ff_6 (.D(d_ff_5_q), .clk(clk), .Q(d_ff_6_q), .reset(reset));  // open: Qn, preset
  S_R_Flip_Flop s_r_ff_1 (.Q(s_r_ff_1_q), .reset(or_3_out), .preset(rom_1_data_2[1]));  // open: S, R, clk, Qn
  sixt_bit_gatekeeper sixt_bit_gatekeeper_2 (
    .in_1(not_1_out[4]), .in_2({sixt_bit_gatekeeper_1_out_3, sixt_bit_gatekeeper_1_out_3_2}),
    .out_3(sixt_bit_gatekeeper_2_out_3));
  assign and_7_out = register_1_q & {5{not_1_out[4]}};  // AND_Gate and_7, 5 bits wide
  sixt_bit_gatekeeper sixt_bit_gatekeeper_3 (.in_1(not_1_out[4]), .in_2(tmpc), .out_3(sixt_bit_gatekeeper_3_out_3));
  Register #(.width(16)) register_2 (.D(data_bus), .en(d_ff_5_q), .clk(clk), .Q(register_2_q), .clr(reset));
  Multiplexer #(.width(7)) multiplexer_1 (
    .in0({rom_1_data_2[0], rom_1_data}), .in1(or_9_out), .out(ascii_out), .sel(s_r_ff_1_q));
  or or_7 (or_7_out, s_r_ff_1_q, rom_1_data_2[1]);
  // Probe on or_9_out
  sixt_bit_gatekeeper sixt_bit_gatekeeper_4 (
    .in_1(not_1_out[4]), .in_2(register_2_q), .out_3(sixt_bit_gatekeeper_4_out_3));
  or or_8 (or_8_out, and_8_out, and_9_out);
  eight_bit_eq_cmp eight_bit_eq_cmp_1 (.in_1(8'h11), .in_2(control_bus_1[7:0]), .out_3(eight_bit_eq_cmp_1_out_3));
  four_bit_eq_cmp four_bit_eq_cmp_1 (.in_1(control_bus_1[15:12]), .in_2(4'b0000), .out_3(four_bit_eq_cmp_1_out_3));
  // Probe on {rom_1_data_3, rom_1_data_2, rom_1_data}
  assign or_9_out = parameter_printer_1_out_12 | or_10_out;  // OR_Gate or_9, 7 bits wide
  parameter_printer parameter_printer_1 (
    .enable(or_7_out), .counter(and_7_out), .clock(clock_out), .instruction(sixt_bit_gatekeeper_2_out_3),
    .tmpc(sixt_bit_gatekeeper_3_out_3), .tmpd(sixt_bit_gatekeeper_4_out_3), .reset(or_3_out),
    .param_type(rom_1_data), .nothing_below(parameter_printer_2_nothing_pass_up),
    .done(parameter_printer_1_done), .out_12(parameter_printer_1_out_12));  // open: prev_done, nothing_pass_up
  assign or_10_out = parameter_printer_2_out_12 | parameter_printer_3_out_12;  // OR_Gate or_10, 7 bits wide
  parameter_printer parameter_printer_2 (
    .prev_done(parameter_printer_1_done), .counter(and_7_out), .clock(clock_out),
    .instruction(sixt_bit_gatekeeper_2_out_3), .tmpc(sixt_bit_gatekeeper_3_out_3),
    .tmpd(sixt_bit_gatekeeper_4_out_3), .reset(or_3_out), .param_type(rom_1_data_2),
    .nothing_below(parameter_printer_3_nothing_pass_up), .done(parameter_printer_2_done),
    .out_12(parameter_printer_2_out_12), .nothing_pass_up(parameter_printer_2_nothing_pass_up));  // open: enable
  parameter_printer parameter_printer_3 (
    .prev_done(parameter_printer_2_done), .counter(and_7_out), .clock(clock_out),
    .instruction(sixt_bit_gatekeeper_2_out_3), .tmpc(sixt_bit_gatekeeper_3_out_3),
    .tmpd(sixt_bit_gatekeeper_4_out_3), .reset(or_3_out), .param_type(rom_1_data_3),
    .out_12(parameter_printer_3_out_12), .nothing_pass_up(parameter_printer_3_nothing_pass_up));  // open: enable, nothing_below, done
  and and_8 (and_8_out, eight_bit_eq_cmp_1_out_3, four_bit_eq_cmp_1_out_3);
  eight_bit_eq_cmp eight_bit_eq_cmp_2 (.in_1(8'h11), .in_2(control_bus_2[7:0]), .out_3(eight_bit_eq_cmp_2_out_3));
  four_bit_eq_cmp four_bit_eq_cmp_2 (.in_1(control_bus_2[15:12]), .in_2(4'b0000), .out_3(four_bit_eq_cmp_2_out_3));
  and and_9 (and_9_out, eight_bit_eq_cmp_2_out_3, four_bit_eq_cmp_2_out_3);

  // Notes on the sheet:
  //   contents of rom_1 (hex, n*v repeats v):
  //   63 68 69 6c 6c 27*0 67 6f 74 6f a0 27*4110 67 6f 74 6f 5f 69 66 5f 7a 65 72 6f a0 19*4402 67 6f 74
  //   6f 5f 69 66 5f 6e 6f 6e 7a 65 72 6f a0 16*4402 67 6f 74 6f 5f 69 66 5f 6e 65 67 61 74 69 76 65 a0
  //   15*4402 67 6f 74 6f 5f 69 66 5f 6e 6f 6e 6e 65 67 61 74 69 76 65 a0 12*4402 67 6f 74 6f 5f 69 66 5f
  //   70 6f 73 69 74 69 76 65 a0 15*4402 67 6f 74 6f 5f 69 66 5f 6e 6f 6e 70 6f 73 69 74 69 76 65 a0
  //   12*4402 67 6f 74 6f 5f 69 66 5f 65 71 75 61 6c a0 18*10282 67 6f 74 6f 5f 69 66 5f 75 6e 65 71 75 61
  //   6c a0 16*10282 67 6f 74 6f 5f 69 66 5f 6c 65 73 73 a0 19*10282 67 6f 74 6f 5f 69 66 5f 67 72 65 61
  //   74 65 72 a0 16*10282 67 6f 74 6f 5f 69 66 5f 6c 65 71 a0 20*10282 67 6f 74 6f 5f 69 66 5f 67 65 71
  //   a0 20*10282 67 6f 74 6f 5f 69 66 5f 65 71 75 61 6c a0 18*10602 67 6f 74 6f 5f 69 66 5f 75 6e 65 71
  //   75 61 6c a0 16*10602 67 6f 74 6f 5f 69 66 5f 6c 65 73 73 a0 19*10602 67 6f 74 6f 5f 69 66 5f 67 72
  //   65 61 74 65 72 a0 16*10602 67 6f 74 6f 5f 69 66 5f 6c 65 71 a0 20*10602 67 6f 74 6f 5f 69 66 5f 67
  //   65 71 a0 20*10602 67 6f 74 6f 5f 69 66 5f 6c 65 73 73 5f 75 6e 73 67 6e a0 13*10282 67 6f 74 6f 5f
  //   69 66 5f 67 72 65 61 74 65 72 5f 75 6e 73 67 6e a0 10*10282 67 6f 74 6f 5f 69 66 5f 6c 65 71 5f 75
  //   6e 73 67 6e a0 14*10282 67 6f 74 6f 5f 69 66 5f 67 65 71 5f 75 6e 73 67 6e a0 14*10282 67 6f 74 6f
  //   5f 69 66 5f 65 71 75 61 6c 5f 75 6e 73 67 6e a0 12*10602 67 6f 74 6f 5f 69 66 5f 75 6e 65 71 75 61
  //   6c 5f 75 6e 73 67 6e a0 10*10602 67 6f 74 6f 5f 69 66 5f 6c 65 73 73 5f 75 6e 73 67 6e a0 13*10602
  //   67 6f 74 6f 5f 69 66 5f 67 72 65 61 74 65 72 5f 75 6e 73 67 6e a0 10*10602 67 6f 74 6f 5f 69 66 5f
  //   6c 65 71 5f 75 6e 73 67 6e a0 14*10602 67 6f 74 6f 5f 69 66 5f 67 65 71 5f 75 6e 73 67 6e a0
  //   14*10602 73 77 61 70 a0 27*4282 73 65 74 a0 28*4611 73 65 74 a0 28*4651 73 65 74 a0 28*4291 73 65 74
  //   a0 28*4ad9 73 65 74 a0 28*4391 73 65 74 a0 28*4bd9 73 65 74 a0 28*4402 73 65 74 a0 28*4442 73 65 74
  //   a0 28*4282 73 65 74 a0 28*4ac2 73 65 74 a0 28*4382 73 65 74 a0 28*4bc2 73 65 74 a0 28*4623 73 65 74
  //   a0 28*4063 73 65 74 a0 28*42a3 73 65 74 a0 28*4ee3 73 65 74 a0 28*43a3 73 65 74 a0 28*4fe3 73 65 74
  //   a0 28*4406 73 65 74 a0 28*4446 73 65 74 a0 28*4286 73 65 74 a0 28*4ac6 73 65 74 a0 28*4386 73 65 74
  //   a0 28*4bc6 73 65 74 a0 28*4627 73 65 74 a0 28*4667 73 65 74 a0 28*42a7 73 65 74 a0 28*4ee7 73 65 74
  //   a0 28*43a7 73 65 74 a0 28*4fe7 69 6e 63 a0 28*4102 64 65 63 a0 28*4102 6e 6f 74 a0 28*4102 6c 73 68
  //   69 66 74 a0 25*4102 72 73 68 69 66 74 a0 25*4102 69 6e 63 a0 28*4282 64 65 63 a0 28*4282 6e 6f 74 a0
  //   28*4282 6c 73 68 69 66 74 a0 25*4282 72 73 68 69 66 74 a0 25*4282 61 64 64 a0 28*4402 73 75 62 a0
  //   28*4402 6d 75 6c a0 28*4402 64 69 76 a0 28*4402 72 65 6d a0 28*4402 75 63 6d 70 a0 27*4402 63 6d 70
  //   a0 28*4402 61 6e 64 a0 28*4402 6f 72 a0 29*4402 78 6f 72 a0 28*4402 73 68 69 66 74 a0 26*4402 61 64
  //   64 a0 28*10282 73 75 62 a0 28*10282 6d 75 6c a0 28*10282 64 69 76 a0 28*10282 72 65 6d a0 28*10282
  //   75 63 6d 70 a0 27*10282 63 6d 70 a0 28*10282 61 6e 64 a0 28*10282 6f 72 a0 29*10282 78 6f 72 a0
  //   28*10282 73 68 69 66 74 a0 26*10282 61 64 64 a0 28*4282 73 75 62 a0 28*4282 6d 75 6c a0 28*4282 64
  //   69 76 a0 28*4282 72 65 6d a0 28*4282 75 63 6d 70 a0 27*4282 63 6d 70 a0 28*4282 61 6e 64 a0 28*4282
  //   6f 72 a0 29*4282 78 6f 72 a0 28*4282 73 68 69 66 74 a0 26*4282 61 64 64 a0 28*12282 73 75 62 a0
  //   28*12282 6d 75 6c a0 28*12282 64 69 76 a0 28*12282 72 65 6d a0 28*12282 75 63 6d 70 a0 27*12282 63
  //   6d 70 a0 28*12282 61 6e 64 a0 28*12282 6f 72 a0 29*12282 78 6f 72 a0 28*12282 73 68 69 66 74 a0
  //   26*12282 70 75 73 68 28*0 70 75 73 68 a0 27*4110 70 75 73 68 a0 27*4101 70 75 73 68 a0 27*4102 70 75
  //   73 68 a0 27*4123 70 75 73 68 a0 27*4106 70 75 73 68 a0 27*4127 70 6f 70 29*0 70 6f 70 a0 28*4111 70
  //   6f 70 a0 28*4102 70 6f 70 a0 28*4123 70 6f 70 a0 28*4106 70 6f 70 a0 28*4127 63 61 6c 6c a0 27*4110
  //   66 61 73 74 63 61 6c 6c a0 23*4110 72 65 74 75 72 6e 26*0 70 69 6e 6d 6f 64 65 5f 69 6e 70 75 74 a0
  //   18*4100 70 69 6e 6d 6f 64 65 5f 6f 75 74 70 75 74 a0 17*4100 70 69 6e 6d 6f 64 65 5f 69 6e 70 75 74
  //   a0 18*4102 70 69 6e 6d 6f 64 65 5f 6f 7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
endmodule

module control_unit (
  input  [15:0] RAM_direct,
  input  [15:0] data_bus_in,
  input  pause_after_instruction,
  input  stall,
  input  [15:0] control_bus_1,
  input  [15:0] control_bus_2,
  input  clock,
  input  reset,
  input  [15:0] stack_pointer,
  input  [15:0] addr_bus,
  input  [7:0] interrupt_pins,
  output [15:0] current_instr,
  output pause,
  output [15:0] tmpc_out,
  output [15:0] data_bus_out,
  output [15:0] addr_bus_out,
  output [15:0] control_bus_1_out,
  output [15:0] to_pk,
  output load,
  output [15:0] control_bus_2_out
);

  wire and_1_out, and_2_out, and_5_out, and_6_out, and_7_out, buffer_1_out, buffer_2_out, buffer_3_out,
       buffer_4_out, button_1_out, comparator_1_gt, comparator_1_lt, d_ff_1_q, eight_bit_eq_cmp_1_out_3,
       eight_bit_eq_cmp_2_out_3, interrupt_queue_1_waiting, nor_1_out, or_1_out, or_4_out, or_5_out,
       or_9_out, register_1_q, register_2_q, register_3_q, sixt_bit_eq_cmp_1_out_3, sixt_bit_eq_cmp_2_out_3,
       sixt_bit_eq_cmp_3_out_3, sixt_bit_eq_cmp_4_out_3, sixt_bit_eq_cmp_5_out_3, sixt_bit_eq_cmp_6_out_3,
       sixt_bit_eq_cmp_7_out_3, sixt_bit_eq_cmp_8_out_3, stacker_1_active, unstacker_1_active;
  wire [7:0] interrupt_queue_1_id, multiplexer_2_out;
  wire [15:0] interrupt_table_1_ih_addr, interrupt_table_1_to_data_bus, MAR_q,
       microcode_mixer_1_microcode_out, microcode_mixer_2_microcode_out, multiplexer_1_out,
       multiplexer_3_out, multiplexer_4_out, or_6_out, or_7_out, or_8_out, rom_1_data, rom_2_data,
       rom_3_data, shifter_1_out, shifter_2_out, sixt_bit_gatekeeper_1_out_3, sixt_bit_gatekeeper_2_out_3,
       sixt_bit_gatekeeper_3_out_3, sixt_bit_gatekeeper_4_out_3, sixt_bit_gatekeeper_5_out_3,
       sixt_bit_incrementer_1_out_2, stacker_1_change_mask, stacker_1_control_bus_1_out,
       stacker_1_control_bus_2_out, stacker_1_to_data_bus, temp_registers_1_data_bus_out,
       temp_registers_1_out_9, temp_registers_1_out_11, temp_registers_1_to_sreg,
       unstacker_1_control_bus_1_out, unstacker_1_control_bus_2_out;
  wire [31:0] tick_counter_1_cycle_count, tick_counter_1_negedge_count;

  Button button_1 (.out(button_1_out));
  Pull_Resistor pull_resistor_1 (.node(pause_after_instruction));
  sixt_bit_eq_cmp sixt_bit_eq_cmp_1 (.in_1(16'h1), .in_2(rom_2_data), .out_3(sixt_bit_eq_cmp_1_out_3));
  and and_1 (and_1_out, clock, ~sixt_bit_eq_cmp_2_out_3, ~or_1_out);  // AND_Gate
  or or_1 (or_1_out, button_1_out, reset);
  Multiplexer #(.width(16)) multiplexer_1 (.in0(data_bus_in), .in1(16'hfe), .out(multiplexer_1_out), .sel(and_2_out));
  Register #(.trigger("falling"), .width(16)) instr (
    .D(multiplexer_1_out), .en(sixt_bit_eq_cmp_1_out_3), .clk(and_1_out), .Q(current_instr), .clr(or_1_out));
  ROM #(.dataWidth(16)) rom_1 (.addr(multiplexer_2_out), .data(rom_1_data));
  Multiplexer #(.width(8)) multiplexer_2 (
    .in0(data_bus_in[7:0]), .in1(8'hfe), .out(multiplexer_2_out), .sel(and_2_out));
  interrupt_queue interrupt_queue_1 (
    .next_ir(and_5_out), .pins_in(interrupt_pins), .reset(or_1_out), .waiting(interrupt_queue_1_waiting),
    .id(interrupt_queue_1_id));
  // Probe on tmpc_out
  // Probe on temp_registers_1_out_9
  // Probe on temp_registers_1_out_11
  temp_registers temp_registers_1 (
    .clock(and_1_out), .reset(or_1_out), .control_bus_1(control_bus_1), .control_bus_2(control_bus_2),
    .data_bus_in(data_bus_in), .ram_direct(RAM_direct), .out_9(temp_registers_1_out_9),
    .out_11(temp_registers_1_out_11), .out_12(tmpc_out), .data_bus_out(temp_registers_1_data_bus_out),
    .to_sreg(temp_registers_1_to_sreg), .addr_bus_out(addr_bus_out));
  Register #(.width(1)) register_1 (
    .D(interrupt_queue_1_waiting), .clk(and_1_out), .Q(register_1_q), .clr(or_1_out));  // open: en
  sixt_bit_eq_cmp sixt_bit_eq_cmp_2 (.in_1(current_instr), .in_2(16'hff), .out_3(sixt_bit_eq_cmp_2_out_3));
  interrupt_table interrupt_table_1 (
    .control_bus_1(control_bus_1), .control_bus_2(control_bus_2), .id(interrupt_queue_1_id),
    .data_in(data_bus_in), .clk(and_1_out), .reset(or_1_out), .ih_addr(interrupt_table_1_ih_addr),
    .to_data_bus(interrupt_table_1_to_data_bus));
  sixt_bit_gatekeeper sixt_bit_gatekeeper_1 (
    .in_1(register_2_q), .in_2(interrupt_table_1_ih_addr), .out_3(sixt_bit_gatekeeper_1_out_3));
  and and_2 (and_2_out, sixt_bit_eq_cmp_3_out_3, interrupt_queue_1_waiting);
  assign data_bus_out = stacker_1_to_data_bus | interrupt_table_1_to_data_bus | temp_registers_1_data_bus_out;  // OR_Gate or_2, 16 bits wide
  assign to_pk = temp_registers_1_to_sreg | sixt_bit_gatekeeper_1_out_3;  // OR_Gate or_3, 16 bits wide
  Register #(.trigger("falling"), .width(1)) register_2 (
    .D(interrupt_queue_1_waiting), .en(sixt_bit_eq_cmp_1_out_3), .clk(and_1_out), .Q(register_2_q),
    .clr(or_1_out));
  Multiplexer #(.width(16)) multiplexer_3 (
    .in0(sixt_bit_incrementer_1_out_2), .in1(rom_1_data), .out(multiplexer_3_out),
    .sel(sixt_bit_eq_cmp_3_out_3));
  sixt_bit_eq_cmp sixt_bit_eq_cmp_3 (.in_1(16'h1), .in_2(MAR_q), .out_3(sixt_bit_eq_cmp_3_out_3));
  Multiplexer #(.width(16)) multiplexer_4 (
    .in0(multiplexer_3_out), .in1({16{1'b1}}), .out(multiplexer_4_out), .sel(comparator_1_lt));
  sixt_bit_eq_cmp sixt_bit_eq_cmp_4 (.in_1(16'hfffe), .in_2(rom_2_data), .out_3(sixt_bit_eq_cmp_4_out_3));
  Register #(.trigger("falling"), .width(1)) register_3 (
    .D(stacker_1_active), .en(register_2_q), .clk(and_1_out), .Q(register_3_q), .clr(or_1_out));
  // Probe on multiplexer_4_out
  Register #(.trigger("falling"), .width(16)) MAR (
    .D(multiplexer_4_out), .en(and_6_out), .clk(and_1_out), .Q(MAR_q), .clr(or_4_out));
  or or_4 (or_4_out, sixt_bit_eq_cmp_4_out_3, or_1_out);
  and and_3 (pause, sixt_bit_eq_cmp_4_out_3, pause_after_instruction);
  sixt_bit_eq_cmp sixt_bit_eq_cmp_5 (.in_1({16{1'b0}}), .in_2(MAR_q), .out_3(sixt_bit_eq_cmp_5_out_3));
  and and_4 (load, sixt_bit_eq_cmp_5_out_3, and_6_out, ~comparator_1_lt);  // AND_Gate
  buf buffer_1 (buffer_1_out, buffer_4_out);
  buf buffer_2 (buffer_2_out, buffer_1_out);
  buf buffer_3 (buffer_3_out, register_3_q);
  buf buffer_4 (buffer_4_out, buffer_3_out);
  ROM #(.addrWidth(16), .dataWidth(16)) rom_2 (.addr(MAR_q), .data(rom_2_data));
  ROM #(.addrWidth(16), .dataWidth(16)) rom_3 (.addr(MAR_q), .data(rom_3_data));
  and and_5 (and_5_out, ~register_3_q, buffer_2_out);  // AND_Gate
  and and_6 (and_6_out, ~stall, or_5_out);  // AND_Gate
  sixt_bit_incrementer sixt_bit_incrementer_1 (.in_1(MAR_q), .out_2(sixt_bit_incrementer_1_out_2));
  tick_counter tick_counter_1 (
    .clock(and_1_out), .reset(or_1_out), .cycle_count(tick_counter_1_cycle_count),
    .negedge_count(tick_counter_1_negedge_count));  // open: posedge_count
  or or_5 (or_5_out, d_ff_1_q, comparator_1_lt);
  // Probe on tick_counter_1_cycle_count
  Comparator #(.width(32)) comparator_1 (
    .a(tick_counter_1_negedge_count), .b(32'h1), .gt(comparator_1_gt), .lt(comparator_1_lt));  // open: eq
  and and_7 (and_7_out, comparator_1_gt, ~stall, ~sixt_bit_eq_cmp_2_out_3);  // AND_Gate
  microcode_mixer microcode_mixer_1 (
    .microcode_in(rom_2_data), .instruction(current_instr), .tmpc(tmpc_out), .data_bus(RAM_direct),
    .microcode_out(microcode_mixer_1_microcode_out));
  microcode_mixer microcode_mixer_2 (
    .microcode_in(rom_3_data), .instruction(current_instr), .tmpc(tmpc_out), .data_bus(RAM_direct),
    .microcode_out(microcode_mixer_2_microcode_out));
  sixt_bit_gatekeeper sixt_bit_gatekeeper_2 (
    .in_1(and_7_out), .in_2(microcode_mixer_1_microcode_out), .out_3(sixt_bit_gatekeeper_2_out_3));
  sixt_bit_gatekeeper sixt_bit_gatekeeper_3 (
    .in_1(and_7_out), .in_2(microcode_mixer_2_microcode_out), .out_3(sixt_bit_gatekeeper_3_out_3));
  D_Flip_Flop #(.trigger("falling")) d_ff_1 (
    .D(nor_1_out), .clk(and_1_out), .Q(d_ff_1_q), .reset(or_1_out));  // open: Qn, preset
  Multiplexer #(.width(16)) multiplexer_5 (
    .in0(sixt_bit_gatekeeper_2_out_3), .in1(or_7_out), .out(control_bus_1_out), .sel(or_9_out));
  Multiplexer #(.width(16)) multiplexer_6 (
    .in0(sixt_bit_gatekeeper_3_out_3), .in1(or_8_out), .out(control_bus_2_out), .sel(or_9_out));
  nor nor_1 (nor_1_out, unstacker_1_active, stacker_1_active);
  eight_bit_eq_cmp eight_bit_eq_cmp_1 (.in_1(8'h24), .in_2(control_bus_1_out[7:0]), .out_3(eight_bit_eq_cmp_1_out_3));
  Shifter #(.width(16)) shifter_1 (.in(16'h1), .\dist (control_bus_1_out[15:12]), .out(shifter_1_out));
  eight_bit_eq_cmp eight_bit_eq_cmp_2 (.in_1(8'h24), .in_2(control_bus_2_out[7:0]), .out_3(eight_bit_eq_cmp_2_out_3));
  Shifter #(.width(16)) shifter_2 (.in(16'h1), .\dist (control_bus_2_out[15:12]), .out(shifter_2_out));
  assign or_6_out = sixt_bit_gatekeeper_4_out_3 | sixt_bit_gatekeeper_5_out_3;  // OR_Gate or_6, 16 bits wide
  sixt_bit_gatekeeper sixt_bit_gatekeeper_4 (
    .in_1(eight_bit_eq_cmp_1_out_3), .in_2(shifter_1_out), .out_3(sixt_bit_gatekeeper_4_out_3));
  sixt_bit_gatekeeper sixt_bit_gatekeeper_5 (
    .in_1(eight_bit_eq_cmp_2_out_3), .in_2(shifter_2_out), .out_3(sixt_bit_gatekeeper_5_out_3));
  sixt_bit_eq_cmp sixt_bit_eq_cmp_6 (.in_1(control_bus_1_out), .in_2(16'h64), .out_3(sixt_bit_eq_cmp_6_out_3));
  // Probe on stacker_1_change_mask
  stacker stacker_1 (
    .clk(and_1_out), .reset(or_1_out), .mem_in(RAM_direct), .register_write(or_6_out),
    .stacking_mask(16'hff), .write_changemask(sixt_bit_eq_cmp_8_out_3), .bypass_mask(register_1_q),
    .enable(sixt_bit_eq_cmp_6_out_3), .control_bus_1_out(stacker_1_control_bus_1_out),
    .control_bus_2_out(stacker_1_control_bus_2_out), .to_data_bus(stacker_1_to_data_bus),
    .active(stacker_1_active), .change_mask(stacker_1_change_mask));
  assign or_7_out = stacker_1_control_bus_1_out | unstacker_1_control_bus_1_out;  // OR_Gate or_7, 16 bits wide
  assign or_8_out = stacker_1_control_bus_2_out | unstacker_1_control_bus_2_out;  // OR_Gate or_8, 16 bits wide
  or or_9 (or_9_out, stacker_1_active, unstacker_1_active);
  sixt_bit_eq_cmp sixt_bit_eq_cmp_7 (.in_1(control_bus_1_out), .in_2(16'h66), .out_3(sixt_bit_eq_cmp_7_out_3));
  // Probe on control_bus_1_out
  sixt_bit_eq_cmp sixt_bit_eq_cmp_8 (
    .in_1(16'h65), .in_2(microcode_mixer_1_microcode_out), .out_3(sixt_bit_eq_cmp_8_out_3));
  unstacker unstacker_1 (
    .enable(sixt_bit_eq_cmp_8_out_3), .preunstacking(sixt_bit_eq_cmp_7_out_3), .unstacking_mask(RAM_direct),
    .clk(and_1_out), .reset(or_1_out), .active(unstacker_1_active),
    .control_bus_1_out(unstacker_1_control_bus_1_out), .control_bus_2_out(unstacker_1_control_bus_2_out));
  // Probe on control_bus_2_out
  // Probe on stack_pointer
  // Probe on addr_bus

  // Notes on the sheet:
  //   contents of rom_1 (hex, n*v repeats v):
  //   2 4 6 9 c f 12 15 18 1b 1e 21 24 27 2a 2e 32 36 3a 3e 42 45 48 4b 4e 52 56 5a 5e 62 66 6b 6f 74 77
  //   7c 7f 84 87 8b 8e 91 94 98 9c a1 a5 aa ae b3 b6 ba bd c1 c4 c8 cc d1 d5 da de 14a 14d 156 162 168
  //   17a 17e 191 195 19c e3 e7 eb ef f3 f7 fb ff 103 107 10b 10f 113 117 11b 11f 123 127 12b 12f 133 137
  //   13b 13e 141 144 147 150 153 159 15c 15f 165 16b 16e 171 174 177 182 185 188 18b 18e 199 1a0 1a2 1a5
  //   1a8 1ab 1af 1b2 1b6 1b8 1bc 1bf 1c3 1c6 1ca 1d0 1d7 1dc 1de 1e0 1e4 1e8 1ea 1f2 1f6 1f8 1fb 1fe 203
  //   207 20e 108*0 21b 216
  //   contents of rom_2 (hex, n*v repeats v):
  //   11 1 0 fffe 4010 fffe 10a0 4010 fffe 10a0 4010 fffe 10a0 4010 fffe 10a0 4010 fffe 10a0 4010 fffe
  //   10a0 4010 fffe 12c8 4010 fffe 12c8 4010 fffe 12c8 4010 fffe 12c8 4010 fffe 12c8 4010 fffe 12c8 4010
  //   fffe 111 102f 4010 fffe 111 102f 4010 fffe 111 102f 4010 fffe 111 102f 4010 fffe 111 102f 4010 fffe
  //   111 102f 4010 fffe 12c7 4010 fffe 12c7 4010 fffe 12c7 4010 fffe 12c7 4010 fffe 111 102f 4010 fffe
  //   111 102f 4010 fffe 111 102f 4010 fffe 111 102f 4010 fffe 111 102f 4010 fffe 111 102f 4010 fffe 10a0
  //   2006 10a4 20a4 fffe 111 60 25 fffe 111 2b 60 25 fffe 4003 25 fffe 111 2a 60 25 fffe 4003 25 fffe 111
  //   2a 60 25 fffe 4002 10a4 fffe 4002 63 10a4 fffe 20a0 10a4 fffe 29 10a4 fffe 2082 10a4 fffe 11 2a 10a4
  //   fffe 5010 60 26 fffe 111 2b 60 29 fffe 5010 20a0 26 fffe 111 2a 60 29 fffe 5010 2082 26 fffe 111 2a
  //   60 29 fffe 4002 1086 fffe 4002 63 1086 fffe 20a0 1086 fffe 11 2a 1086 fffe 2082 1086 fffe 11 2a 1086
  //   fffe 5010 60 26 fffe 111 2b 60 29 fffe 5010 20a0 26 fffe 111 2a 60 29 fffe 5010 2082 26 fffe 111 2a
  //   60 29 fffe 11 10c0 10a4 fffe 11 10c1 10a4 fffe 11 10c2 10a4 fffe 11 10c3 10a4 fffe 11 10c4 10a4 fffe
  //   11 10c7 10a4 fffe 11 10c8 10a4 fffe 11 10c9 10a4 fffe 11 10ca 10a4 fffe 11 10cb 10a4 fffe 11 10cf
  //   10a4 fffe 11 20c0 10a4 fffe 11 20c1 10a4 fffe 11 20c2 10a4 fffe 11 20c3 10a4 fffe 11 20c4 10a4 fffe
  //   11 20c7 10a4 fffe 11 20c8 10a4 fffe 11 20c9 10a4 fffe 11 20ca 10a4 fffe 11 20cb 10a4 fffe 11 20cf
  //   10a4 fffe 12c0 10a4 fffe 12c1 10a4 fffe 12c2 10a4 fffe 12c3 10a4 fffe 12c4 10a4 fffe 11c5 10a4 fffe
  //   11c6 10a4 fffe 12c7 10a4 fffe 12c8 10a4 fffe 11cc 10a4 fffe 12c9 10a4 fffe 12ca 10a4 fffe 12cb 10a4
  //   fffe 11cd 10a4 fffe 12cf 10a4 fffe 11ce 10a4 fffe 28c0 10a4 fffe 28c1 10a4 fffe 28c2 10a4 fffe 28c3
  //   10a4 fffe 28c4 10a4 fffe 11 20c5 10a4 fffe 11 20c6 10a4 fffe 28c7 10a4 fffe 28c8 10a4 fffe 28c9 10a4
  //   fffe 28ca 10a4 fffe 28cb 10a4 fffe 11 20cc 10a4 fffe 11 20cd 10a4 fffe 28cf 10a4 fffe 11 20ce 10a4
  //   fffe 1011 fffe 4002 25 fffe 4004 25 fffe 10a0 25 fffe 10 60 29 fffe 1012 25 fffe 10 60 29 fffe 1010
  //   fffe 10 60 25 fffe 1013 10a4 fffe 10 60 29 fffe 1013 1086 fffe 10 60 29 fffe 10 2 25 4010 64 fffe 10
  //   2 25 4010 1012 25 fffe 1013 65 1004 6 fffe 10b0 fffe 10b1 fffe 10a0 4006 10b0 fffe 10a0 4006 10b1
  //   fffe 10b2 fffe 10b3 fffe 10b2 fffe 10a0 4006 b0b3 fffe 10a0 4006 b0b2 fffe 10b3 fffe 10b4 20a4 fffe
  //   20a0 10b5 fffe 10a0 4006 b0b4 20a4 fffe 10a0 4006 b0b5 fffe 111 4002 25 3031 3033 3032 fffe 111 5006
  //   10a0 26 3031 3033 3032 fffe 1011 2 25 64 fffe 10 2 25 5006 4003 6 64 fffe
  //   contents of rom_3 (hex, n*v repeats v):
  //   0 4 0 0 14 0 10 15 0 10 16 0 10 17 0 10 18 0 10 19 0 10 1a 0 10 15 0 10 16 0 10 17 0 10 19 0 10 1a 0
  //   10 18 0 0 12c8 15 0 0 12c8 16 0 0 12c8 17 0 0 12c8 19 0 0 12c8 1a 0 0 12c8 18 0 10 17 0 10 19 0 10
  //   1a 0 10 18 0 0 12c8 15 0 0 12c8 16 0 0 12c8 17 0 0 12c8 19 0 0 12c8 1a 0 0 12c8 18 0 0 20a0 2002 0 0
  //   0 4003 0 0 0 27 4003 0 0 20a0 10 0 0 2a3 4003 0 0 2082 0 0 0 2085 4003 0 0 0 10 0 0 27 10 4*0 2a3 10
  //   5*0 2085 0 0 111 1a1 0 0 0 27 1a1 26 0 10 1a1 0 0 0 2a3 1a1 26 0 10 1a1 0 0 0 2085 1a1 26 0 0 10 0 0
  //   27 10 5*0 2a3 6*0 2085 0 0 111 1083 0 0 0 27 1083 26 0 10 1083 0 0 0 2a3 1083 26 0 10 1083 0 0 0
  //   2085 1083 26 0 0 102f 0 0 0 102f 0 0 0 102f 0 0 0 102f 0 0 0 102f 0 0 0 102f 0 0 0 102f 0 0 0 102f 0
  //   0 0 102f 0 0 0 102f 0 0 0 102f 0 0 0 102f 0 0 0 102f 0 0 0 102f 0 0 0 102f 0 0 0 102f 0 0 0 102f 0 0
  //   0 102f 0 0 0 102f 0 0 0 102f 0 0 0 102f 0 0 0 102f 50*0 67 10 0 67 10 0 67 10 0 67 10 0 67 10 0 0
  //   102f 0 0 0 102f 0 0 67 10 0 67 10 0 67 10 0 67 10 0 67 10 0 0 102f 0 0 0 102f 0 0 67 10 0 0 102f 4*0
  //   1012 10 0 1012 10 0 1012 0 0 1a2 1012 26 0 1082 0 0 1084 1012 26 0 0 0 1013 4003 5*0 1013 1a1 26 4*0
  //   1013 1083 26 0 0 1012 0 14 0 0 0 1012 0 14 5*0 1010 46*0 63 7*0 4003 5*0 12 1003 1b 0 0 0 1012 7a 0
  //   28
endmodule

module special_registers (
  input  [15:0] data_bus_in,
  input  [15:0] control_bus_1,
  input  [15:0] control_bus_2,
  input  [15:0] temp_register,
  input  [15:0] sp_reset_value,
  input  clock,
  input  reset,
  output [15:0] program_kounter,
  output [15:0] data_bus_out,
  output [15:0] addr_bus_out,
  output [15:0] stack_pointer,
  output [15:0] offset_out
);

  wire and_1_out, and_2_out, and_3_out, buffer_1_out, buffer_2_out, buffer_3_out, buffer_4_out, buffer_5_out,
       buffer_6_out, buffer_7_out, d_ff_1_q, not_1_out, offs_to_addr_out, offs_to_data_out, offs_write_out,
       or_1_out, or_2_out, or_3_out, or_4_out, or_5_out, pk_decrement_out, pk_increment_out, pk_to_addr_out,
       pk_to_data_out, pk_write_out, s_r_ff_1_qn, s_r_ff_2_q, s_r_ff_3_q, sixt_bit_eq_zero_1_out_2,
       sp_decrement_out, sp_increment_out, sp_postinc_to_addr_out, sp_predec_to_addr_out, sp_to_addr_out,
       sp_to_data_out, sp_write_out, special_registers_opdec_1_offs_to_addr,
       special_registers_opdec_1_offs_to_data, special_registers_opdec_1_offs_write,
       special_registers_opdec_1_pk_dec, special_registers_opdec_1_pk_inc,
       special_registers_opdec_1_pk_to_addr, special_registers_opdec_1_pk_to_data,
       special_registers_opdec_1_pk_write, special_registers_opdec_1_sp_dec,
       special_registers_opdec_1_sp_inc, special_registers_opdec_1_sp_postinc_to_addr,
       special_registers_opdec_1_sp_predec_to_addr, special_registers_opdec_1_sp_to_addr,
       special_registers_opdec_1_sp_to_data, special_registers_opdec_1_sp_write,
       special_registers_opdec_2_offs_to_addr, special_registers_opdec_2_offs_to_data,
       special_registers_opdec_2_offs_write, special_registers_opdec_2_pk_dec,
       special_registers_opdec_2_pk_inc, special_registers_opdec_2_pk_to_addr,
       special_registers_opdec_2_pk_to_data, special_registers_opdec_2_pk_write,
       special_registers_opdec_2_sp_dec, special_registers_opdec_2_sp_inc,
       special_registers_opdec_2_sp_postinc_to_addr, special_registers_opdec_2_sp_predec_to_addr,
       special_registers_opdec_2_sp_to_addr, special_registers_opdec_2_sp_to_data,
       special_registers_opdec_2_sp_write;
  wire [3:0] pk_param_out, sp_param_out, special_registers_opdec_1_pk_param,
       special_registers_opdec_1_sp_param, special_registers_opdec_2_pk_param,
       special_registers_opdec_2_sp_param;
  wire [15:0] data_to_offs_out, data_to_pk_out, multiplexer_1_out, multiplexer_2_out, or_8_out, or_9_out,
       or_10_out, or_11_out, sixt_bit_gatekeeper_1_out_3, sixt_bit_gatekeeper_2_out_3,
       sixt_bit_gatekeeper_3_out_3, sixt_bit_gatekeeper_4_out_3, sixt_bit_gatekeeper_5_out_3,
       sixt_bit_gatekeeper_6_out_3, special_registers_opdec_1_data_to_offs,
       special_registers_opdec_1_data_to_pk, special_registers_opdec_2_data_to_offs,
       special_registers_opdec_2_data_to_pk, subtractor_1_out;

  Pull_Resistor pull_resistor_1 (.node(sp_reset_value));
  S_R_Flip_Flop s_r_ff_1 (.Qn(s_r_ff_1_qn), .preset(clock));  // open: S, R, clk, Q, reset
  Multiplexer #(.width(16)) multiplexer_1 (
    .in0(16'hefff), .in1(sp_reset_value), .out(multiplexer_1_out), .sel(not_1_out));
  not not_1 (not_1_out, sixt_bit_eq_zero_1_out_2);
  sixt_bit_eq_zero sixt_bit_eq_zero_1 (.in_1(sp_reset_value), .out_2(sixt_bit_eq_zero_1_out_2));
  or or_1 (or_1_out, s_r_ff_1_qn, reset);
  buf buffer_1 (buffer_1_out, clock);
  buf buffer_2 (buffer_2_out, buffer_1_out);
  buf buffer_3 (buffer_3_out, buffer_2_out);
  S_R_Flip_Flop s_r_ff_2 (.Q(s_r_ff_2_q), .reset(and_2_out), .preset(or_1_out));  // open: S, R, clk, Qn
  special_registers_opdec special_registers_opdec_1 (
    .ctrl_unit_in(temp_register), .control(control_bus_2), .data_in(data_bus_in),
    .data_to_offs(special_registers_opdec_1_data_to_offs), .sp_to_data(special_registers_opdec_1_sp_to_data),
    .sp_to_addr(special_registers_opdec_1_sp_to_addr), .sp_write(special_registers_opdec_1_sp_write),
    .sp_param(special_registers_opdec_1_sp_param), .sp_inc(special_registers_opdec_1_sp_inc),
    .sp_dec(special_registers_opdec_1_sp_dec),
    .sp_predec_to_addr(special_registers_opdec_1_sp_predec_to_addr),
    .sp_postinc_to_addr(special_registers_opdec_1_sp_postinc_to_addr),
    .offs_to_data(special_registers_opdec_1_offs_to_data),
    .offs_to_addr(special_registers_opdec_1_offs_to_addr), .offs_write(special_registers_opdec_1_offs_write),
    .data_to_pk(special_registers_opdec_1_data_to_pk), .pk_param(special_registers_opdec_1_pk_param),
    .pk_to_data(special_registers_opdec_1_pk_to_data), .pk_to_addr(special_registers_opdec_1_pk_to_addr),
    .pk_inc(special_registers_opdec_1_pk_inc), .pk_dec(special_registers_opdec_1_pk_dec),
    .pk_write(special_registers_opdec_1_pk_write));
  and and_1 (and_1_out, clock, ~buffer_4_out);  // AND_Gate
  buf buffer_4 (buffer_4_out, buffer_3_out);
  and and_2 (and_2_out, ~s_r_ff_3_q, buffer_7_out, s_r_ff_2_q);  // AND_Gate
  Multiplexer #(.width(16)) multiplexer_2 (
    .in0(data_bus_in), .in1(multiplexer_1_out), .out(multiplexer_2_out), .sel(s_r_ff_2_q));
  D_Flip_Flop d_ff_1 (.D(clock), .clk(s_r_ff_2_q), .Q(d_ff_1_q), .reset(and_1_out));  // open: Qn, preset
  buf buffer_5 (buffer_5_out, and_1_out);
  buf buffer_6 (buffer_6_out, buffer_5_out);
  buf buffer_7 (buffer_7_out, buffer_6_out);
  S_R_Flip_Flop s_r_ff_3 (.Q(s_r_ff_3_q), .reset(and_1_out), .preset(and_3_out));  // open: S, R, clk, Qn
  special_registers_opdec special_registers_opdec_2 (
    .ctrl_unit_in(temp_register), .control(control_bus_1), .data_in(data_bus_in),
    .data_to_offs(special_registers_opdec_2_data_to_offs), .sp_to_data(special_registers_opdec_2_sp_to_data),
    .sp_to_addr(special_registers_opdec_2_sp_to_addr), .sp_write(special_registers_opdec_2_sp_write),
    .sp_param(special_registers_opdec_2_sp_param), .sp_inc(special_registers_opdec_2_sp_inc),
    .sp_dec(special_registers_opdec_2_sp_dec),
    .sp_predec_to_addr(special_registers_opdec_2_sp_predec_to_addr),
    .sp_postinc_to_addr(special_registers_opdec_2_sp_postinc_to_addr),
    .offs_to_data(special_registers_opdec_2_offs_to_data),
    .offs_to_addr(special_registers_opdec_2_offs_to_addr), .offs_write(special_registers_opdec_2_offs_write),
    .data_to_pk(special_registers_opdec_2_data_to_pk), .pk_param(special_registers_opdec_2_pk_param),
    .pk_to_data(special_registers_opdec_2_pk_to_data), .pk_to_addr(special_registers_opdec_2_pk_to_addr),
    .pk_inc(special_registers_opdec_2_pk_inc), .pk_dec(special_registers_opdec_2_pk_dec),
    .pk_write(special_registers_opdec_2_pk_write));
  and and_3 (and_3_out, d_ff_1_q, ~s_r_ff_3_q);  // AND_Gate
  assign data_to_pk_out = special_registers_opdec_2_data_to_pk | special_registers_opdec_1_data_to_pk;  // OR_Gate data_to_pk, 16 bits wide
  or pk_to_addr (pk_to_addr_out, special_registers_opdec_2_pk_to_addr, special_registers_opdec_1_pk_to_addr);
  or pk_to_data (pk_to_data_out, special_registers_opdec_2_pk_to_data, special_registers_opdec_1_pk_to_data);
  assign pk_param_out = special_registers_opdec_2_pk_param | special_registers_opdec_1_pk_param;  // OR_Gate pk_param, 4 bits wide
  or pk_increment (pk_increment_out, special_registers_opdec_2_pk_inc, special_registers_opdec_1_pk_inc);
  or pk_decrement (pk_decrement_out, special_registers_opdec_2_pk_dec, special_registers_opdec_1_pk_dec);
  or pk_write (pk_write_out, special_registers_opdec_2_pk_write, special_registers_opdec_1_pk_write);
  or sp_to_data (sp_to_data_out, special_registers_opdec_2_sp_to_data, special_registers_opdec_1_sp_to_data);
  or sp_to_addr (sp_to_addr_out, special_registers_opdec_2_sp_to_addr, special_registers_opdec_1_sp_to_addr);
  assign sp_param_out = special_registers_opdec_2_sp_param | special_registers_opdec_1_sp_param;  // OR_Gate sp_param, 4 bits wide
  or sp_increment (sp_increment_out, special_registers_opdec_2_sp_inc, special_registers_opdec_1_sp_inc);
  or sp_decrement (sp_decrement_out, special_registers_opdec_2_sp_dec, special_registers_opdec_1_sp_dec);
  or sp_predec_to_addr (sp_predec_to_addr_out, special_registers_opdec_2_sp_predec_to_addr, special_registers_opdec_1_sp_predec_to_addr);
  or sp_postinc_to_addr (sp_postinc_to_addr_out, special_registers_opdec_2_sp_postinc_to_addr, special_registers_opdec_1_sp_postinc_to_addr);
  or sp_write (sp_write_out, special_registers_opdec_2_sp_write, special_registers_opdec_1_sp_write);
  or offs_to_data (offs_to_data_out, special_registers_opdec_2_offs_to_data, special_registers_opdec_1_offs_to_data);
  or offs_to_addr (offs_to_addr_out, special_registers_opdec_2_offs_to_addr, special_registers_opdec_1_offs_to_addr);
  assign data_to_offs_out = special_registers_opdec_2_data_to_offs | special_registers_opdec_1_data_to_offs;  // OR_Gate data_to_offs, 16 bits wide
  or offs_write (offs_write_out, special_registers_opdec_2_offs_write, special_registers_opdec_1_offs_write);
  or or_2 (or_2_out, sp_predec_to_addr_out, sp_decrement_out);
  or or_3 (or_3_out, sp_write_out, s_r_ff_2_q);
  or or_4 (or_4_out, sp_postinc_to_addr_out, sp_increment_out);
  or or_5 (or_5_out, sp_predec_to_addr_out, sp_postinc_to_addr_out, sp_to_addr_out);
  // Probe on data_to_pk_out
  Register #(.width(16)) register_1 (
    .D(data_to_offs_out), .en(offs_write_out), .clk(clock), .Q(offset_out), .clr(or_1_out));
  counting_register counting_register_1 (
    .data_in(data_to_pk_out), .param(pk_param_out), .increment(pk_increment_out),
    .decrement(pk_decrement_out), .write(pk_write_out), .clk(clock), .reset(or_1_out), .out_8(program_kounter));
  sixt_bit_gatekeeper sixt_bit_gatekeeper_1 (
    .in_1(pk_to_data_out), .in_2(program_kounter), .out_3(sixt_bit_gatekeeper_1_out_3));
  counting_register counting_register_2 (
    .data_in(multiplexer_2_out), .param(sp_param_out), .increment(or_4_out), .decrement(or_2_out),
    .write(or_3_out), .clk(clock), .out_8(stack_pointer));  // open: reset
  sixt_bit_gatekeeper sixt_bit_gatekeeper_2 (
    .in_1(or_5_out), .in_2(stack_pointer), .out_3(sixt_bit_gatekeeper_2_out_3));
  assign data_bus_out = sixt_bit_gatekeeper_1_out_3 | or_8_out;  // OR_Gate or_6, 16 bits wide
  assign addr_bus_out = sixt_bit_gatekeeper_3_out_3 | or_10_out;  // OR_Gate or_7, 16 bits wide
  sixt_bit_gatekeeper sixt_bit_gatekeeper_3 (
    .in_1(pk_to_addr_out), .in_2(program_kounter), .out_3(sixt_bit_gatekeeper_3_out_3));
  assign or_8_out = sixt_bit_gatekeeper_4_out_3 | or_9_out;  // OR_Gate or_8, 16 bits wide
  sixt_bit_gatekeeper sixt_bit_gatekeeper_4 (
    .in_1(sp_to_data_out), .in_2(stack_pointer), .out_3(sixt_bit_gatekeeper_4_out_3));
  Subtractor #(.width(16)) subtractor_1 (
    .a(sixt_bit_gatekeeper_2_out_3), .b({16{1'b0}}), .out(subtractor_1_out), .bin(sp_predec_to_addr_out));  // open: bout
  assign or_9_out = sixt_bit_gatekeeper_5_out_3 | sixt_bit_gatekeeper_5_out_3;  // OR_Gate or_9, 16 bits wide
  sixt_bit_gatekeeper sixt_bit_gatekeeper_5 (
    .in_1(offs_to_data_out), .in_2(offset_out), .out_3(sixt_bit_gatekeeper_5_out_3));
  sixt_bit_gatekeeper sixt_bit_gatekeeper_6 (
    .in_1(offs_to_addr_out), .in_2(offset_out), .out_3(sixt_bit_gatekeeper_6_out_3));
  // Probe on program_kounter
  // Probe on stack_pointer
  assign or_10_out = subtractor_1_out | or_11_out;  // OR_Gate or_10, 16 bits wide
  assign or_11_out = sixt_bit_gatekeeper_6_out_3 | sixt_bit_gatekeeper_6_out_3;  // OR_Gate or_11, 16 bits wide

  // Notes on the sheet:
  //   this part handles automatic
  //   resetting of sp to a default
  //   value
  //   --->
endmodule

module temp_registers (
  input  [15:0] data_bus_in,
  input  [15:0] control_bus_1,
  input  [15:0] control_bus_2,
  input  [15:0] ram_direct,
  input  clock,
  input  reset,
  output [15:0] data_bus_out,
  output [15:0] addr_bus_out,
  output [15:0] out_9,
  output [15:0] to_sreg,
  output [15:0] out_11,
  output [15:0] out_12
);

  wire or_1_out, or_2_out, or_3_out, sixt_bit_eq_cmp_1_out_3, sixt_bit_eq_cmp_2_out_3,
       sixt_bit_eq_cmp_3_out_3, special_register_dual_opdec_1_addr_bus_enable,
       special_register_dual_opdec_1_data_bus_enable, special_register_dual_opdec_1_write_enable,
       special_register_dual_opdec_2_addr_bus_enable, special_register_dual_opdec_2_data_bus_enable,
       special_register_dual_opdec_2_write_enable, special_register_dual_opdec_3_addr_bus_enable,
       special_register_dual_opdec_3_data_bus_enable, special_register_dual_opdec_3_write_enable;
  wire [15:0] multiplexer_1_out, register_1_q, sixt_bit_gatekeeper_1_out_3, sixt_bit_gatekeeper_2_out_3,
       sixt_bit_gatekeeper_3_out_3, sixt_bit_gatekeeper_4_out_3, sixt_bit_gatekeeper_5_out_3,
       sixt_bit_gatekeeper_6_out_3, sixt_bit_gatekeeper_7_out_3, sixt_bit_gatekeeper_8_out_3,
       sixt_bit_gatekeeper_9_out_3, special_register_dual_opdec_1_special_functions,
       special_register_dual_opdec_2_special_functions, special_register_dual_opdec_3_special_functions,
       special_register_dual_opdec_4_special_functions;

  Register #(.trigger("falling"), .width(16)) register_1 (
    .D(data_bus_in), .clk(clock), .Q(register_1_q), .clr(reset));  // open: en
  sixt_bit_eq_cmp sixt_bit_eq_cmp_1 (.in_1(control_bus_1), .in_2(16'h13), .out_3(sixt_bit_eq_cmp_1_out_3));
  sixt_bit_eq_cmp sixt_bit_eq_cmp_2 (.in_1(16'h13), .in_2(control_bus_2), .out_3(sixt_bit_eq_cmp_2_out_3));
  sixt_bit_eq_cmp sixt_bit_eq_cmp_3 (.in_1(control_bus_1), .in_2(16'h1), .out_3(sixt_bit_eq_cmp_3_out_3));
  special_register_dual_opdec special_register_dual_opdec_1 (
    .control_bus_2(control_bus_2), .id(4'b0010), .control_bus_1(control_bus_1),
    .data_bus_enable(special_register_dual_opdec_1_data_bus_enable),
    .addr_bus_enable(special_register_dual_opdec_1_addr_bus_enable),
    .write_enable(special_register_dual_opdec_1_write_enable),
    .special_functions(special_register_dual_opdec_1_special_functions));  // open: param
  or or_1 (or_1_out, sixt_bit_eq_cmp_1_out_3, special_register_dual_opdec_1_special_functions[0], sixt_bit_eq_cmp_2_out_3);
  special_register_dual_opdec special_register_dual_opdec_2 (
    .control_bus_2(control_bus_2), .id(4'b0011), .control_bus_1(control_bus_1),
    .data_bus_enable(special_register_dual_opdec_2_data_bus_enable),
    .addr_bus_enable(special_register_dual_opdec_2_addr_bus_enable),
    .write_enable(special_register_dual_opdec_2_write_enable),
    .special_functions(special_register_dual_opdec_2_special_functions));  // open: param
  special_register_dual_opdec special_register_dual_opdec_3 (
    .control_bus_2(control_bus_2), .id(4'b0100), .control_bus_1(control_bus_1),
    .data_bus_enable(special_register_dual_opdec_3_data_bus_enable),
    .addr_bus_enable(special_register_dual_opdec_3_addr_bus_enable),
    .write_enable(special_register_dual_opdec_3_write_enable),
    .special_functions(special_register_dual_opdec_3_special_functions));  // open: param
  or or_2 (or_2_out, special_register_dual_opdec_3_special_functions[0], special_register_dual_opdec_4_special_functions[0]);
  or or_3 (or_3_out, special_register_dual_opdec_3_write_enable, sixt_bit_eq_cmp_3_out_3);
  special_register_dual_opdec special_register_dual_opdec_4 (
    .control_bus_2(control_bus_2), .id(4'b0101), .control_bus_1(control_bus_1),
    .special_functions(special_register_dual_opdec_4_special_functions));  // open: data_bus_enable, addr_bus_enable, write_enable, param
  Register #(.width(16)) register_2 (
    .D(register_1_q), .en(special_register_dual_opdec_1_write_enable), .clk(clock), .Q(out_9), .clr(reset));
  Register #(.width(16)) register_3 (
    .D(register_1_q), .en(special_register_dual_opdec_2_write_enable), .clk(clock), .Q(out_11), .clr(reset));
  Multiplexer #(.width(16)) multiplexer_1 (
    .in0(register_1_q), .in1(ram_direct), .out(multiplexer_1_out), .sel(or_3_out));
  Register #(.width(16)) register_4 (.D(multiplexer_1_out), .en(or_3_out), .clk(clock), .Q(out_12), .clr(reset));
  // Probe on out_12
  sixt_bit_gatekeeper sixt_bit_gatekeeper_1 (
    .in_1(special_register_dual_opdec_1_data_bus_enable), .in_2(out_9), .out_3(sixt_bit_gatekeeper_1_out_3));
  sixt_bit_gatekeeper sixt_bit_gatekeeper_2 (
    .in_1(special_register_dual_opdec_1_addr_bus_enable), .in_2(out_9), .out_3(sixt_bit_gatekeeper_2_out_3));
  sixt_bit_gatekeeper sixt_bit_gatekeeper_3 (.in_1(or_1_out), .in_2(out_9), .out_3(sixt_bit_gatekeeper_3_out_3));
  sixt_bit_gatekeeper sixt_bit_gatekeeper_4 (
    .in_1(special_register_dual_opdec_2_data_bus_enable), .in_2(out_11), .out_3(sixt_bit_gatekeeper_4_out_3));
  sixt_bit_gatekeeper sixt_bit_gatekeeper_5 (
    .in_1(special_register_dual_opdec_2_addr_bus_enable), .in_2(out_11), .out_3(sixt_bit_gatekeeper_5_out_3));
  sixt_bit_gatekeeper sixt_bit_gatekeeper_6 (
    .in_1(special_register_dual_opdec_2_special_functions[0]), .in_2(out_11),
    .out_3(sixt_bit_gatekeeper_6_out_3));
  sixt_bit_gatekeeper sixt_bit_gatekeeper_7 (
    .in_1(special_register_dual_opdec_3_data_bus_enable), .in_2(out_12), .out_3(sixt_bit_gatekeeper_7_out_3));
  sixt_bit_gatekeeper sixt_bit_gatekeeper_8 (
    .in_1(special_register_dual_opdec_3_addr_bus_enable), .in_2(out_12), .out_3(sixt_bit_gatekeeper_8_out_3));
  sixt_bit_gatekeeper sixt_bit_gatekeeper_9 (.in_1(or_2_out), .in_2(out_12), .out_3(sixt_bit_gatekeeper_9_out_3));
  assign data_bus_out = sixt_bit_gatekeeper_1_out_3 | sixt_bit_gatekeeper_4_out_3 | sixt_bit_gatekeeper_7_out_3;  // OR_Gate or_4, 16 bits wide
  assign addr_bus_out = sixt_bit_gatekeeper_2_out_3 | sixt_bit_gatekeeper_8_out_3 | sixt_bit_gatekeeper_5_out_3;  // OR_Gate or_5, 16 bits wide
  assign to_sreg = sixt_bit_gatekeeper_3_out_3 | sixt_bit_gatekeeper_9_out_3 | sixt_bit_gatekeeper_6_out_3;  // OR_Gate or_6, 16 bits wide
endmodule

module register_unit (
  input  [15:0] data_bus_in,
  input  [15:0] control_bus_1,
  input  [15:0] control_bus_2,
  input  clock,
  input  reset,
  output [15:0] data_bus_out,
  output [15:0] addr_bus_out,
  output [15:0] alu1_out,
  output [15:0] alu2_out
);

  wire and_5_out, and_6_out, and_7_out, and_8_out, and_9_out, and_10_out, and_11_out, and_12_out, and_13_out,
       and_14_out, and_15_out, and_16_out, and_17_out, and_18_out, and_19_out, and_20_out, and_21_out,
       and_22_out, and_23_out, and_24_out, eight_bit_eq_cmp_1_out_3, eight_bit_eq_cmp_2_out_3,
       eight_bit_eq_cmp_3_out_3, eight_bit_eq_cmp_4_out_3, eight_bit_eq_cmp_5_out_3,
       eight_bit_eq_cmp_6_out_3, eight_bit_eq_cmp_7_out_3, eight_bit_eq_cmp_8_out_3,
       eight_bit_eq_cmp_9_out_3, eight_bit_eq_cmp_10_out_3, eight_bit_eq_cmp_11_out_3,
       eight_bit_eq_cmp_12_out_3, four_bit_eq_cmp_1_out_3, four_bit_eq_cmp_2_out_3, four_bit_eq_cmp_3_out_3,
       four_bit_eq_cmp_4_out_3, four_bit_eq_cmp_5_out_3, four_bit_eq_cmp_6_out_3, four_bit_eq_cmp_7_out_3,
       four_bit_eq_cmp_8_out_3, four_bit_eq_cmp_9_out_3, four_bit_eq_cmp_10_out_3, four_bit_eq_cmp_11_out_3,
       four_bit_eq_cmp_12_out_3, four_bit_eq_cmp_13_out_3, four_bit_eq_cmp_14_out_3,
       four_bit_eq_cmp_15_out_3, four_bit_eq_cmp_16_out_3, four_bit_eq_cmp_17_out_3,
       four_bit_eq_cmp_18_out_3, four_bit_eq_cmp_19_out_3, four_bit_eq_cmp_20_out_3,
       four_bit_eq_cmp_21_out_3, four_bit_eq_cmp_22_out_3, four_bit_eq_cmp_23_out_3,
       four_bit_eq_cmp_24_out_3, four_bit_eq_cmp_25_out_3, four_bit_eq_cmp_26_out_3,
       four_bit_eq_cmp_27_out_3, four_bit_eq_cmp_28_out_3, four_bit_eq_cmp_29_out_3,
       four_bit_eq_cmp_30_out_3, four_bit_eq_cmp_31_out_3, four_bit_eq_cmp_32_out_3,
       four_bit_eq_cmp_33_out_3, four_bit_eq_cmp_34_out_3, or_1_out, or_2_out, or_3_out, or_4_out, or_5_out,
       or_6_out, or_7_out, or_8_out, or_9_out, or_10_out, or_11_out, or_14_out, or_15_out;
  wire [3:0] and_1_out, and_2_out, and_3_out, and_4_out, bit_extender_1_out, bit_extender_2_out,
       bit_extender_3_out, bit_extender_4_out, or_12_out, or_13_out;
  wire [15:0] and_25_out, and_26_out, and_27_out, and_28_out, and_29_out, and_30_out, and_31_out, and_32_out,
       and_33_out, and_34_out, and_35_out, and_36_out, and_37_out, and_38_out, and_39_out, and_40_out,
       and_41_out, and_42_out, and_43_out, and_44_out, and_45_out, and_46_out, and_47_out, and_48_out,
       and_49_out, and_50_out, and_51_out, and_52_out, and_53_out, and_54_out, and_55_out, and_56_out,
       bit_extender_5_out, bit_extender_6_out, bit_extender_7_out, bit_extender_8_out, bit_extender_9_out,
       bit_extender_10_out, bit_extender_11_out, bit_extender_12_out, bit_extender_13_out,
       bit_extender_14_out, bit_extender_15_out, bit_extender_16_out, bit_extender_17_out,
       bit_extender_18_out, bit_extender_19_out, bit_extender_20_out, bit_extender_21_out,
       bit_extender_22_out, bit_extender_23_out, bit_extender_24_out, bit_extender_25_out,
       bit_extender_26_out, bit_extender_27_out, bit_extender_28_out, bit_extender_29_out,
       bit_extender_30_out, bit_extender_31_out, bit_extender_32_out, bit_extender_33_out,
       bit_extender_34_out, bit_extender_35_out, bit_extender_36_out, or_16_out, or_17_out, or_18_out,
       or_19_out, or_20_out, or_21_out, or_22_out, or_23_out, or_24_out, or_25_out, or_26_out, or_27_out,
       or_28_out, or_29_out, or_30_out, or_31_out, or_32_out, or_33_out, or_34_out, or_35_out, or_36_out,
       or_37_out, or_38_out, or_39_out, or_40_out, or_41_out, or_42_out, or_43_out, or_44_out, or_45_out,
       or_46_out, or_47_out, register_1_q, register_2_q, register_3_q, register_4_q, register_5_q,
       register_6_q, register_7_q, register_8_q, register_9_q, register_10_q, register_11_q, register_12_q,
       register_13_q, register_14_q, register_15_q, register_16_q, register_17_q;

  four_bit_eq_cmp four_bit_eq_cmp_1 (.in_1(control_bus_1[7:4]), .in_2(4'b0100), .out_3(four_bit_eq_cmp_1_out_3));
  eight_bit_eq_cmp eight_bit_eq_cmp_1 (.in_1(control_bus_1[7:0]), .in_2(8'h20), .out_3(eight_bit_eq_cmp_1_out_3));
  eight_bit_eq_cmp eight_bit_eq_cmp_2 (.in_1(control_bus_1[7:0]), .in_2(8'h21), .out_3(eight_bit_eq_cmp_2_out_3));
  eight_bit_eq_cmp eight_bit_eq_cmp_3 (.in_1(control_bus_1[7:0]), .in_2(8'h22), .out_3(eight_bit_eq_cmp_3_out_3));
  eight_bit_eq_cmp eight_bit_eq_cmp_4 (.in_1(control_bus_1[7:0]), .in_2(8'h23), .out_3(eight_bit_eq_cmp_4_out_3));
  eight_bit_eq_cmp eight_bit_eq_cmp_5 (.in_1(control_bus_1[7:0]), .in_2(8'h24), .out_3(eight_bit_eq_cmp_5_out_3));
  eight_bit_eq_cmp eight_bit_eq_cmp_6 (.in_1(control_bus_1[7:0]), .in_2(8'h2f), .out_3(eight_bit_eq_cmp_6_out_3));
  eight_bit_eq_cmp eight_bit_eq_cmp_7 (.in_1(control_bus_2[7:0]), .in_2(8'h20), .out_3(eight_bit_eq_cmp_7_out_3));
  eight_bit_eq_cmp eight_bit_eq_cmp_8 (.in_1(control_bus_2[7:0]), .in_2(8'h21), .out_3(eight_bit_eq_cmp_8_out_3));
  eight_bit_eq_cmp eight_bit_eq_cmp_9 (.in_1(control_bus_2[7:0]), .in_2(8'h22), .out_3(eight_bit_eq_cmp_9_out_3));
  eight_bit_eq_cmp eight_bit_eq_cmp_10 (.in_1(control_bus_2[7:0]), .in_2(8'h23), .out_3(eight_bit_eq_cmp_10_out_3));
  eight_bit_eq_cmp eight_bit_eq_cmp_11 (.in_1(control_bus_2[7:0]), .in_2(8'h24), .out_3(eight_bit_eq_cmp_11_out_3));
  eight_bit_eq_cmp eight_bit_eq_cmp_12 (.in_1(control_bus_2[7:0]), .in_2(8'h2f), .out_3(eight_bit_eq_cmp_12_out_3));
  four_bit_eq_cmp four_bit_eq_cmp_2 (.in_1(control_bus_2[7:4]), .in_2(4'b0100), .out_3(four_bit_eq_cmp_2_out_3));
  Register #(.trigger("falling"), .width(16)) register_1 (
    .D(data_bus_in), .clk(clock), .Q(register_1_q), .clr(reset));  // open: en
  or or_1 (or_1_out, eight_bit_eq_cmp_2_out_3, or_2_out);
  or or_2 (or_2_out, eight_bit_eq_cmp_3_out_3, eight_bit_eq_cmp_4_out_3);
  or or_3 (or_3_out, eight_bit_eq_cmp_1_out_3, four_bit_eq_cmp_1_out_3, eight_bit_eq_cmp_5_out_3);
  or or_4 (or_4_out, eight_bit_eq_cmp_8_out_3, or_5_out);
  or or_5 (or_5_out, eight_bit_eq_cmp_9_out_3, eight_bit_eq_cmp_10_out_3);
  assign bit_extender_1_out = {{3{or_6_out}}, or_6_out};  // Bit_Extender bit_extender_1
  or or_6 (or_6_out, four_bit_eq_cmp_1_out_3, or_1_out);
  assign bit_extender_2_out = {{3{or_3_out}}, or_3_out};  // Bit_Extender bit_extender_2
  assign bit_extender_3_out = {{3{or_7_out}}, or_7_out};  // Bit_Extender bit_extender_3
  or or_7 (or_7_out, four_bit_eq_cmp_2_out_3, or_4_out);
  assign bit_extender_4_out = {{3{or_8_out}}, or_8_out};  // Bit_Extender bit_extender_4
  or or_8 (or_8_out, eight_bit_eq_cmp_7_out_3, four_bit_eq_cmp_2_out_3, eight_bit_eq_cmp_11_out_3);
  assign and_1_out = bit_extender_1_out & control_bus_1[11:8];  // AND_Gate and_1, 4 bits wide
  assign and_2_out = bit_extender_2_out & control_bus_1[15:12];  // AND_Gate and_2, 4 bits wide
  assign and_3_out = bit_extender_3_out & control_bus_2[11:8];  // AND_Gate and_3, 4 bits wide
  assign and_4_out = bit_extender_4_out & control_bus_2[15:12];  // AND_Gate and_4, 4 bits wide
  or or_9 (or_9_out, eight_bit_eq_cmp_1_out_3, eight_bit_eq_cmp_7_out_3);
  or or_10 (or_10_out, or_1_out, or_4_out);
  or or_11 (or_11_out, eight_bit_eq_cmp_5_out_3, eight_bit_eq_cmp_11_out_3);
  assign or_12_out = and_1_out | and_3_out;  // OR_Gate or_12, 4 bits wide
  assign or_13_out = and_2_out | and_4_out;  // OR_Gate or_13, 4 bits wide
  assign bit_extender_5_out = {{15{four_bit_eq_cmp_3_out_3}}, four_bit_eq_cmp_3_out_3};  // Bit_Extender bit_extender_5
  four_bit_eq_cmp four_bit_eq_cmp_3 (.in_1(or_13_out), .in_2(4'b0000), .out_3(four_bit_eq_cmp_3_out_3));
  four_bit_eq_cmp four_bit_eq_cmp_4 (.in_1(or_12_out), .in_2(4'b0000), .out_3(four_bit_eq_cmp_4_out_3));
  assign bit_extender_6_out = {{15{four_bit_eq_cmp_4_out_3}}, four_bit_eq_cmp_4_out_3};  // Bit_Extender bit_extender_6
  assign bit_extender_7_out = {{15{four_bit_eq_cmp_5_out_3}}, four_bit_eq_cmp_5_out_3};  // Bit_Extender bit_extender_7
  four_bit_eq_cmp four_bit_eq_cmp_5 (.in_1(or_13_out), .in_2(4'b0001), .out_3(four_bit_eq_cmp_5_out_3));
  four_bit_eq_cmp four_bit_eq_cmp_6 (.in_1(or_12_out), .in_2(4'b0001), .out_3(four_bit_eq_cmp_6_out_3));
  assign bit_extender_8_out = {{15{four_bit_eq_cmp_6_out_3}}, four_bit_eq_cmp_6_out_3};  // Bit_Extender bit_extender_8
  assign bit_extender_9_out = {{15{four_bit_eq_cmp_7_out_3}}, four_bit_eq_cmp_7_out_3};  // Bit_Extender bit_extender_9
  four_bit_eq_cmp four_bit_eq_cmp_7 (.in_1(or_13_out), .in_2(4'b0010), .out_3(four_bit_eq_cmp_7_out_3));
  four_bit_eq_cmp four_bit_eq_cmp_8 (.in_1(or_12_out), .in_2(4'b0010), .out_3(four_bit_eq_cmp_8_out_3));
  assign bit_extender_10_out = {{15{four_bit_eq_cmp_8_out_3}}, four_bit_eq_cmp_8_out_3};  // Bit_Extender bit_extender_10
  assign bit_extender_11_out = {{15{four_bit_eq_cmp_9_out_3}}, four_bit_eq_cmp_9_out_3};  // Bit_Extender bit_extender_11
  four_bit_eq_cmp four_bit_eq_cmp_9 (.in_1(or_13_out), .in_2(4'b0011), .out_3(four_bit_eq_cmp_9_out_3));
  four_bit_eq_cmp four_bit_eq_cmp_10 (.in_1(or_12_out), .in_2(4'b0011), .out_3(four_bit_eq_cmp_10_out_3));
  assign bit_extender_12_out = {{15{four_bit_eq_cmp_10_out_3}}, four_bit_eq_cmp_10_out_3};  // Bit_Extender bit_extender_12
  assign bit_extender_13_out = {{15{four_bit_eq_cmp_11_out_3}}, four_bit_eq_cmp_11_out_3};  // Bit_Extender bit_extender_13
  four_bit_eq_cmp four_bit_eq_cmp_11 (.in_1(or_13_out), .in_2(4'b0100), .out_3(four_bit_eq_cmp_11_out_3));
  four_bit_eq_cmp four_bit_eq_cmp_12 (.in_1(or_12_out), .in_2(4'b0100), .out_3(four_bit_eq_cmp_12_out_3));
  assign bit_extender_14_out = {{15{four_bit_eq_cmp_12_out_3}}, four_bit_eq_cmp_12_out_3};  // Bit_Extender bit_extender_14
  assign bit_extender_15_out = {{15{four_bit_eq_cmp_13_out_3}}, four_bit_eq_cmp_13_out_3};  // Bit_Extender bit_extender_15
  four_bit_eq_cmp four_bit_eq_cmp_13 (.in_1(or_13_out), .in_2(4'b0101), .out_3(four_bit_eq_cmp_13_out_3));
  four_bit_eq_cmp four_bit_eq_cmp_14 (.in_1(or_12_out), .in_2(4'b0101), .out_3(four_bit_eq_cmp_14_out_3));
  assign bit_extender_16_out = {{15{four_bit_eq_cmp_14_out_3}}, four_bit_eq_cmp_14_out_3};  // Bit_Extender bit_extender_16
  assign bit_extender_17_out = {{15{four_bit_eq_cmp_15_out_3}}, four_bit_eq_cmp_15_out_3};  // Bit_Extender bit_extender_17
  four_bit_eq_cmp four_bit_eq_cmp_15 (.in_1(or_13_out), .in_2(4'b0110), .out_3(four_bit_eq_cmp_15_out_3));
  four_bit_eq_cmp four_bit_eq_cmp_16 (.in_1(or_12_out), .in_2(4'b0110), .out_3(four_bit_eq_cmp_16_out_3));
  assign bit_extender_18_out = {{15{four_bit_eq_cmp_16_out_3}}, four_bit_eq_cmp_16_out_3};  // Bit_Extender bit_extender_18
  assign bit_extender_19_out = {{15{four_bit_eq_cmp_17_out_3}}, four_bit_eq_cmp_17_out_3};  // Bit_Extender bit_extender_19
  four_bit_eq_cmp four_bit_eq_cmp_17 (.in_1(or_13_out), .in_2(4'b0111), .out_3(four_bit_eq_cmp_17_out_3));
  four_bit_eq_cmp four_bit_eq_cmp_18 (.in_1(or_12_out), .in_2(4'b0111), .out_3(four_bit_eq_cmp_18_out_3));
  assign bit_extender_20_out = {{15{four_bit_eq_cmp_18_out_3}}, four_bit_eq_cmp_18_out_3};  // Bit_Extender bit_extender_20
  assign bit_extender_21_out = {{15{four_bit_eq_cmp_19_out_3}}, four_bit_eq_cmp_19_out_3};  // Bit_Extender bit_extender_21
  four_bit_eq_cmp four_bit_eq_cmp_19 (.in_1(or_13_out), .in_2(4'b1000), .out_3(four_bit_eq_cmp_19_out_3));
  four_bit_eq_cmp four_bit_eq_cmp_20 (.in_1(or_12_out), .in_2(4'b1000), .out_3(four_bit_eq_cmp_20_out_3));
  assign bit_extender_22_out = {{15{four_bit_eq_cmp_20_out_3}}, four_bit_eq_cmp_20_out_3};  // Bit_Extender bit_extender_22
  assign bit_extender_23_out = {{15{four_bit_eq_cmp_21_out_3}}, four_bit_eq_cmp_21_out_3};  // Bit_Extender bit_extender_23
  four_bit_eq_cmp four_bit_eq_cmp_21 (.in_1(or_13_out), .in_2(4'b1001), .out_3(four_bit_eq_cmp_21_out_3));
  four_bit_eq_cmp four_bit_eq_cmp_22 (.in_1(or_12_out), .in_2(4'b1001), .out_3(four_bit_eq_cmp_22_out_3));
  assign bit_extender_24_out = {{15{four_bit_eq_cmp_22_out_3}}, four_bit_eq_cmp_22_out_3};  // Bit_Extender bit_extender_24
  assign bit_extender_25_out = {{15{four_bit_eq_cmp_23_out_3}}, four_bit_eq_cmp_23_out_3};  // Bit_Extender bit_extender_25
  four_bit_eq_cmp four_bit_eq_cmp_23 (.in_1(or_13_out), .in_2(4'b1010), .out_3(four_bit_eq_cmp_23_out_3));
  four_bit_eq_cmp four_bit_eq_cmp_24 (.in_1(or_12_out), .in_2(4'b1010), .out_3(four_bit_eq_cmp_24_out_3));
  assign bit_extender_26_out = {{15{four_bit_eq_cmp_24_out_3}}, four_bit_eq_cmp_24_out_3};  // Bit_Extender bit_extender_26
  assign bit_extender_27_out = {{15{four_bit_eq_cmp_25_out_3}}, four_bit_eq_cmp_25_out_3};  // Bit_Extender bit_extender_27
  four_bit_eq_cmp four_bit_eq_cmp_25 (.in_1(or_13_out), .in_2(4'b1011), .out_3(four_bit_eq_cmp_25_out_3));
  four_bit_eq_cmp four_bit_eq_cmp_26 (.in_1(or_12_out), .in_2(4'b1011), .out_3(four_bit_eq_cmp_26_out_3));
  assign bit_extender_28_out = {{15{four_bit_eq_cmp_26_out_3}}, four_bit_eq_cmp_26_out_3};  // Bit_Extender bit_extender_28
  assign bit_extender_29_out = {{15{four_bit_eq_cmp_27_out_3}}, four_bit_eq_cmp_27_out_3};  // Bit_Extender bit_extender_29
  four_bit_eq_cmp four_bit_eq_cmp_27 (.in_1(or_13_out), .in_2(4'b1100), .out_3(four_bit_eq_cmp_27_out_3));
  four_bit_eq_cmp four_bit_eq_cmp_28 (.in_1(or_12_out), .in_2(4'b1100), .out_3(four_bit_eq_cmp_28_out_3));
  assign bit_extender_30_out = {{15{four_bit_eq_cmp_28_out_3}}, four_bit_eq_cmp_28_out_3};  // Bit_Extender bit_extender_30
  assign bit_extender_31_out = {{15{four_bit_eq_cmp_29_out_3}}, four_bit_eq_cmp_29_out_3};  // Bit_Extender bit_extender_31
  four_bit_eq_cmp four_bit_eq_cmp_29 (.in_1(or_13_out), .in_2(4'b1101), .out_3(four_bit_eq_cmp_29_out_3));
  four_bit_eq_cmp four_bit_eq_cmp_30 (.in_1(or_12_out), .in_2(4'b1101), .out_3(four_bit_eq_cmp_30_out_3));
  assign bit_extender_32_out = {{15{four_bit_eq_cmp_30_out_3}}, four_bit_eq_cmp_30_out_3};  // Bit_Extender bit_extender_32
  assign bit_extender_33_out = {{15{four_bit_eq_cmp_31_out_3}}, four_bit_eq_cmp_31_out_3};  // Bit_Extender bit_extender_33
  four_bit_eq_cmp four_bit_eq_cmp_31 (.in_1(or_13_out), .in_2(4'b1110), .out_3(four_bit_eq_cmp_31_out_3));
  four_bit_eq_cmp four_bit_eq_cmp_32 (.in_1(or_12_out), .in_2(4'b1110), .out_3(four_bit_eq_cmp_32_out_3));
  assign bit_extender_34_out = {{15{four_bit_eq_cmp_32_out_3}}, four_bit_eq_cmp_32_out_3};  // Bit_Extender bit_extender_34
  assign bit_extender_35_out = {{15{four_bit_eq_cmp_33_out_3}}, four_bit_eq_cmp_33_out_3};  // Bit_Extender bit_extender_35
  four_bit_eq_cmp four_bit_eq_cmp_33 (.in_1(or_13_out), .in_2(4'b1111), .out_3(four_bit_eq_cmp_33_out_3));
  four_bit_eq_cmp four_bit_eq_cmp_34 (.in_1(or_12_out), .in_2(4'b1111), .out_3(four_bit_eq_cmp_34_out_3));
  assign bit_extender_36_out = {{15{four_bit_eq_cmp_34_out_3}}, four_bit_eq_cmp_34_out_3};  // Bit_Extender bit_extender_36
  and and_5 (and_5_out, or_11_out, four_bit_eq_cmp_3_out_3);
  and and_6 (and_6_out, or_11_out, four_bit_eq_cmp_5_out_3);
  and and_7 (and_7_out, or_11_out, four_bit_eq_cmp_7_out_3);
  and and_8 (and_8_out, or_11_out, four_bit_eq_cmp_9_out_3);
  and and_9 (and_9_out, or_11_out, four_bit_eq_cmp_11_out_3);
  and and_10 (and_10_out, or_11_out, four_bit_eq_cmp_13_out_3);
  and and_11 (and_11_out, or_11_out, four_bit_eq_cmp_15_out_3);
  and and_12 (and_12_out, or_11_out, four_bit_eq_cmp_17_out_3);
  and and_13 (and_13_out, or_11_out, four_bit_eq_cmp_19_out_3);
  and and_14 (and_14_out, or_11_out, four_bit_eq_cmp_21_out_3);
  and and_15 (and_15_out, or_11_out, four_bit_eq_cmp_23_out_3);
  and and_16 (and_16_out, or_11_out, four_bit_eq_cmp_25_out_3);
  and and_17 (and_17_out, or_11_out, four_bit_eq_cmp_27_out_3);
  and and_18 (and_18_out, or_11_out, four_bit_eq_cmp_29_out_3);
  and and_19 (and_19_out, or_11_out, four_bit_eq_cmp_31_out_3);
  and and_20 (and_20_out, or_11_out, four_bit_eq_cmp_33_out_3);
  Register #(.width(16)) register_2 (.D(register_1_q), .en(and_5_out), .clk(clock), .Q(register_2_q), .clr(reset));
  Register #(.width(16)) register_3 (.D(register_1_q), .en(and_6_out), .clk(clock), .Q(register_3_q), .clr(reset));
  Register #(.width(16)) register_4 (.D(register_1_q), .en(and_7_out), .clk(clock), .Q(register_4_q), .clr(reset));
  Register #(.width(16)) register_5 (.D(register_1_q), .en(and_8_out), .clk(clock), .Q(register_5_q), .clr(reset));
  Register #(.width(16)) register_6 (.D(register_1_q), .en(and_9_out), .clk(clock), .Q(register_6_q), .clr(reset));
  Register #(.width(16)) register_7 (.D(register_1_q), .en(and_10_out), .clk(clock), .Q(register_7_q), .clr(reset));
  Register #(.width(16)) register_8 (.D(register_1_q), .en(and_11_out), .clk(clock), .Q(register_8_q), .clr(reset));
  Register #(.width(16)) register_9 (.D(register_1_q), .en(and_12_out), .clk(clock), .Q(register_9_q), .clr(reset));
  Register #(.width(16)) register_10 (.D(register_1_q), .en(and_13_out), .clk(clock), .Q(register_10_q), .clr(reset));
  Register #(.width(16)) register_11 (.D(register_1_q), .en(and_14_out), .clk(clock), .Q(register_11_q), .clr(reset));
  Register #(.width(16)) register_12 (.D(register_1_q), .en(and_15_out), .clk(clock), .Q(register_12_q), .clr(reset));
  Register #(.width(16)) register_13 (.D(register_1_q), .en(and_16_out), .clk(clock), .Q(register_13_q), .clr(reset));
  Register #(.width(16)) register_14 (.D(register_1_q), .en(and_17_out), .clk(clock), .Q(register_14_q), .clr(reset));
  Register #(.width(16)) register_15 (.D(register_1_q), .en(and_18_out), .clk(clock), .Q(register_15_q), .clr(reset));
  Register #(.width(16)) register_16 (.D(register_1_q), .en(and_19_out), .clk(clock), .Q(register_16_q), .clr(reset));
  Register #(.width(16)) register_17 (.D(register_1_q), .en(and_20_out), .clk(clock), .Q(register_17_q), .clr(reset));
  and and_21 (and_21_out, control_bus_1[12], eight_bit_eq_cmp_6_out_3);
  or or_14 (or_14_out, and_24_out, and_22_out);
  and and_22 (and_22_out, ~control_bus_1[12], eight_bit_eq_cmp_6_out_3);  // AND_Gate
  or or_15 (or_15_out, and_21_out, and_23_out);
  and and_23 (and_23_out, control_bus_2[12], eight_bit_eq_cmp_12_out_3);
  and and_24 (and_24_out, ~control_bus_2[12], eight_bit_eq_cmp_12_out_3);  // AND_Gate
  assign and_25_out = register_2_q & bit_extender_5_out;  // AND_Gate and_25, 16 bits wide
  assign or_16_out = and_25_out | and_25_out;  // OR_Gate or_16, 16 bits wide
  assign and_26_out = register_3_q & bit_extender_7_out;  // AND_Gate and_26, 16 bits wide
  assign or_17_out = and_26_out | or_16_out;  // OR_Gate or_17, 16 bits wide
  assign and_27_out = register_4_q & bit_extender_9_out;  // AND_Gate and_27, 16 bits wide
  assign or_18_out = and_27_out | or_17_out;  // OR_Gate or_18, 16 bits wide
  assign and_28_out = register_5_q & bit_extender_11_out;  // AND_Gate and_28, 16 bits wide
  assign or_19_out = and_28_out | or_18_out;  // OR_Gate or_19, 16 bits wide
  assign and_29_out = register_6_q & bit_extender_13_out;  // AND_Gate and_29, 16 bits wide
  assign or_20_out = and_29_out | or_19_out;  // OR_Gate or_20, 16 bits wide
  assign and_30_out = register_7_q & bit_extender_15_out;  // AND_Gate and_30, 16 bits wide
  assign or_21_out = and_30_out | or_20_out;  // OR_Gate or_21, 16 bits wide
  assign and_31_out = register_8_q & bit_extender_17_out;  // AND_Gate and_31, 16 bits wide
  assign or_22_out = and_31_out | or_21_out;  // OR_Gate or_22, 16 bits wide
  assign and_32_out = register_9_q & bit_extender_19_out;  // AND_Gate and_32, 16 bits wide
  assign or_23_out = and_32_out | or_22_out;  // OR_Gate or_23, 16 bits wide
  assign and_33_out = register_10_q & bit_extender_21_out;  // AND_Gate and_33, 16 bits wide
  assign or_24_out = and_33_out | or_23_out;  // OR_Gate or_24, 16 bits wide
  assign and_34_out = register_11_q & bit_extender_23_out;  // AND_Gate and_34, 16 bits wide
  assign or_25_out = and_34_out | or_24_out;  // OR_Gate or_25, 16 bits wide
  assign and_35_out = register_12_q & bit_extender_25_out;  // AND_Gate and_35, 16 bits wide
  assign or_26_out = and_35_out | or_25_out;  // OR_Gate or_26, 16 bits wide
  assign and_36_out = register_13_q & bit_extender_27_out;  // AND_Gate and_36, 16 bits wide
  assign or_27_out = and_36_out | or_26_out;  // OR_Gate or_27, 16 bits wide
  assign and_37_out = register_14_q & bit_extender_29_out;  // AND_Gate and_37, 16 bits wide
  assign or_28_out = and_37_out | or_27_out;  // OR_Gate or_28, 16 bits wide
  assign and_38_out = register_15_q & bit_extender_31_out;  // AND_Gate and_38, 16 bits wide
  assign or_29_out = and_38_out | or_28_out;  // OR_Gate or_29, 16 bits wide
  assign and_39_out = register_16_q & bit_extender_33_out;  // AND_Gate and_39, 16 bits wide
  assign or_30_out = and_39_out | or_29_out;  // OR_Gate or_30, 16 bits wide
  assign and_40_out = register_17_q & bit_extender_35_out;  // AND_Gate and_40, 16 bits wide
  assign or_31_out = and_40_out | or_30_out;  // OR_Gate or_31, 16 bits wide
  assign and_41_out = register_2_q & bit_extender_6_out;  // AND_Gate and_41, 16 bits wide
  assign or_32_out = and_41_out | and_41_out;  // OR_Gate or_32, 16 bits wide
  assign and_42_out = register_3_q & bit_extender_8_out;  // AND_Gate and_42, 16 bits wide
  assign or_33_out = and_42_out | or_32_out;  // OR_Gate or_33, 16 bits wide
  assign and_43_out = register_4_q & bit_extender_10_out;  // AND_Gate and_43, 16 bits wide
  assign or_34_out = and_43_out | or_33_out;  // OR_Gate or_34, 16 bits wide
  assign and_44_out = register_5_q & bit_extender_12_out;  // AND_Gate and_44, 16 bits wide
  assign or_35_out = and_44_out | or_34_out;  // OR_Gate or_35, 16 bits wide
  assign and_45_out = register_6_q & bit_extender_14_out;  // AND_Gate and_45, 16 bits wide
  assign or_36_out = and_45_out | or_35_out;  // OR_Gate or_36, 16 bits wide
  assign and_46_out = register_7_q & bit_extender_16_out;  // AND_Gate and_46, 16 bits wide
  assign or_37_out = and_46_out | or_36_out;  // OR_Gate or_37, 16 bits wide
  assign and_47_out = register_8_q & bit_extender_18_out;  // AND_Gate and_47, 16 bits wide
  assign or_38_out = and_47_out | or_37_out;  // OR_Gate or_38, 16 bits wide
  assign and_48_out = register_9_q & bit_extender_20_out;  // AND_Gate and_48, 16 bits wide
  assign or_39_out = and_48_out | or_38_out;  // OR_Gate or_39, 16 bits wide
  assign and_49_out = register_10_q & bit_extender_22_out;  // AND_Gate and_49, 16 bits wide
  assign or_40_out = and_49_out | or_39_out;  // OR_Gate or_40, 16 bits wide
  assign and_50_out = register_11_q & bit_extender_24_out;  // AND_Gate and_50, 16 bits wide
  assign or_41_out = and_50_out | or_40_out;  // OR_Gate or_41, 16 bits wide
  assign and_51_out = register_12_q & bit_extender_26_out;  // AND_Gate and_51, 16 bits wide
  assign or_42_out = and_51_out | or_41_out;  // OR_Gate or_42, 16 bits wide
  assign and_52_out = register_13_q & bit_extender_28_out;  // AND_Gate and_52, 16 bits wide
  assign or_43_out = and_52_out | or_42_out;  // OR_Gate or_43, 16 bits wide
  assign and_53_out = register_14_q & bit_extender_30_out;  // AND_Gate and_53, 16 bits wide
  assign or_44_out = and_53_out | or_43_out;  // OR_Gate or_44, 16 bits wide
  assign and_54_out = register_15_q & bit_extender_32_out;  // AND_Gate and_54, 16 bits wide
  assign or_45_out = and_54_out | or_44_out;  // OR_Gate or_45, 16 bits wide
  assign and_55_out = register_16_q & bit_extender_34_out;  // AND_Gate and_55, 16 bits wide
  assign or_46_out = and_55_out | or_45_out;  // OR_Gate or_46, 16 bits wide
  assign and_56_out = register_17_q & bit_extender_36_out;  // AND_Gate and_56, 16 bits wide
  assign or_47_out = and_56_out | or_46_out;  // OR_Gate or_47, 16 bits wide
  Multiplexer #(.width(16)) multiplexer_1 (.in0(or_31_out), .in1(register_1_q), .out(alu1_out), .sel(or_14_out));
  Multiplexer #(.width(16)) multiplexer_2 (.in0(or_47_out), .in1(register_1_q), .out(alu2_out), .sel(or_15_out));
  sixt_bit_gatekeeper sixt_bit_gatekeeper_1 (.in_1(or_9_out), .in_2(or_31_out), .out_3(data_bus_out));
  sixt_bit_gatekeeper sixt_bit_gatekeeper_2 (.in_1(or_10_out), .in_2(or_47_out), .out_3(addr_bus_out));
endmodule

module ALU (
  input  [15:0] control_bus_1,
  input  [15:0] control_bus_2,
  input  [15:0] argument1,
  input  [15:0] argument2,
  output [15:0] carry_data,
  output carry,
  output [15:0] result
);

  wire adder_1_cout, adder_2_cout, comparator_1_gt, comparator_1_lt, comparator_2_gt, comparator_2_lt,
       comparator_3_eq, comparator_4_eq, comparator_5_eq, comparator_6_eq, four_bit_eq_cmp_1_out_3,
       four_bit_eq_cmp_2_out_3, four_bit_eq_cmp_3_out_3, four_bit_eq_cmp_4_out_3, multiplexer_4_out,
       nor_1_out, not_3_out, or_1_out, or_2_out, or_4_out, or_9_out, subtractor_1_bout, subtractor_2_bout;
  wire [3:0] multiplexer_1_out, multiplexer_2_out, or_3_out;
  wire [15:0] adder_1_out, adder_2_out, and_1_out, divider_1_out, divider_1_rem, multiplexer_3_out,
       multiplexer_5_out, multiplexer_6_out, multiplier_1_cout, multiplier_1_out, not_1_out, not_2_out,
       or_5_out, or_6_out, or_7_out, or_8_out, shifter_1_out, shifter_2_out, shifter_4_out, shifter_4_out_2,
       sixt_bit_gatekeeper_1_out_3, sixt_bit_gatekeeper_2_out_3, sixt_bit_gatekeeper_3_out_3,
       sixt_bit_gatekeeper_4_out_3, sixt_bit_gatekeeper_6_out_3, sixt_bit_gatekeeper_7_out_3,
       sixt_bit_gatekeeper_8_out_3, sixt_bit_incrementer_1_out_2, subtractor_1_out, subtractor_2_out,
       xor_1_out;
  wire [31:0] and_2_out, and_3_out, bit_extender_1_out, bit_extender_2_out, shifter_3_out;
  wire [31:16] multiplexer_6_out_2;

  four_bit_eq_cmp four_bit_eq_cmp_1 (.in_1(control_bus_1[7:4]), .in_2(4'b0100), .out_3(four_bit_eq_cmp_1_out_3));
  four_bit_eq_cmp four_bit_eq_cmp_2 (.in_1(control_bus_1[7:4]), .in_2(4'b0101), .out_3(four_bit_eq_cmp_2_out_3));
  four_bit_eq_cmp four_bit_eq_cmp_3 (.in_1(control_bus_2[7:4]), .in_2(4'b0100), .out_3(four_bit_eq_cmp_3_out_3));
  four_bit_eq_cmp four_bit_eq_cmp_4 (.in_1(control_bus_2[7:4]), .in_2(4'b0101), .out_3(four_bit_eq_cmp_4_out_3));
  Multiplexer #(.width(4)) multiplexer_1 (
    .in0(4'b0000), .in1(control_bus_1[3:0]), .out(multiplexer_1_out), .sel(or_1_out));
  or or_1 (or_1_out, four_bit_eq_cmp_1_out_3, four_bit_eq_cmp_2_out_3);
  Multiplexer #(.width(4)) multiplexer_2 (
    .in0(4'b0000), .in1(control_bus_2[3:0]), .out(multiplexer_2_out), .sel(or_2_out));
  or or_2 (or_2_out, four_bit_eq_cmp_3_out_3, four_bit_eq_cmp_4_out_3);
  assign or_3_out = multiplexer_1_out | multiplexer_2_out;  // OR_Gate or_3, 4 bits wide
  or or_4 (or_4_out, or_1_out, or_2_out);
  Adder #(.width(16)) adder_1 (.a(argument1), .b(argument2), .out(adder_1_out), .cout(adder_1_cout));  // open: cin
  Subtractor #(.width(16)) subtractor_1 (
    .a(argument1), .b(argument2), .out(subtractor_1_out), .bout(subtractor_1_bout));  // open: bin
  Multiplier #(.width(16)) multiplier_1 (
    .a(argument1), .b(argument2), .out(multiplier_1_out), .cout(multiplier_1_cout));  // open: cin
  Divider #(.width(16)) divider_1 (
    .a(argument1), .b(argument2), .out(divider_1_out), .rem(divider_1_rem));  // open: upper
  Adder #(.width(16)) adder_2 (.a(argument1), .b(16'h1), .out(adder_2_out), .cout(adder_2_cout));  // open: cin
  Subtractor #(.width(16)) subtractor_2 (
    .a(argument1), .b(16'h1), .out(subtractor_2_out), .bout(subtractor_2_bout));  // open: bin
  Comparator #(.mode("unsigned"), .width(16)) comparator_1 (
    .a(argument1), .b(argument2), .gt(comparator_1_gt), .lt(comparator_1_lt));  // open: eq
  Comparator #(.width(16)) comparator_2 (
    .a(argument1), .b(argument2), .gt(comparator_2_gt), .lt(comparator_2_lt));  // open: eq
  assign and_1_out = argument1 & argument2;  // AND_Gate and_1, 16 bits wide
  assign or_5_out = argument1 | argument2;  // OR_Gate or_5, 16 bits wide
  assign xor_1_out = argument1 ^ argument2;  // XOR_Gate xor_1, 16 bits wide
  assign not_1_out = ~argument1;  // NOT_Gate not_1, 16 bits wide
  Shifter #(.width(16)) shifter_1 (.in(argument1), .\dist (4'b0001), .out(shifter_1_out));
  Shifter #(.shift("lr"), .width(16)) shifter_2 (.in(argument1), .\dist (4'b0001), .out(shifter_2_out));
  assign not_2_out = ~argument2;  // NOT_Gate not_2, 16 bits wide
  // Probe on argument1
  sixt_bit_gatekeeper sixt_bit_gatekeeper_1 (.in_1(comparator_1_gt), .in_2(16'h1), .out_3(sixt_bit_gatekeeper_1_out_3));
  sixt_bit_gatekeeper sixt_bit_gatekeeper_2 (
    .in_1(comparator_1_lt), .in_2({16{1'b1}}), .out_3(sixt_bit_gatekeeper_2_out_3));
  sixt_bit_gatekeeper sixt_bit_gatekeeper_3 (.in_1(comparator_2_gt), .in_2(16'h1), .out_3(sixt_bit_gatekeeper_3_out_3));
  sixt_bit_gatekeeper sixt_bit_gatekeeper_4 (
    .in_1(comparator_2_lt), .in_2({16{1'b1}}), .out_3(sixt_bit_gatekeeper_4_out_3));
  assign bit_extender_1_out = {{16{1'b0}}, argument1};  // Bit_Extender bit_extender_1
  Multiplexer #(.width(16)) multiplexer_3 (
    .in0(argument2), .in1(sixt_bit_incrementer_1_out_2), .out(multiplexer_3_out), .sel(argument2[15]));
  sixt_bit_incrementer sixt_bit_incrementer_1 (.in_1(not_2_out), .out_2(sixt_bit_incrementer_1_out_2));
  // Probe on argument2
  assign or_6_out = sixt_bit_gatekeeper_1_out_3 | sixt_bit_gatekeeper_2_out_3;  // OR_Gate or_6, 16 bits wide
  assign or_7_out = sixt_bit_gatekeeper_3_out_3 | sixt_bit_gatekeeper_4_out_3;  // OR_Gate or_7, 16 bits wide
  Shifter #(.width(32)) shifter_3 (.in(bit_extender_1_out), .\dist (multiplexer_3_out[4:0]), .out(shifter_3_out));
  Shifter #(.shift("lr"), .width(32)) shifter_4 (
    .in({bit_extender_1_out[15:0], bit_extender_1_out[31:16]}), .\dist (multiplexer_3_out[4:0]),
    .out({shifter_4_out, shifter_4_out_2}));
  not not_3 (not_3_out, nor_1_out);
  assign bit_extender_2_out = {{31{nor_1_out}}, nor_1_out};  // Bit_Extender bit_extender_2
  nor nor_1 (nor_1_out, multiplexer_3_out[5], multiplexer_3_out[6], multiplexer_3_out[7], multiplexer_3_out[8], multiplexer_3_out[9], multiplexer_3_out[10], multiplexer_3_out[11], multiplexer_3_out[12], multiplexer_3_out[13], multiplexer_3_out[14], multiplexer_3_out[15]);
  Multiplexer #(.select(4)) multiplexer_4 (
    .in0(adder_1_cout), .in1(subtractor_1_bout), .in2(1'b0), .in3(1'b0), .in4(adder_2_cout),
    .in5(subtractor_2_bout), .in6(1'b0), .in7(1'b0), .in8(1'b0), .in9(1'b0), .in10(1'b0), .in11(1'b0),
    .in12(1'b0), .in13(argument1[15]), .in14(argument1[0]), .in15(not_3_out), .out(multiplexer_4_out));  // open: sel
  Multiplexer #(.select(4), .width(16)) multiplexer_5 (
    .in0(adder_1_out), .in1(subtractor_1_out), .in2(multiplier_1_out), .in3(divider_1_out),
    .in4(divider_1_rem), .in5(adder_2_out), .in6(subtractor_2_out), .in7(or_6_out), .in8(or_7_out),
    .in9(and_1_out), .in10(or_5_out), .in11(xor_1_out), .in12(not_1_out), .in13(shifter_1_out),
    .in14(shifter_2_out), .in15(multiplexer_6_out), .out(multiplexer_5_out));  // open: sel
  sixt_bit_gatekeeper sixt_bit_gatekeeper_5 (.in_1(or_4_out), .in_2(multiplexer_5_out), .out_3(result));
  assign and_2_out = bit_extender_2_out & shifter_3_out;  // AND_Gate and_2, 32 bits wide
  Multiplexer #(.width(32)) multiplexer_6 (
    .in0(and_2_out), .in1(and_3_out), .out({multiplexer_6_out_2, multiplexer_6_out}), .sel(argument2[15]));
  assign and_3_out = bit_extender_2_out & {shifter_4_out_2, shifter_4_out};  // AND_Gate and_3, 32 bits wide
  Comparator #(.width(4)) comparator_3 (.a(or_3_out), .b(4'b0010), .eq(comparator_3_eq));  // open: gt, lt
  Comparator #(.width(4)) comparator_4 (.a(or_3_out), .b(4'b1111), .eq(comparator_4_eq));  // open: gt, lt
  Comparator #(.width(4)) comparator_5 (.a(or_3_out), .b(4'b0011), .eq(comparator_5_eq));  // open: gt, lt
  sixt_bit_gatekeeper sixt_bit_gatekeeper_6 (
    .in_1(comparator_3_eq), .in_2(multiplier_1_cout), .out_3(sixt_bit_gatekeeper_6_out_3));
  assign or_8_out = sixt_bit_gatekeeper_6_out_3 | sixt_bit_gatekeeper_7_out_3 | sixt_bit_gatekeeper_8_out_3;  // OR_Gate or_8, 16 bits wide
  sixt_bit_gatekeeper sixt_bit_gatekeeper_7 (
    .in_1(comparator_4_eq), .in_2(multiplexer_6_out_2), .out_3(sixt_bit_gatekeeper_7_out_3));
  sixt_bit_gatekeeper sixt_bit_gatekeeper_8 (
    .in_1(comparator_5_eq), .in_2(divider_1_rem), .out_3(sixt_bit_gatekeeper_8_out_3));
  Comparator #(.width(16)) comparator_6 (.a(or_8_out), .b({16{1'b0}}), .eq(comparator_6_eq));  // open: gt, lt
  sixt_bit_gatekeeper sixt_bit_gatekeeper_9 (.in_1(or_4_out), .in_2(or_8_out), .out_3(carry_data));
  and and_4 (carry, or_4_out, or_9_out);
  or or_9 (or_9_out, ~comparator_6_eq, multiplexer_4_out);  // OR_Gate

  // Notes on the sheet:
  //   AND (9)
  //   OR (a)
  //   XOR (b)
  //   NOT (c)
  //   << (d)
  //   >> (e)
  //   Bit shift (f)
  //   Subtract (1)
  //   Multiply (2)
  //   Divide (3)
  //   Increment (5)
  //   Decrement (6)
  //   Unsigned Cmp (7)
  //   Signed Cmp (8)
  //   Add (0)
  //   Rem (4)
endmodule

module mmio_registers (
  input  [15:0] data_in,
  input  [1:0] reg_select,
  input  write,
  input  clock,
  input  reset,
  output [15:0] value_out,
  output [15:0] out_7,
  output [15:0] out_8,
  output [15:0] out_9,
  output [15:0] out_10
);

  wire and_1_out, and_2_out, and_3_out, and_4_out, decoder_1_out0, decoder_1_out1, decoder_1_out2,
       decoder_1_out3;
  wire [15:0] sixt_bit_gatekeeper_1_out_3, sixt_bit_gatekeeper_2_out_3, sixt_bit_gatekeeper_3_out_3,
       sixt_bit_gatekeeper_4_out_3;

  Decoder #(.enable("false"), .select(2)) decoder_1 (
    .out0(decoder_1_out0), .out1(decoder_1_out1), .out2(decoder_1_out2), .out3(decoder_1_out3),
    .sel(reg_select));
  Register #(.width(16)) register_1 (.D(data_in), .en(and_1_out), .clk(clock), .Q(out_7), .clr(reset));
  and and_1 (and_1_out, decoder_1_out0, write);
  Register #(.width(16)) register_2 (.D(data_in), .en(and_2_out), .clk(clock), .Q(out_8), .clr(reset));
  and and_2 (and_2_out, decoder_1_out1, write);
  Register #(.width(16)) register_3 (.D(data_in), .en(and_3_out), .clk(clock), .Q(out_9), .clr(reset));
  and and_3 (and_3_out, decoder_1_out2, write);
  Register #(.width(16)) register_4 (.D(data_in), .en(and_4_out), .clk(clock), .Q(out_10), .clr(reset));
  and and_4 (and_4_out, decoder_1_out3, write);
  sixt_bit_gatekeeper sixt_bit_gatekeeper_1 (.in_1(decoder_1_out0), .in_2(out_7), .out_3(sixt_bit_gatekeeper_1_out_3));
  sixt_bit_gatekeeper sixt_bit_gatekeeper_2 (.in_1(decoder_1_out1), .in_2(out_8), .out_3(sixt_bit_gatekeeper_2_out_3));
  sixt_bit_gatekeeper sixt_bit_gatekeeper_3 (.in_1(decoder_1_out2), .in_2(out_9), .out_3(sixt_bit_gatekeeper_3_out_3));
  sixt_bit_gatekeeper sixt_bit_gatekeeper_4 (.in_1(decoder_1_out3), .in_2(out_10), .out_3(sixt_bit_gatekeeper_4_out_3));
  assign value_out = sixt_bit_gatekeeper_1_out_3 | sixt_bit_gatekeeper_2_out_3 | sixt_bit_gatekeeper_3_out_3 | sixt_bit_gatekeeper_4_out_3;  // OR_Gate or_1, 16 bits wide
endmodule

module control_box (
  input  [15:0] program_kounter,
  input  [15:0] control_bus_1,
  input  ctl_unit_pause,
  input  pause,
  input  resume,
  input  SI_mode,
  input  [15:0] instr,
  input  clock_in,
  input  reset_in,
  input  quick_instruction,
  output clock_out,
  output reset_out,
  output out_13
);

  wire and_1_out, and_2_out, and_3_out, and_4_out, and_5_out, and_6_out, and_7_out, and_8_out, and_9_out,
       and_11_out, and_12_out, and_13_out, and_14_out, buffer_1_out, buffer_2_out, buffer_3_out,
       buffer_4_out, buffer_5_out, buffer_6_out, buffer_7_out, buffer_8_out, buffer_9_out, buffer_10_out,
       buffer_11_out, buffer_12_out, buffer_13_out, buffer_14_out, buffer_16_out, buffer_17_out,
       buffer_18_out, buffer_19_out, buffer_20_out, buffer_21_out, buffer_22_out, buffer_23_out,
       buffer_24_out, buffer_25_out, buffer_27_out, buffer_28_out, buffer_29_out, button_1_out,
       comparator_1_lt, micro_tick_delay_25_1_out_2, micro_tick_delay_25_2_out_2,
       micro_tick_delay_100_1_out_2, micro_tick_delay_100_2_out_2, or_1_out, or_2_out, or_3_out, or_4_out,
       or_5_out, or_6_out, or_7_out, or_8_out, or_10_out, pull_resistor_2_node, s_r_ff_1_q, s_r_ff_2_q,
       s_r_ff_4_q, sixt_bit_eq_cmp_1_out_3, sixt_bit_eq_cmp_2_out_3, sixt_bit_eq_cmp_3_out_3,
       sixt_bit_eq_cmp_4_out_3;
  wire [7:0] adder_1_out, register_1_q;
  wire [15:0] pull_resistor_1_node, pull_resistor_4_node;

  Button button_1 (.out(button_1_out));
  and and_1 (and_1_out, clock_in, ~reset_in);  // AND_Gate
  buf buffer_1 (buffer_1_out, 1'b1);
  buf buffer_2 (buffer_2_out, buffer_1_out);
  buf buffer_3 (buffer_3_out, buffer_2_out);
  buf buffer_4 (buffer_4_out, buffer_5_out);
  buf buffer_5 (buffer_5_out, buffer_6_out);
  buf buffer_6 (buffer_6_out, buffer_7_out);
  buf buffer_7 (buffer_7_out, buffer_13_out);
  buf buffer_8 (buffer_8_out, buffer_4_out);
  buf buffer_9 (buffer_9_out, buffer_8_out);
  buf buffer_10 (buffer_10_out, buffer_9_out);
  Pull_Resistor #(.pull(1)) pull_resistor_1 (.node(pull_resistor_1_node));
  and and_2 (and_2_out, SI_mode, ~reset_in);  // AND_Gate
  buf buffer_11 (buffer_11_out, buffer_3_out);
  buf buffer_12 (buffer_12_out, buffer_11_out);
  buf buffer_13 (buffer_13_out, buffer_12_out);
  Pull_Resistor pull_resistor_2 (.node(pull_resistor_2_node));
  buf buffer_14 (buffer_14_out, buffer_10_out);
  buf buffer_15 (pull_resistor_2_node, buffer_14_out);
  Pull_Resistor pull_resistor_3 (.node(quick_instruction));
  or or_1 (or_1_out, quick_instruction, button_1_out);
  sixt_bit_eq_cmp sixt_bit_eq_cmp_1 (.in_1(pull_resistor_1_node), .in_2(instr), .out_3(sixt_bit_eq_cmp_1_out_3));
  and and_3 (and_3_out, 1'b1, ~pull_resistor_2_node);  // AND_Gate
  and and_4 (and_4_out, and_2_out, or_1_out);
  sixt_bit_eq_cmp sixt_bit_eq_cmp_2 (.in_1(pull_resistor_4_node), .in_2({16{1'b1}}), .out_3(sixt_bit_eq_cmp_2_out_3));
  Pull_Resistor #(.pull(1)) pull_resistor_4 (.node(pull_resistor_4_node));
  or or_2 (or_2_out, reset_in, and_3_out);
  buf buffer_16 (buffer_16_out, or_2_out);
  buf buffer_17 (buffer_17_out, buffer_16_out);
  buf buffer_18 (buffer_18_out, and_4_out);
  sixt_bit_eq_cmp sixt_bit_eq_cmp_3 (
    .in_1(program_kounter), .in_2(pull_resistor_4_node), .out_3(sixt_bit_eq_cmp_3_out_3));
  micro_tick_delay_25 micro_tick_delay_25_1 (.in_1(and_2_out), .out_2(micro_tick_delay_25_1_out_2));
  buf buffer_19 (buffer_19_out, buffer_17_out);
  buf buffer_20 (buffer_20_out, buffer_19_out);
  buf buffer_21 (buffer_21_out, buffer_20_out);
  buf buffer_22 (buffer_22_out, buffer_21_out);
  and and_5 (and_5_out, ~buffer_18_out, and_4_out);  // AND_Gate
  sixt_bit_eq_cmp sixt_bit_eq_cmp_4 (.in_1(16'h11), .in_2(control_bus_1), .out_3(sixt_bit_eq_cmp_4_out_3));
  Pull_Resistor pull_resistor_5 (.node(pause));
  or or_3 (or_3_out, pause, ctl_unit_pause);
  and and_6 (and_6_out, ~sixt_bit_eq_cmp_2_out_3, and_7_out);  // AND_Gate
  and and_7 (and_7_out, sixt_bit_eq_cmp_3_out_3, sixt_bit_eq_cmp_4_out_3);
  buf buffer_23 (buffer_23_out, buffer_22_out);
  buf buffer_24 (buffer_24_out, buffer_23_out);
  buf buffer_25 (buffer_25_out, buffer_24_out);
  buf buffer_26 (reset_out, buffer_25_out);
  or or_4 (or_4_out, and_6_out, or_3_out, sixt_bit_eq_cmp_1_out_3, micro_tick_delay_25_1_out_2);
  Pull_Resistor pull_resistor_6 (.node(ctl_unit_pause));
  and and_8 (and_8_out, or_4_out, ~buffer_28_out);  // AND_Gate
  buf buffer_27 (buffer_27_out, or_4_out);
  buf buffer_28 (buffer_28_out, buffer_27_out);
  buf buffer_29 (buffer_29_out, and_2_out);
  and and_9 (and_9_out, buffer_29_out, ~and_2_out);  // AND_Gate
  S_R_Flip_Flop s_r_ff_1 (.Q(s_r_ff_1_q), .reset(or_5_out), .preset(and_8_out));  // open: S, R, clk, Qn
  or or_5 (or_5_out, reset_out, and_9_out, resume);
  Pull_Resistor #(.pull(1)) pull_resistor_7 (.node(resume));
  S_R_Flip_Flop s_r_ff_2 (.Q(s_r_ff_2_q), .reset(ctl_unit_pause), .preset(and_5_out));  // open: S, R, clk, Qn
  or or_6 (or_6_out, ~s_r_ff_1_q, s_r_ff_2_q);  // OR_Gate
  and and_10 (out_13, ~reset_out, or_6_out);  // AND_Gate
  S_R_Flip_Flop s_r_ff_3 (.reset(or_7_out), .preset(and_8_out));  // open: S, R, clk, Q, Qn
  or or_7 (or_7_out, and_5_out, or_5_out);
  Pull_Resistor pull_resistor_8 (.node(s_r_ff_1_q));
  and and_11 (and_11_out, s_r_ff_2_q, micro_tick_delay_100_2_out_2);
  micro_tick_delay_25 micro_tick_delay_25_2 (.in_1(and_5_out), .out_2(micro_tick_delay_25_2_out_2));
  or or_8 (or_8_out, micro_tick_delay_25_2_out_2, and_11_out);
  S_R_Flip_Flop s_r_ff_4 (
    .Q(s_r_ff_4_q), .reset(micro_tick_delay_100_1_out_2), .preset(or_8_out));  // open: S, R, clk, Qn
  and and_12 (and_12_out, ~s_r_ff_1_q, and_1_out);  // AND_Gate
  and and_13 (and_13_out, micro_tick_delay_100_1_out_2, comparator_1_lt);
  and and_14 (and_14_out, s_r_ff_4_q, s_r_ff_2_q);
  micro_tick_delay_100 micro_tick_delay_100_1 (.in_1(s_r_ff_4_q), .out_2(micro_tick_delay_100_1_out_2));
  micro_tick_delay_100 micro_tick_delay_100_2 (.in_1(and_13_out), .out_2(micro_tick_delay_100_2_out_2));
  or or_9 (clock_out, and_14_out, and_12_out);
  Register register_1 (.D(adder_1_out), .clk(and_14_out), .Q(register_1_q), .clr(or_10_out));  // open: en
  Adder adder_1 (.a(register_1_q), .b(8'h1), .out(adder_1_out));  // open: cin, cout
  or or_10 (or_10_out, and_5_out, reset_out, ~comparator_1_lt);  // OR_Gate
  Comparator #(.mode("unsigned")) comparator_1 (.a(register_1_q), .b(8'h19), .lt(comparator_1_lt));  // open: gt, eq
endmodule

module control_bus_controller (
  input  [15:0] control_1,
  input  running,
  input  [15:0] control_2,
  input  clock,
  input  reset,
  output [15:0] control_bus_1,
  output [15:0] control_bus_2
);

  wire and_1_out, comparator_1_eq, comparator_2_eq, d_ff_1_q, or_1_out;
  wire [15:0] a_q, b_q, multiplexer_1_out, multiplexer_2_out, register_1_q, register_2_q;

  Register #(.trigger("falling"), .width(16)) register_1 (
    .D(control_1), .clk(clock), .Q(register_1_q), .clr(reset));  // open: en
  Register #(.width(16)) a (.D(control_1), .clk(clock), .Q(a_q), .clr(reset));  // open: en
  Register #(.width(16)) b (.D(control_2), .clk(clock), .Q(b_q), .clr(reset));  // open: en
  Register #(.trigger("falling"), .width(16)) register_2 (
    .D(control_2), .clk(clock), .Q(register_2_q), .clr(reset));  // open: en
  and and_1 (and_1_out, ~clock, or_1_out);  // AND_Gate
  Multiplexer #(.width(16)) multiplexer_1 (.in0(a_q), .in1(register_1_q), .out(multiplexer_1_out), .sel(and_1_out));
  Multiplexer #(.width(16)) multiplexer_2 (.in0(b_q), .in1(register_2_q), .out(multiplexer_2_out), .sel(and_1_out));
  D_Flip_Flop d_ff_1 (.D(running), .clk(clock), .Q(d_ff_1_q));  // open: Qn, preset, reset
  sixt_bit_gatekeeper sixt_bit_gatekeeper_1 (.in_1(d_ff_1_q), .in_2(multiplexer_1_out), .out_3(control_bus_1));
  sixt_bit_gatekeeper sixt_bit_gatekeeper_2 (.in_1(d_ff_1_q), .in_2(multiplexer_2_out), .out_3(control_bus_2));
  Comparator #(.width(16)) comparator_1 (.a(16'h67), .b(a_q), .eq(comparator_1_eq));  // open: gt, lt
  Comparator #(.width(16)) comparator_2 (.a(16'h67), .b(b_q), .eq(comparator_2_eq));  // open: gt, lt
  or or_1 (or_1_out, comparator_1_eq, comparator_2_eq);
  // Probe on control_bus_1
endmodule
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module sub_parameter_printer (
  input  [2:0] param_type,
  input  [3:0] nibble,
  input  [15:0] following,
  input  [7:0] last,
  input  [3:0] counter,
  output [7:0] ascii_out
);

  wire and_1_out, and_2_out, and_3_out, nor_1_out, nor_2_out, nor_3_out, nor_4_out, or_30_out;
  wire [7:0] and_22_out, and_23_out, and_24_out, and_25_out, and_26_out, and_27_out, and_28_out, and_29_out,
       and_30_out, and_31_out, and_32_out, and_33_out, and_34_out, and_35_out, and_36_out, and_37_out,
       and_38_out, and_39_out, and_40_out, and_41_out, and_42_out, and_43_out, and_44_out, and_45_out,
       and_46_out, and_47_out, and_48_out, and_49_out, and_50_out, and_51_out, and_52_out, and_53_out,
       and_54_out, and_55_out, and_56_out, and_57_out, and_58_out, and_59_out, and_60_out, and_61_out,
       and_62_out, and_63_out, and_64_out, and_65_out, and_66_out, and_67_out, and_68_out, and_69_out,
       and_70_out, and_71_out, and_72_out, and_73_out, and_74_out, and_75_out, and_76_out, and_77_out,
       and_78_out, and_79_out, and_80_out, and_81_out, and_82_out, and_83_out, and_84_out, and_85_out,
       and_86_out, and_87_out, and_88_out, and_89_out, and_90_out, byte_gate_1_out_3, byte_gate_2_out_3,
       byte_gate_3_out_3, byte_gate_4_out_3, byte_gate_5_out_3, byte_gate_6_out_3, byte_gate_7_out_3,
       byte_gate_8_out_3, byte_gate_9_out_3, byte_gate_10_out_3, byte_gate_11_out_3, byte_gate_12_out_3,
       byte_gate_13_out_3, byte_gate_14_out_3, byte_gate_15_out_3,
       byte_if_zero_replace_2carry_1_carry_1_carry, byte_if_zero_replace_2carry_1_out_7,
       byte_if_zero_replace_2carry_1_vanishes, byte_if_zero_replace_2carry_2_carry_1_carry,
       byte_if_zero_replace_2carry_2_out_7, byte_if_zero_replace_2carry_2_vanishes,
       byte_if_zero_replace_2carry_3_carry_1_carry, byte_if_zero_replace_2carry_3_out_7,
       byte_if_zero_replace_2carry_3_vanishes, byte_if_zero_replace_2carry_4_carry_1_carry,
       byte_if_zero_replace_2carry_4_out_7, byte_if_zero_replace_2carry_4_vanishes,
       byte_if_zero_replace_2carry_5_carry_1_carry, byte_if_zero_replace_2carry_5_out_7,
       byte_if_zero_replace_2carry_5_vanishes, byte_if_zero_replace_2carry_6_carry_1_carry,
       byte_if_zero_replace_2carry_6_out_7, byte_if_zero_replace_2carry_6_vanishes,
       byte_if_zero_replace_2carry_7_carry_1_carry, byte_if_zero_replace_2carry_7_out_7,
       byte_if_zero_replace_2carry_7_vanishes, byte_if_zero_replace_2carry_8_carry_1_carry,
       byte_if_zero_replace_2carry_8_out_7, byte_if_zero_replace_2carry_8_vanishes,
       byte_if_zero_replace_2carry_9_carry_1_carry, byte_if_zero_replace_2carry_9_out_7,
       byte_if_zero_replace_2carry_9_vanishes, byte_if_zero_replace_2carry_10_carry_1_carry,
       byte_if_zero_replace_2carry_10_out_7, byte_if_zero_replace_2carry_10_vanishes,
       byte_if_zero_replace_2carry_11_carry_1_carry, byte_if_zero_replace_2carry_11_out_7,
       byte_if_zero_replace_2carry_11_vanishes, byte_if_zero_replace_2carry_12_out_7,
       hex_digit_to_ascii_1_out_2, hex_digit_to_ascii_2_out_2, hex_digit_to_ascii_3_out_2,
       hex_digit_to_ascii_4_out_2, hex_digit_to_ascii_5_out_2, or_1_out, or_2_out, or_3_out, or_4_out,
       or_5_out, or_6_out, or_7_out, or_8_out, or_9_out, or_10_out, or_11_out, or_12_out, or_13_out,
       or_14_out, or_15_out, or_16_out, or_17_out, or_18_out, or_19_out, or_20_out, or_21_out, or_22_out,
       or_23_out, or_24_out, or_25_out, or_26_out, or_27_out, or_28_out, or_29_out;
  wire [7:7] and_20_out, and_21_out, not_1_out, not_2_out, not_3_out, not_4_out;
  wire [15:0] and_4_out;

  hex_digit_to_ascii hex_digit_to_ascii_1 (.in_1(nibble), .out_2(hex_digit_to_ascii_1_out_2));
  hex_digit_to_ascii hex_digit_to_ascii_2 (.in_1(following[3:0]), .out_2(hex_digit_to_ascii_2_out_2));
  hex_digit_to_ascii hex_digit_to_ascii_3 (.in_1(following[7:4]), .out_2(hex_digit_to_ascii_3_out_2));
  hex_digit_to_ascii hex_digit_to_ascii_4 (.in_1(following[11:8]), .out_2(hex_digit_to_ascii_4_out_2));
  hex_digit_to_ascii hex_digit_to_ascii_5 (.in_1(following[15:12]), .out_2(hex_digit_to_ascii_5_out_2));
  not not_1 (not_1_out[7], and_1_out);
  and and_1 (and_1_out, nor_1_out, and_2_out);
  nor nor_1 (nor_1_out, following[0], following[1], following[3], following[2]);
  and and_2 (and_2_out, nor_2_out, and_3_out);
  nor nor_2 (nor_2_out, following[4], following[5], following[7], following[6]);
  and and_3 (and_3_out, nor_3_out, nor_4_out);
  nor nor_3 (nor_3_out, following[8], following[9], following[11], following[10]);
  nor nor_4 (nor_4_out, following[12], following[13], following[15], following[14]);
  and and_4 (and_4_out[0], ~counter[0], ~counter[1], ~counter[2], ~counter[3]);  // AND_Gate
  and and_5 (and_4_out[1], counter[0], ~counter[1], ~counter[2], ~counter[3]);  // AND_Gate
  and and_6 (and_4_out[2], ~counter[0], counter[1], ~counter[2], ~counter[3]);  // AND_Gate
  and and_7 (and_4_out[3], counter[0], counter[1], ~counter[2], ~counter[3]);  // AND_Gate
  and and_8 (and_4_out[4], ~counter[0], ~counter[1], counter[2], ~counter[3]);  // AND_Gate
  and and_9 (and_4_out[5], counter[0], ~counter[1], counter[2], ~counter[3]);  // AND_Gate
  and and_10 (and_4_out[6], ~counter[0], counter[1], counter[2], ~counter[3]);  // AND_Gate
  and and_11 (and_4_out[7], counter[0], counter[1], counter[2], ~counter[3]);  // AND_Gate
  and and_12 (and_4_out[8], ~counter[0], ~counter[1], ~counter[2], counter[3]);  // AND_Gate
  and and_13 (and_4_out[9], counter[0], ~counter[1], ~counter[2], counter[3]);  // AND_Gate
  and and_14 (and_4_out[10], ~counter[0], counter[1], ~counter[2], counter[3]);  // AND_Gate
  and and_15 (and_4_out[11], counter[0], counter[1], ~counter[2], counter[3]);  // AND_Gate
  and and_16 (and_4_out[12], ~counter[0], ~counter[1], counter[2], counter[3]);  // AND_Gate
  and and_17 (and_4_out[13], counter[0], ~counter[1], counter[2], counter[3]);  // AND_Gate
  and and_18 (and_4_out[14], ~counter[0], counter[1], counter[2], counter[3]);  // AND_Gate
  and and_19 (and_4_out[15], counter[0], counter[1], counter[2], counter[3]);
  not not_2 (not_2_out[7], and_2_out);
  not not_3 (not_3_out[7], and_3_out);
  not not_4 (not_4_out[7], nor_4_out);
  and and_20 (and_20_out[7], ~param_type[1], ~param_type[2]);  // AND_Gate
  and and_21 (and_21_out[7], param_type[1], ~param_type[2]);  // AND_Gate
  assign or_1_out = {8{and_21_out[7]}} | {8{param_type[2]}};  // OR_Gate or_1, 8 bits wide
  assign and_22_out = {8{and_20_out[7]}} & 8'h30;  // AND_Gate and_22, 8 bits wide
  assign and_23_out = {8{and_21_out[7]}} & 8'h72;  // AND_Gate and_23, 8 bits wide
  assign and_24_out = {8{param_type[2]}} & 8'h73;  // AND_Gate and_24, 8 bits wide
  assign and_25_out = {8{and_20_out[7]}} & 8'h78;  // AND_Gate and_25, 8 bits wide
  assign and_26_out = {8{and_21_out[7]}} & hex_digit_to_ascii_1_out_2;  // AND_Gate and_26, 8 bits wide
  assign and_27_out = {8{param_type[2]}} & 8'h72;  // AND_Gate and_27, 8 bits wide
  assign and_28_out = {8{and_20_out[7]}} & hex_digit_to_ascii_5_out_2;  // AND_Gate and_28, 8 bits wide
  assign and_29_out = {8{param_type[2]}} & hex_digit_to_ascii_1_out_2;  // AND_Gate and_29, 8 bits wide
  assign and_30_out = {8{and_20_out[7]}} & hex_digit_to_ascii_4_out_2;  // AND_Gate and_30, 8 bits wide
  assign and_31_out = {8{and_20_out[7]}} & hex_digit_to_ascii_3_out_2;  // AND_Gate and_31, 8 bits wide
  assign and_32_out = {8{and_20_out[7]}} & hex_digit_to_ascii_2_out_2;  // AND_Gate and_32, 8 bits wide
  assign and_33_out = and_59_out & hex_digit_to_ascii_5_out_2;  // AND_Gate and_33, 8 bits wide
  assign or_2_out = and_33_out | and_34_out;  // OR_Gate or_2, 8 bits wide
  assign and_34_out = ~and_59_out & hex_digit_to_ascii_4_out_2;  // AND_Gate and_34, 8 bits wide
  assign and_35_out = and_59_out & hex_digit_to_ascii_4_out_2;  // AND_Gate and_35, 8 bits wide
  assign or_3_out = and_35_out | and_36_out;  // OR_Gate or_3, 8 bits wide
  assign and_36_out = ~and_59_out & hex_digit_to_ascii_3_out_2;  // AND_Gate and_36, 8 bits wide
  assign and_37_out = and_59_out & hex_digit_to_ascii_3_out_2;  // AND_Gate and_37, 8 bits wide
  assign or_4_out = and_37_out | and_38_out;  // OR_Gate or_4, 8 bits wide
  assign and_38_out = ~and_59_out & hex_digit_to_ascii_2_out_2;  // AND_Gate and_38, 8 bits wide
  assign or_5_out = and_22_out | and_23_out | and_24_out;  // OR_Gate or_5, 8 bits wide
  assign or_6_out = and_25_out | and_26_out | and_27_out;  // OR_Gate or_6, 8 bits wide
  assign or_7_out = and_28_out | and_29_out;  // OR_Gate or_7, 8 bits wide
  assign and_39_out = and_60_out & or_2_out;  // AND_Gate and_39, 8 bits wide
  assign and_40_out = ~and_60_out & hex_digit_to_ascii_3_out_2;  // AND_Gate and_40, 8 bits wide
  assign and_41_out = and_60_out & or_3_out;  // AND_Gate and_41, 8 bits wide
  assign and_42_out = ~and_60_out & hex_digit_to_ascii_2_out_2;  // AND_Gate and_42, 8 bits wide
  assign and_43_out = {8{param_type[0]}} & 8'h2a;  // AND_Gate and_43, 8 bits wide
  assign and_44_out = ~{8{param_type[0]}} & or_5_out;  // AND_Gate and_44, 8 bits wide
  assign and_45_out = {8{param_type[0]}} & or_5_out;  // AND_Gate and_45, 8 bits wide
  assign and_46_out = ~{8{param_type[0]}} & or_6_out;  // AND_Gate and_46, 8 bits wide
  assign and_47_out = {8{param_type[0]}} & or_6_out;  // AND_Gate and_47, 8 bits wide
  assign and_48_out = ~{8{param_type[0]}} & or_7_out;  // AND_Gate and_48, 8 bits wide
  assign and_49_out = {8{param_type[0]}} & or_7_out;  // AND_Gate and_49, 8 bits wide
  assign and_50_out = ~{8{param_type[0]}} & and_30_out;  // AND_Gate and_50, 8 bits wide
  assign and_51_out = {8{param_type[0]}} & and_30_out;  // AND_Gate and_51, 8 bits wide
  assign and_52_out = ~{8{param_type[0]}} & and_31_out;  // AND_Gate and_52, 8 bits wide
  assign and_53_out = {8{param_type[0]}} & and_31_out;  // AND_Gate and_53, 8 bits wide
  assign and_54_out = ~{8{param_type[0]}} & and_32_out;  // AND_Gate and_54, 8 bits wide
  assign and_55_out = {8{param_type[0]}} & and_32_out;  // AND_Gate and_55, 8 bits wide
  assign and_56_out = ~{8{param_type[0]}} & {8{1'b0}};  // AND_Gate and_56, 8 bits wide
  assign or_8_out = and_39_out | and_40_out;  // OR_Gate or_8, 8 bits wide
  assign or_9_out = and_41_out | and_42_out;  // OR_Gate or_9, 8 bits wide
  assign or_10_out = and_43_out | and_44_out;  // OR_Gate or_10, 8 bits wide
  assign or_11_out = and_45_out | and_46_out;  // OR_Gate or_11, 8 bits wide
  assign or_12_out = and_47_out | and_48_out;  // OR_Gate or_12, 8 bits wide
  assign or_13_out = and_49_out | and_50_out;  // OR_Gate or_13, 8 bits wide
  assign or_14_out = and_51_out | and_52_out;  // OR_Gate or_14, 8 bits wide
  assign or_15_out = and_53_out | and_54_out;  // OR_Gate or_15, 8 bits wide
  assign or_16_out = and_55_out | and_56_out;  // OR_Gate or_16, 8 bits wide
  assign and_57_out = and_61_out & or_8_out;  // AND_Gate and_57, 8 bits wide
  assign or_17_out = and_57_out | and_58_out;  // OR_Gate or_17, 8 bits wide
  assign and_58_out = ~and_61_out & hex_digit_to_ascii_2_out_2;  // AND_Gate and_58, 8 bits wide
  assign and_59_out = {8{not_4_out[7]}} & {8{param_type[0]}};  // AND_Gate and_59, 8 bits wide
  assign and_60_out = {8{not_3_out[7]}} & {8{param_type[0]}};  // AND_Gate and_60, 8 bits wide
  assign and_61_out = {8{not_2_out[7]}} & {8{param_type[0]}};  // AND_Gate and_61, 8 bits wide
  assign and_62_out = {8{not_1_out[7]}} & or_1_out & {8{param_type[0]}};  // AND_Gate and_62, 8 bits wide
  assign and_63_out = and_62_out & 8'h29;  // AND_Gate and_63, 8 bits wide
  assign and_64_out = ~and_62_out & last;  // AND_Gate and_64, 8 bits wide
  assign and_65_out = and_62_out & 8'h28;  // AND_Gate and_65, 8 bits wide
  assign and_66_out = ~and_62_out & or_11_out;  // AND_Gate and_66, 8 bits wide
  assign and_67_out = and_62_out & or_11_out;  // AND_Gate and_67, 8 bits wide
  assign and_68_out = ~and_62_out & or_12_out;  // AND_Gate and_68, 8 bits wide
  assign and_69_out = and_62_out & or_12_out;  // AND_Gate and_69, 8 bits wide
  assign and_70_out = ~and_62_out & or_13_out;  // AND_Gate and_70, 8 bits wide
  assign and_71_out = and_62_out & {8{param_type[2]}} & or_13_out;  // AND_Gate and_71, 8 bits wide
  assign and_72_out = and_62_out & ~{8{param_type[2]}} & 8'h2b;  // AND_Gate and_72, 8 bits wide
  assign and_73_out = ~and_62_out & or_14_out;  // AND_Gate and_73, 8 bits wide
  assign and_74_out = and_62_out & {8{param_type[2]}} & 8'h2b;  // AND_Gate and_74, 8 bits wide
  assign and_75_out = and_62_out & ~{8{param_type[2]}} & 8'h30;  // AND_Gate and_75, 8 bits wide
  assign and_76_out = ~and_62_out & or_15_out;  // AND_Gate and_76, 8 bits wide
  assign and_77_out = and_62_out & {8{param_type[2]}} & 8'h30;  // AND_Gate and_77, 8 bits wide
  assign and_78_out = and_62_out & ~{8{param_type[2]}} & 8'h78;  // AND_Gate and_78, 8 bits wide
  assign and_79_out = ~and_62_out & or_16_out;  // AND_Gate and_79, 8 bits wide
  assign and_80_out = and_62_out & {8{param_type[2]}} & 8'h78;  // AND_Gate and_80, 8 bits wide
  assign and_81_out = and_62_out & ~{8{param_type[2]}} & or_17_out;  // AND_Gate and_81, 8 bits wide
  assign and_82_out = or_17_out & and_62_out & {8{param_type[2]}};  // AND_Gate and_82, 8 bits wide
  assign and_83_out = and_62_out & ~{8{param_type[2]}} & and_61_out & or_9_out;  // AND_Gate and_83, 8 bits wide
  assign and_84_out = or_9_out & and_62_out & {8{param_type[2]}} & and_61_out;  // AND_Gate and_84, 8 bits wide
  assign and_85_out = and_62_out & ~{8{param_type[2]}} & or_4_out & and_60_out;  // AND_Gate and_85, 8 bits wide
  assign and_86_out = or_4_out & and_62_out & {8{param_type[2]}} & and_60_out;  // AND_Gate and_86, 8 bits wide
  assign and_87_out = and_62_out & ~{8{param_type[2]}} & hex_digit_to_ascii_2_out_2 & and_59_out;  // AND_Gate and_87, 8 bits wide
  assign and_88_out = hex_digit_to_ascii_2_out_2 & {8{param_type[2]}} & and_62_out & and_59_out;  // AND_Gate and_88, 8 bits wide
  assign or_18_out = and_63_out | and_64_out;  // OR_Gate or_18, 8 bits wide
  assign or_19_out = and_65_out | and_66_out;  // OR_Gate or_19, 8 bits wide
  assign or_20_out = and_67_out | and_68_out;  // OR_Gate or_20, 8 bits wide
  assign or_21_out = and_69_out | and_70_out;  // OR_Gate or_21, 8 bits wide
  assign or_22_out = and_71_out | and_72_out | and_73_out;  // OR_Gate or_22, 8 bits wide
  assign or_23_out = and_74_out | and_75_out | and_76_out;  // OR_Gate or_23, 8 bits wide
  assign or_24_out = and_77_out | and_78_out | and_79_out;  // OR_Gate or_24, 8 bits wide
  assign or_25_out = and_80_out | and_81_out;  // OR_Gate or_25, 8 bits wide
  assign or_26_out = and_82_out | and_83_out;  // OR_Gate or_26, 8 bits wide
  assign or_27_out = and_84_out | and_85_out;  // OR_Gate or_27, 8 bits wide
  assign or_28_out = and_86_out | and_87_out;  // OR_Gate or_28, 8 bits wide
  assign and_89_out = and_62_out & last;  // AND_Gate and_89, 8 bits wide
  assign and_90_out = ~and_62_out & 8'h80;  // AND_Gate and_90, 8 bits wide
  byte_if_zero_replace_2carry byte_if_zero_replace_2carry_1 (
    .if_zero(or_18_out), .carryover(or_29_out), .carryover_2(8'h80), .candidate_1(or_20_out),
    .vanishes(byte_if_zero_replace_2carry_1_vanishes),
    .carry_1_carry(byte_if_zero_replace_2carry_1_carry_1_carry), .out_7(byte_if_zero_replace_2carry_1_out_7));  // open: carry_1, carry_2
  byte_if_zero_replace_2carry byte_if_zero_replace_2carry_2 (
    .if_zero(or_18_out), .carryover(or_29_out), .carryover_2(8'h80), .candidate_1(or_21_out),
    .carry_1(byte_if_zero_replace_2carry_1_vanishes), .carry_2(byte_if_zero_replace_2carry_1_carry_1_carry),
    .vanishes(byte_if_zero_replace_2carry_2_vanishes),
    .carry_1_carry(byte_if_zero_replace_2carry_2_carry_1_carry), .out_7(byte_if_zero_replace_2carry_2_out_7));
  byte_if_zero_replace_2carry byte_if_zero_replace_2carry_3 (
    .if_zero(or_18_out), .carryover(or_29_out), .carryover_2(8'h80), .candidate_1(or_22_out),
    .carry_1(byte_if_zero_replace_2carry_2_vanishes), .carry_2(byte_if_zero_replace_2carry_2_carry_1_carry),
    .vanishes(byte_if_zero_replace_2carry_3_vanishes),
    .carry_1_carry(byte_if_zero_replace_2carry_3_carry_1_carry), .out_7(byte_if_zero_replace_2carry_3_out_7));
  byte_if_zero_replace_2carry byte_if_zero_replace_2carry_4 (
    .if_zero(or_18_out), .carryover(or_29_out), .carryover_2(8'h80), .candidate_1(or_23_out),
    .carry_1(byte_if_zero_replace_2carry_3_vanishes), .carry_2(byte_if_zero_replace_2carry_3_carry_1_carry),
    .vanishes(byte_if_zero_replace_2carry_4_vanishes),
    .carry_1_carry(byte_if_zero_replace_2carry_4_carry_1_carry), .out_7(byte_if_zero_replace_2carry_4_out_7));
  byte_if_zero_replace_2carry byte_if_zero_replace_2carry_5 (
    .if_zero(or_18_out), .carryover(or_29_out), .carryover_2(8'h80), .candidate_1(or_24_out),
    .carry_1(byte_if_zero_replace_2carry_4_vanishes), .carry_2(byte_if_zero_replace_2carry_4_carry_1_carry),
    .vanishes(byte_if_zero_replace_2carry_5_vanishes),
    .carry_1_carry(byte_if_zero_replace_2carry_5_carry_1_carry), .out_7(byte_if_zero_replace_2carry_5_out_7));
  byte_if_zero_replace_2carry byte_if_zero_replace_2carry_6 (
    .if_zero(or_18_out), .carryover(or_29_out), .carryover_2(8'h80), .candidate_1(or_25_out),
    .carry_1(byte_if_zero_replace_2carry_5_vanishes), .carry_2(byte_if_zero_replace_2carry_5_carry_1_carry),
    .vanishes(byte_if_zero_replace_2carry_6_vanishes),
    .carry_1_carry(byte_if_zero_replace_2carry_6_carry_1_carry), .out_7(byte_if_zero_replace_2carry_6_out_7));
  byte_if_zero_replace_2carry byte_if_zero_replace_2carry_7 (
    .if_zero(or_18_out), .carryover(or_29_out), .carryover_2(8'h80), .candidate_1(or_26_out),
    .carry_1(byte_if_zero_replace_2carry_6_vanishes), .carry_2(byte_if_zero_replace_2carry_6_carry_1_carry),
    .vanishes(byte_if_zero_replace_2carry_7_vanishes),
    .carry_1_carry(byte_if_zero_replace_2carry_7_carry_1_carry), .out_7(byte_if_zero_replace_2carry_7_out_7));
  byte_if_zero_replace_2carry byte_if_zero_replace_2carry_8 (
    .if_zero(or_18_out), .carryover(or_29_out), .carryover_2(8'h80), .candidate_1(or_27_out),
    .carry_1(byte_if_zero_replace_2carry_7_vanishes), .carry_2(byte_if_zero_replace_2carry_7_carry_1_carry),
    .vanishes(byte_if_zero_replace_2carry_8_vanishes),
    .carry_1_carry(byte_if_zero_replace_2carry_8_carry_1_carry), .out_7(byte_if_zero_replace_2carry_8_out_7));
  byte_if_zero_replace_2carry byte_if_zero_replace_2carry_9 (
    .if_zero(or_18_out), .carryover(or_29_out), .carryover_2(8'h80), .candidate_1(or_28_out),
    .carry_1(byte_if_zero_replace_2carry_8_vanishes), .carry_2(byte_if_zero_replace_2carry_8_carry_1_carry),
    .vanishes(byte_if_zero_replace_2carry_9_vanishes),
    .carry_1_carry(byte_if_zero_replace_2carry_9_carry_1_carry), .out_7(byte_if_zero_replace_2carry_9_out_7));
  byte_if_zero_replace_2carry byte_if_zero_replace_2carry_10 (
    .if_zero(or_18_out), .carryover(or_29_out), .carryover_2(8'h80), .candidate_1(and_88_out),
    .carry_1(byte_if_zero_replace_2carry_9_vanishes), .carry_2(byte_if_zero_replace_2carry_9_carry_1_carry),
    .vanishes(byte_if_zero_replace_2carry_10_vanishes),
    .carry_1_carry(byte_if_zero_replace_2carry_10_carry_1_carry), .out_7(byte_if_zero_replace_2carry_10_out_7));
  byte_if_zero_replace_2carry byte_if_zero_replace_2carry_11 (
    .if_zero(or_18_out), .carryover(or_29_out), .carryover_2(8'h80), .candidate_1({8{1'b0}}),
    .carry_1(byte_if_zero_replace_2carry_10_vanishes),
    .carry_2(byte_if_zero_replace_2carry_10_carry_1_carry),
    .vanishes(byte_if_zero_replace_2carry_11_vanishes),
    .carry_1_carry(byte_if_zero_replace_2carry_11_carry_1_carry), .out_7(byte_if_zero_replace_2carry_11_out_7));
  byte_if_zero_replace_2carry byte_if_zero_replace_2carry_12 (
    .if_zero(or_18_out), .carryover(or_29_out), .carryover_2(8'h80), .candidate_1({8{1'b0}}),
    .carry_1(byte_if_zero_replace_2carry_11_vanishes),
    .carry_2(byte_if_zero_replace_2carry_11_carry_1_carry), .out_7(byte_if_zero_replace_2carry_12_out_7));  // open: vanishes, carry_1_carry
  assign or_29_out = and_89_out | and_90_out;  // OR_Gate or_29, 8 bits wide
  byte_gate byte_gate_1 (.in_2(byte_if_zero_replace_2carry_5_out_7), .in_1(and_4_out[6]), .out_3(byte_gate_1_out_3));
  byte_gate byte_gate_2 (.in_2(byte_if_zero_replace_2carry_6_out_7), .in_1(and_4_out[7]), .out_3(byte_gate_2_out_3));
  byte_gate byte_gate_3 (.in_2(byte_if_zero_replace_2carry_7_out_7), .in_1(and_4_out[8]), .out_3(byte_gate_3_out_3));
  byte_gate byte_gate_4 (.in_2(byte_if_zero_replace_2carry_8_out_7), .in_1(and_4_out[9]), .out_3(byte_gate_4_out_3));
  byte_gate byte_gate_5 (.in_2(byte_if_zero_replace_2carry_9_out_7), .in_1(and_4_out[10]), .out_3(byte_gate_5_out_3));
  byte_gate byte_gate_6 (.in_2(byte_if_zero_replace_2carry_10_out_7), .in_1(and_4_out[11]), .out_3(byte_gate_6_out_3));
  byte_gate byte_gate_7 (.in_2(byte_if_zero_replace_2carry_11_out_7), .in_1(and_4_out[12]), .out_3(byte_gate_7_out_3));
  byte_gate byte_gate_8 (.in_2(byte_if_zero_replace_2carry_12_out_7), .in_1(and_4_out[13]), .out_3(byte_gate_8_out_3));
  or or_30 (or_30_out, and_4_out[14], and_4_out[15]);
  byte_gate byte_gate_9 (.in_2(8'h80), .in_1(or_30_out), .out_3(byte_gate_9_out_3));
  byte_gate byte_gate_10 (.in_2(or_10_out), .in_1(and_4_out[0]), .out_3(byte_gate_10_out_3));
  byte_gate byte_gate_11 (.in_2(or_19_out), .in_1(and_4_out[1]), .out_3(byte_gate_11_out_3));
  byte_gate byte_gate_12 (.in_2(byte_if_zero_replace_2carry_1_out_7), .in_1(and_4_out[2]), .out_3(byte_gate_12_out_3));
  byte_gate byte_gate_13 (.in_2(byte_if_zero_replace_2carry_2_out_7), .in_1(and_4_out[3]), .out_3(byte_gate_13_out_3));
  byte_gate byte_gate_14 (.in_2(byte_if_zero_replace_2carry_3_out_7), .in_1(and_4_out[4]), .out_3(byte_gate_14_out_3));
  byte_gate byte_gate_15 (.in_2(byte_if_zero_replace_2carry_4_out_7), .in_1(and_4_out[5]), .out_3(byte_gate_15_out_3));
  assign ascii_out = byte_gate_10_out_3 | byte_gate_11_out_3 | byte_gate_12_out_3 | byte_gate_13_out_3 | byte_gate_14_out_3 | byte_gate_15_out_3 | byte_gate_1_out_3 | byte_gate_2_out_3 | byte_gate_3_out_3 | byte_gate_4_out_3 | byte_gate_5_out_3 | byte_gate_6_out_3 | byte_gate_7_out_3 | byte_gate_8_out_3 | byte_gate_9_out_3;  // OR_Gate or_31, 8 bits wide
endmodule

module hex_digits_ascii (
  input  [15:0] in_1,
  output [7:0] out_2,
  output [7:0] out_3,
  output [7:0] out_4,
  output [7:0] out_5
);

  wire comparator_1_gt, comparator_2_gt, comparator_3_gt, comparator_4_gt;
  wire [7:0] adder_1_out, adder_2_out, adder_3_out, adder_4_out, adder_5_out, adder_6_out, adder_7_out,
       adder_8_out, bit_extender_1_out, bit_extender_2_out, bit_extender_3_out, bit_extender_4_out;
  wire [15:0] divider_1_out, divider_1_rem, divider_2_out, divider_2_rem, divider_3_out, divider_3_rem,
       divider_4_rem;

  Divider #(.width(16)) divider_1 (.a(in_1), .b(16'h10), .out(divider_1_out), .rem(divider_1_rem));  // open: upper
  Divider #(.width(16)) divider_2 (
    .a(divider_1_out), .b(16'h10), .out(divider_2_out), .rem(divider_2_rem));  // open: upper
  Divider #(.width(16)) divider_3 (
    .a(divider_2_out), .b(16'h10), .out(divider_3_out), .rem(divider_3_rem));  // open: upper
  Divider #(.width(16)) divider_4 (.a(divider_3_out), .b(16'h10), .rem(divider_4_rem));  // open: out, upper
  Comparator #(.mode("unsigned"), .width(4)) comparator_1 (
    .a(divider_4_rem[3:0]), .b(4'b1001), .gt(comparator_1_gt));  // open: eq, lt
  assign bit_extender_1_out = {{4{1'b0}}, divider_4_rem[3:0]};  // Bit_Extender bit_extender_1
  Comparator #(.mode("unsigned"), .width(4)) comparator_2 (
    .a(divider_3_rem[3:0]), .b(4'b1001), .gt(comparator_2_gt));  // open: eq, lt
  assign bit_extender_2_out = {{4{1'b0}}, divider_3_rem[3:0]};  // Bit_Extender bit_extender_2
  Comparator #(.mode("unsigned"), .width(4)) comparator_3 (
    .a(divider_2_rem[3:0]), .b(4'b1001), .gt(comparator_3_gt));  // open: eq, lt
  assign bit_extender_3_out = {{4{1'b0}}, divider_2_rem[3:0]};  // Bit_Extender bit_extender_3
  Comparator #(.mode("unsigned"), .width(4)) comparator_4 (
    .a(divider_1_rem[3:0]), .b(4'b1001), .gt(comparator_4_gt));  // open: eq, lt
  assign bit_extender_4_out = {{4{1'b0}}, divider_1_rem[3:0]};  // Bit_Extender bit_extender_4
  Adder adder_1 (.a(8'h30), .b(bit_extender_1_out), .out(adder_1_out));  // open: cin, cout
  Multiplexer #(.width(8)) multiplexer_1 (.in0(adder_1_out), .in1(adder_2_out), .out(out_2), .sel(comparator_1_gt));
  Adder adder_2 (.a(bit_extender_1_out), .b(8'h61), .out(adder_2_out));  // open: cin, cout
  Adder adder_3 (.a(8'h30), .b(bit_extender_2_out), .out(adder_3_out));  // open: cin, cout
  Multiplexer #(.width(8)) multiplexer_2 (.in0(adder_3_out), .in1(adder_4_out), .out(out_3), .sel(comparator_2_gt));
  Adder adder_4 (.a(bit_extender_2_out), .b(8'h61), .out(adder_4_out));  // open: cin, cout
  Adder adder_5 (.a(8'h30), .b(bit_extender_3_out), .out(adder_5_out));  // open: cin, cout
  Multiplexer #(.width(8)) multiplexer_3 (.in0(adder_5_out), .in1(adder_6_out), .out(out_4), .sel(comparator_3_gt));
  Adder adder_6 (.a(bit_extender_3_out), .b(8'h61), .out(adder_6_out));  // open: cin, cout
  Adder adder_7 (.a(8'h30), .b(bit_extender_4_out), .out(adder_7_out));  // open: cin, cout
  Multiplexer #(.width(8)) multiplexer_4 (.in0(adder_7_out), .in1(adder_8_out), .out(out_5), .sel(comparator_4_gt));
  Adder adder_8 (.a(bit_extender_4_out), .b(8'h61), .out(adder_8_out));  // open: cin, cout
endmodule

module hex_digit_to_ascii (
  input  [3:0] in_1,
  output [7:0] out_2
);

  wire [7:0] adder_1_out, adder_2_out, and_1_out, and_2_out;
  wire [7:7] comparator_1_gt;

  Comparator #(.mode("unsigned"), .width(4)) comparator_1 (
    .a(in_1), .b(4'b1001), .gt(comparator_1_gt[7]));  // open: eq, lt
  Adder adder_1 (.a(8'h30), .b({4'b0000, in_1}), .out(adder_1_out));  // open: cin, cout
  Adder adder_2 (.a({4'b0000, in_1}), .b(8'h57), .out(adder_2_out));  // open: cin, cout
  assign and_1_out = ~{8{comparator_1_gt[7]}} & adder_1_out;  // AND_Gate and_1, 8 bits wide
  assign out_2 = and_1_out | and_2_out;  // OR_Gate or_1, 8 bits wide
  assign and_2_out = {8{comparator_1_gt[7]}} & adder_2_out;  // AND_Gate and_2, 8 bits wide
endmodule

module microclock_delay (
  input  in_1,
  output out_2
);

  wire buffer_1_out, buffer_2_out, buffer_3_out, buffer_4_out, buffer_6_out, buffer_7_out, buffer_8_out,
       buffer_9_out, buffer_10_out, buffer_11_out, buffer_12_out, buffer_13_out, buffer_14_out,
       buffer_15_out, buffer_16_out, buffer_17_out, buffer_18_out, buffer_19_out, buffer_20_out,
       buffer_21_out, buffer_22_out, buffer_23_out, buffer_24_out, buffer_25_out;

  buf buffer_1 (buffer_1_out, buffer_6_out);
  buf buffer_2 (buffer_2_out, buffer_1_out);
  buf buffer_3 (buffer_3_out, buffer_14_out);
  buf buffer_4 (buffer_4_out, buffer_3_out);
  buf buffer_5 (out_2, buffer_22_out);
  buf buffer_6 (buffer_6_out, buffer_8_out);
  buf buffer_7 (buffer_7_out, buffer_9_out);
  buf buffer_8 (buffer_8_out, buffer_7_out);
  buf buffer_9 (buffer_9_out, in_1);
  buf buffer_10 (buffer_10_out, buffer_2_out);
  buf buffer_11 (buffer_11_out, buffer_12_out);
  buf buffer_12 (buffer_12_out, buffer_10_out);
  buf buffer_13 (buffer_13_out, buffer_11_out);
  buf buffer_14 (buffer_14_out, buffer_16_out);
  buf buffer_15 (buffer_15_out, buffer_17_out);
  buf buffer_16 (buffer_16_out, buffer_15_out);
  buf buffer_17 (buffer_17_out, buffer_13_out);
  buf buffer_18 (buffer_18_out, buffer_4_out);
  buf buffer_19 (buffer_19_out, buffer_20_out);
  buf buffer_20 (buffer_20_out, buffer_18_out);
  buf buffer_21 (buffer_21_out, buffer_19_out);
  buf buffer_22 (buffer_22_out, buffer_24_out);
  buf buffer_23 (buffer_23_out, buffer_25_out);
  buf buffer_24 (buffer_24_out, buffer_23_out);
  buf buffer_25 (buffer_25_out, buffer_21_out);
endmodule

module hex_digits_ascii_2 (
  input  [15:0] in_1,
  output [7:0] out_2,
  output [7:0] out_3,
  output [7:0] out_4,
  output [7:0] out_5
);

  wire comparator_1_gt, comparator_2_gt, comparator_3_gt, comparator_4_gt;
  wire [7:0] adder_1_out, adder_2_out, adder_3_out, adder_4_out, adder_5_out, adder_6_out, adder_7_out,
       adder_8_out, bit_extender_1_out, bit_extender_2_out, bit_extender_3_out, bit_extender_4_out;

  Comparator #(.mode("unsigned"), .width(4)) comparator_1 (
    .a(in_1[3:0]), .b(4'b1001), .gt(comparator_1_gt));  // open: eq, lt
  assign bit_extender_1_out = {{4{1'b0}}, in_1[3:0]};  // Bit_Extender bit_extender_1
  Comparator #(.mode("unsigned"), .width(4)) comparator_2 (
    .a(in_1[7:4]), .b(4'b1001), .gt(comparator_2_gt));  // open: eq, lt
  assign bit_extender_2_out = {{4{1'b0}}, in_1[7:4]};  // Bit_Extender bit_extender_2
  Comparator #(.mode("unsigned"), .width(4)) comparator_3 (
    .a(in_1[11:8]), .b(4'b1001), .gt(comparator_3_gt));  // open: eq, lt
  Adder adder_1 (.a(8'h30), .b(bit_extender_3_out), .out(adder_1_out));  // open: cin, cout
  assign bit_extender_3_out = {{4{1'b0}}, in_1[11:8]};  // Bit_Extender bit_extender_3
  Adder adder_2 (.a(bit_extender_3_out), .b(8'h57), .out(adder_2_out));  // open: cin, cout
  Comparator #(.mode("unsigned"), .width(4)) comparator_4 (
    .a(in_1[15:12]), .b(4'b1001), .gt(comparator_4_gt));  // open: eq, lt
  Adder adder_3 (.a(8'h30), .b(bit_extender_4_out), .out(adder_3_out));  // open: cin, cout
  assign bit_extender_4_out = {{4{1'b0}}, in_1[15:12]};  // Bit_Extender bit_extender_4
  Adder adder_4 (.a(bit_extender_4_out), .b(8'h57), .out(adder_4_out));  // open: cin, cout
  Adder adder_5 (.a(8'h30), .b(bit_extender_1_out), .out(adder_5_out));  // open: cin, cout
  Multiplexer #(.width(8)) multiplexer_1 (.in0(adder_5_out), .in1(adder_6_out), .out(out_2), .sel(comparator_1_gt));
  Adder adder_6 (.a(bit_extender_1_out), .b(8'h57), .out(adder_6_out));  // open: cin, cout
  Adder adder_7 (.a(8'h30), .b(bit_extender_2_out), .out(adder_7_out));  // open: cin, cout
  Multiplexer #(.width(8)) multiplexer_2 (.in0(adder_7_out), .in1(adder_8_out), .out(out_3), .sel(comparator_2_gt));
  Adder adder_8 (.a(bit_extender_2_out), .b(8'h57), .out(adder_8_out));  // open: cin, cout
  Multiplexer #(.width(8)) multiplexer_3 (.in0(adder_1_out), .in1(adder_2_out), .out(out_4), .sel(comparator_3_gt));
  Multiplexer #(.width(8)) multiplexer_4 (.in0(adder_3_out), .in1(adder_4_out), .out(out_5), .sel(comparator_4_gt));
endmodule

module byte_gate (
  input  in_1,
  input  [7:0] in_2,
  output [7:0] out_3
);

  assign out_3 = {8{in_1}} & in_2;  // AND_Gate and_1, 8 bits wide
endmodule

module byte_if_zero_replace_2carry (
  input  [7:0] carry_1,
  input  [7:0] carry_2,
  input  [7:0] if_zero,
  input  [7:0] carryover,
  input  [7:0] carryover_2,
  input  [7:0] candidate_1,
  output [7:0] out_7,
  output [7:0] vanishes,
  output [7:0] carry_1_carry
);

  wire [7:0] and_1_out, and_2_out, and_3_out, and_4_out, and_5_out, and_6_out, or_1_out, or_2_out;

  nor nor_1 (vanishes[7], candidate_1[7], candidate_1[6], candidate_1[5], candidate_1[4], candidate_1[3], candidate_1[2], candidate_1[1], candidate_1[0]);
  assign and_1_out = candidate_1 & ~{8{vanishes[7]}};  // AND_Gate and_1, 8 bits wide
  assign and_2_out = if_zero & {8{vanishes[7]}};  // AND_Gate and_2, 8 bits wide
  Pull_Resistor pull_resistor_1 (.node(carry_1));
  assign or_1_out = and_1_out | and_2_out;  // OR_Gate or_1, 8 bits wide
  Pull_Resistor pull_resistor_2 (.node(carry_2));
  assign and_3_out = carryover & carry_1;  // AND_Gate and_3, 8 bits wide
  assign or_2_out = and_3_out | and_4_out;  // OR_Gate or_2, 8 bits wide
  assign and_4_out = ~carry_1 & or_1_out;  // AND_Gate and_4, 8 bits wide
  assign and_5_out = carryover_2 & carry_2;  // AND_Gate and_5, 8 bits wide
  assign and_6_out = ~carry_2 & or_2_out;  // AND_Gate and_6, 8 bits wide
  assign out_7 = and_5_out | and_6_out;  // OR_Gate or_3, 8 bits wide

  assign carry_1_carry = carry_1;
  assign vanishes[6:0] = {7{vanishes[7]}};
endmodule

module five_bit_subtractor (
  input  in_1,
  input  [4:0] a,
  input  [4:0] b,
  output [4:0] out_4,
  output out_5
);

  wire and_1_out, and_2_out, and_3_out, and_4_out, and_5_out, and_6_out, and_7_out, and_8_out, and_9_out,
       and_10_out, not_2_out, xor_1_out, xor_2_out, xor_3_out, xor_4_out, xor_5_out, xor_11_out, xor_12_out,
       xor_13_out, xor_14_out;
  wire [4:0] not_1_out;

  assign not_1_out = ~b;  // NOT_Gate not_1, 5 bits wide
  xor xor_1 (xor_1_out, a[0], not_1_out[0]);
  and and_1 (and_1_out, a[0], not_1_out[0]);
  xor xor_2 (xor_2_out, a[1], not_1_out[1]);
  and and_2 (and_2_out, a[1], not_1_out[1]);
  xor xor_3 (xor_3_out, a[2], not_1_out[2]);
  and and_3 (and_3_out, a[2], not_1_out[2]);
  xor xor_4 (xor_4_out, a[3], not_1_out[3]);
  and and_4 (and_4_out, a[3], not_1_out[3]);
  xor xor_5 (xor_5_out, a[4], not_1_out[4]);
  and and_5 (and_5_out, a[4], not_1_out[4]);
  Pull_Resistor pull_resistor_1 (.node(in_1));
  not not_2 (not_2_out, in_1);
  xor xor_6 (out_4[0], xor_1_out, not_2_out);
  and and_6 (and_6_out, xor_1_out, not_2_out);
  xor xor_7 (out_4[1], xor_2_out, xor_11_out);
  and and_7 (and_7_out, xor_2_out, xor_11_out);
  xor xor_8 (out_4[2], xor_3_out, xor_12_out);
  and and_8 (and_8_out, xor_3_out, xor_12_out);
  xor xor_9 (out_4[3], xor_4_out, xor_13_out);
  and and_9 (and_9_out, xor_4_out, xor_13_out);
  xor xor_10 (out_4[4], xor_5_out, xor_14_out);
  and and_10 (and_10_out, xor_5_out, xor_14_out);
  xor xor_11 (xor_11_out, and_1_out, and_6_out);
  xor xor_12 (xor_12_out, and_2_out, and_7_out);
  xor xor_13 (xor_13_out, and_3_out, and_8_out);
  xor xor_14 (xor_14_out, and_4_out, and_9_out);
  xor xor_15 (out_5, and_5_out, and_10_out);
endmodule

module register_unstacker (
  input  enable,
  input  [15:0] unstacking_mask,
  input  [3:0] id,
  input  clk,
  input  reset,
  input  active_below,
  output active_carry,
  output [15:0] control_bus_1_out,
  output [15:0] control_bus_2_out,
  output enable_carry
);

  wire bitselector_1_out, d_ff_1_q, d_ff_3_q, d_ff_4_q, or_1_out;
  wire [1:0] d_ff_2_q;

  BitSelector #(.width(16)) bitselector_1 (.in(unstacking_mask), .out(bitselector_1_out), .sel(id));
  D_Flip_Flop d_ff_1 (.D(bitselector_1_out), .clk(enable), .Q(d_ff_1_q), .reset(d_ff_3_q));  // open: Qn, preset
  and and_1 (active_carry, or_1_out, ~d_ff_3_q);  // AND_Gate
  or or_1 (or_1_out, active_below, d_ff_2_q[1]);
  Pull_Resistor pull_resistor_1 (.node(active_below));
  D_Flip_Flop d_ff_2 (.D(d_ff_2_q[1]), .clk(clk), .Q(d_ff_2_q[0]), .reset(reset));  // open: Qn, preset
  and and_2 (d_ff_2_q[1], d_ff_1_q, enable, ~active_below);  // AND_Gate
  D_Flip_Flop d_ff_3 (.D(d_ff_2_q[0]), .clk(clk), .Q(d_ff_3_q), .reset(reset));  // open: Qn, preset
  D_Flip_Flop #(.trigger("falling")) d_ff_4 (.D(d_ff_3_q), .clk(clk), .Q(d_ff_4_q), .reset(reset));  // open: Qn, preset
  Multiplexer #(.select(2), .width(16)) multiplexer_1 (
    .in0({16{1'b0}}), .in1({16{1'b0}}), .in2(16'h1004), .in3({id, 12'h24}), .out(control_bus_1_out));  // open: sel
  Multiplexer #(.select(2), .width(16)) multiplexer_2 (
    .in0({16{1'b0}}), .in1({16{1'b0}}), .in2({16{1'b0}}), .in3(16'h1010), .out(control_bus_2_out));  // open: sel

  assign enable_carry = enable;
endmodule

module fast_printer (
  input  enable,
  input  [15:0] addr,
  input  [15:0] data_in,
  input  clk,
  input  reset,
  output active,
  output [15:0] addr_out,
  output [6:0] data_out,
  output send
);

  wire and_1_out, and_2_out, and_3_out, and_4_out, buffer_1_out, buffer_2_out, comparator_1_eq, d_ff_1_q,
       d_ff_2_q, multiplexer_2_out, not_1_out, not_2_out, or_1_out, or_2_out, or_3_out, or_4_out,
       register_1_q;
  wire [15:0] adder_1_out, multiplexer_1_out;

  Pull_Resistor pull_resistor_1 (.node(enable));
  or or_1 (or_1_out, enable, active);
  Adder #(.width(16)) adder_1 (.a(16'h1), .b(addr_out), .out(adder_1_out));  // open: cin, cout
  and and_1 (and_1_out, ~register_1_q, enable);  // AND_Gate
  and and_2 (and_2_out, ~comparator_1_eq, active);  // AND_Gate
  or or_2 (or_2_out, active, enable);
  Multiplexer #(.width(16)) multiplexer_1 (.in0(addr), .in1(adder_1_out), .out(multiplexer_1_out), .sel(active));
  Register #(.trigger("falling"), .width(1)) register_1 (
    .D(enable), .clk(clk), .Q(register_1_q), .clr(reset));  // open: en
  or or_3 (or_3_out, and_1_out, and_2_out);
  Register #(.trigger("falling"), .width(1)) register_2 (
    .D(or_3_out), .en(or_2_out), .clk(clk), .Q(active), .clr(reset));
  Register #(.trigger("falling"), .width(16)) register_3 (
    .D(multiplexer_1_out), .en(or_1_out), .clk(clk), .Q(addr_out), .clr(reset));
  not not_1 (not_1_out, clk);
  buf buffer_1 (buffer_1_out, clk);
  buf buffer_2 (buffer_2_out, not_1_out);
  D_Flip_Flop d_ff_1 (.D(clk), .clk(clk), .Q(d_ff_1_q));  // open: Qn, preset, reset
  D_Flip_Flop #(.trigger("falling")) d_ff_2 (.D(clk), .clk(clk), .Q(d_ff_2_q));  // open: Qn, preset, reset
  and and_3 (and_3_out, clk, active, ~buffer_1_out);  // AND_Gate
  or or_4 (or_4_out, and_3_out, and_4_out);
  and and_4 (and_4_out, not_1_out, active, ~buffer_2_out);  // AND_Gate
  Multiplexer multiplexer_2 (.in0(d_ff_1_q), .in1(d_ff_2_q), .out(multiplexer_2_out), .sel(clk));
  not not_2 (not_2_out, multiplexer_2_out);
  Multiplexer #(.width(7)) multiplexer_3 (.in0(data_in[6:0]), .in1(data_in[14:8]), .out(data_out), .sel(not_2_out));
  Comparator #(.width(7)) comparator_1 (.a({7{1'b0}}), .b(data_out), .eq(comparator_1_eq));  // open: gt, lt
  and and_5 (send, ~comparator_1_eq, or_4_out);  // AND_Gate
endmodule

module micro_tick_delay_100 (
  input  in_1,
  output out_2
);

  wire buffer_1_out, buffer_2_out, buffer_3_out, buffer_4_out, buffer_5_out, buffer_6_out, buffer_7_out,
       buffer_8_out, buffer_9_out, buffer_10_out, buffer_11_out, buffer_12_out, buffer_13_out, buffer_14_out,
       buffer_15_out, buffer_16_out, buffer_17_out, buffer_18_out, buffer_19_out, buffer_20_out,
       buffer_21_out, buffer_22_out, buffer_23_out, buffer_24_out, buffer_25_out, buffer_26_out,
       buffer_27_out, buffer_28_out, buffer_29_out, buffer_30_out, buffer_31_out, buffer_32_out,
       buffer_33_out, buffer_34_out, buffer_35_out, buffer_36_out, buffer_37_out, buffer_38_out,
       buffer_39_out, buffer_40_out, buffer_41_out, buffer_42_out, buffer_43_out, buffer_44_out,
       buffer_45_out, buffer_46_out, buffer_47_out, buffer_49_out, buffer_50_out, buffer_51_out,
       buffer_52_out, buffer_53_out, buffer_54_out, buffer_55_out, buffer_56_out, buffer_57_out,
       buffer_58_out, buffer_59_out, buffer_60_out, buffer_61_out, buffer_62_out, buffer_63_out,
       buffer_64_out, buffer_65_out, buffer_66_out, buffer_67_out, buffer_68_out, buffer_69_out,
       buffer_70_out, buffer_71_out, buffer_72_out, buffer_73_out, buffer_74_out, buffer_75_out,
       buffer_76_out, buffer_77_out, buffer_78_out, buffer_79_out, buffer_80_out, buffer_81_out,
       buffer_82_out, buffer_83_out, buffer_84_out, buffer_85_out, buffer_86_out, buffer_87_out,
       buffer_88_out, buffer_89_out, buffer_90_out, buffer_91_out, buffer_92_out, buffer_93_out,
       buffer_94_out, buffer_95_out, buffer_96_out, buffer_97_out, buffer_98_out, buffer_99_out,
       buffer_100_out, buffer_101_out, buffer_102_out, buffer_103_out, buffer_104_out, buffer_105_out,
       buffer_106_out, buffer_107_out, buffer_108_out, buffer_109_out, buffer_110_out, buffer_111_out,
       buffer_112_out, buffer_113_out, buffer_114_out, buffer_115_out, buffer_116_out, buffer_117_out,
       buffer_118_out, buffer_119_out, buffer_120_out, buffer_121_out, buffer_122_out, buffer_123_out,
       buffer_124_out, buffer_125_out, buffer_126_out, buffer_127_out, buffer_128_out, buffer_129_out,
       buffer_130_out, buffer_131_out, buffer_132_out, buffer_133_out, buffer_134_out, buffer_135_out,
       buffer_136_out, buffer_137_out, buffer_138_out, buffer_139_out, buffer_140_out, buffer_141_out,
       buffer_142_out, buffer_143_out, buffer_144_out, buffer_145_out, buffer_146_out, buffer_147_out,
       buffer_148_out, buffer_149_out, buffer_150_out, buffer_151_out, buffer_152_out, buffer_153_out,
       buffer_154_out, buffer_155_out, buffer_156_out, buffer_157_out, buffer_158_out, buffer_159_out,
       buffer_160_out, buffer_161_out, buffer_162_out, buffer_163_out, buffer_164_out, buffer_165_out,
       buffer_166_out, buffer_167_out, buffer_168_out, buffer_169_out, buffer_170_out, buffer_171_out,
       buffer_172_out, buffer_173_out, buffer_174_out, buffer_175_out, buffer_176_out, buffer_177_out,
       buffer_178_out, buffer_179_out, buffer_180_out, buffer_181_out, buffer_182_out, buffer_183_out,
       buffer_184_out, buffer_185_out, buffer_186_out, buffer_187_out, buffer_188_out, buffer_189_out,
       buffer_190_out, buffer_191_out, buffer_192_out, buffer_193_out, buffer_194_out, buffer_195_out,
       buffer_196_out, buffer_197_out, buffer_198_out, buffer_199_out, buffer_200_out;

  buf buffer_1 (buffer_1_out, in_1);
  buf buffer_2 (buffer_2_out, buffer_1_out);
  buf buffer_3 (buffer_3_out, buffer_4_out);
  buf buffer_4 (buffer_4_out, buffer_5_out);
  buf buffer_5 (buffer_5_out, buffer_55_out);
  buf buffer_6 (buffer_6_out, buffer_3_out);
  buf buffer_7 (buffer_7_out, buffer_6_out);
  buf buffer_8 (buffer_8_out, buffer_9_out);
  buf buffer_9 (buffer_9_out, buffer_10_out);
  buf buffer_10 (buffer_10_out, buffer_63_out);
  buf buffer_11 (buffer_11_out, buffer_8_out);
  buf buffer_12 (buffer_12_out, buffer_11_out);
  buf buffer_13 (buffer_13_out, buffer_14_out);
  buf buffer_14 (buffer_14_out, buffer_15_out);
  buf buffer_15 (buffer_15_out, buffer_71_out);
  buf buffer_16 (buffer_16_out, buffer_13_out);
  buf buffer_17 (buffer_17_out, buffer_16_out);
  buf buffer_18 (buffer_18_out, buffer_19_out);
  buf buffer_19 (buffer_19_out, buffer_20_out);
  buf buffer_20 (buffer_20_out, buffer_79_out);
  buf buffer_21 (buffer_21_out, buffer_18_out);
  buf buffer_22 (buffer_22_out, buffer_21_out);
  buf buffer_23 (buffer_23_out, buffer_24_out);
  buf buffer_24 (buffer_24_out, buffer_25_out);
  buf buffer_25 (buffer_25_out, buffer_87_out);
  buf buffer_26 (buffer_26_out, buffer_23_out);
  buf buffer_27 (buffer_27_out, buffer_26_out);
  buf buffer_28 (buffer_28_out, buffer_29_out);
  buf buffer_29 (buffer_29_out, buffer_30_out);
  buf buffer_30 (buffer_30_out, buffer_95_out);
  buf buffer_31 (buffer_31_out, buffer_28_out);
  buf buffer_32 (buffer_32_out, buffer_31_out);
  buf buffer_33 (buffer_33_out, buffer_34_out);
  buf buffer_34 (buffer_34_out, buffer_35_out);
  buf buffer_35 (buffer_35_out, buffer_103_out);
  buf buffer_36 (buffer_36_out, buffer_33_out);
  buf buffer_37 (buffer_37_out, buffer_36_out);
  buf buffer_38 (buffer_38_out, buffer_39_out);
  buf buffer_39 (buffer_39_out, buffer_40_out);
  buf buffer_40 (buffer_40_out, buffer_111_out);
  buf buffer_41 (buffer_41_out, buffer_38_out);
  buf buffer_42 (buffer_42_out, buffer_41_out);
  buf buffer_43 (buffer_43_out, buffer_44_out);
  buf buffer_44 (buffer_44_out, buffer_45_out);
  buf buffer_45 (buffer_45_out, buffer_119_out);
  buf buffer_46 (buffer_46_out, buffer_43_out);
  buf buffer_47 (buffer_47_out, buffer_46_out);
  buf buffer_48 (out_2, buffer_49_out);
  buf buffer_49 (buffer_49_out, buffer_50_out);
  buf buffer_50 (buffer_50_out, buffer_127_out);
  buf buffer_51 (buffer_51_out, buffer_2_out);
  buf buffer_52 (buffer_52_out, buffer_51_out);
  buf buffer_53 (buffer_53_out, buffer_52_out);
  buf buffer_54 (buffer_54_out, buffer_53_out);
  buf buffer_55 (buffer_55_out, buffer_56_out);
  buf buffer_56 (buffer_56_out, buffer_57_out);
  buf buffer_57 (buffer_57_out, buffer_58_out);
  buf buffer_58 (buffer_58_out, buffer_135_out);
  buf buffer_59 (buffer_59_out, buffer_7_out);
  buf buffer_60 (buffer_60_out, buffer_59_out);
  buf buffer_61 (buffer_61_out, buffer_60_out);
  buf buffer_62 (buffer_62_out, buffer_61_out);
  buf buffer_63 (buffer_63_out, buffer_64_out);
  buf buffer_64 (buffer_64_out, buffer_65_out);
  buf buffer_65 (buffer_65_out, buffer_66_out);
  buf buffer_66 (buffer_66_out, buffer_142_out);
  buf buffer_67 (buffer_67_out, buffer_12_out);
  buf buffer_68 (buffer_68_out, buffer_67_out);
  buf buffer_69 (buffer_69_out, buffer_68_out);
  buf buffer_70 (buffer_70_out, buffer_69_out);
  buf buffer_71 (buffer_71_out, buffer_72_out);
  buf buffer_72 (buffer_72_out, buffer_73_out);
  buf buffer_73 (buffer_73_out, buffer_74_out);
  buf buffer_74 (buffer_74_out, buffer_149_out);
  buf buffer_75 (buffer_75_out, buffer_17_out);
  buf buffer_76 (buffer_76_out, buffer_75_out);
  buf buffer_77 (buffer_77_out, buffer_76_out);
  buf buffer_78 (buffer_78_out, buffer_77_out);
  buf buffer_79 (buffer_79_out, buffer_80_out);
  buf buffer_80 (buffer_80_out, buffer_81_out);
  buf buffer_81 (buffer_81_out, buffer_82_out);
  buf buffer_82 (buffer_82_out, buffer_156_out);
  buf buffer_83 (buffer_83_out, buffer_22_out);
  buf buffer_84 (buffer_84_out, buffer_83_out);
  buf buffer_85 (buffer_85_out, buffer_84_out);
  buf buffer_86 (buffer_86_out, buffer_85_out);
  buf buffer_87 (buffer_87_out, buffer_88_out);
  buf buffer_88 (buffer_88_out, buffer_89_out);
  buf buffer_89 (buffer_89_out, buffer_90_out);
  buf buffer_90 (buffer_90_out, buffer_163_out);
  buf buffer_91 (buffer_91_out, buffer_27_out);
  buf buffer_92 (buffer_92_out, buffer_91_out);
  buf buffer_93 (buffer_93_out, buffer_92_out);
  buf buffer_94 (buffer_94_out, buffer_93_out);
  buf buffer_95 (buffer_95_out, buffer_96_out);
  buf buffer_96 (buffer_96_out, buffer_97_out);
  buf buffer_97 (buffer_97_out, buffer_98_out);
  buf buffer_98 (buffer_98_out, buffer_170_out);
  buf buffer_99 (buffer_99_out, buffer_32_out);
  buf buffer_100 (buffer_100_out, buffer_99_out);
  buf buffer_101 (buffer_101_out, buffer_100_out);
  buf buffer_102 (buffer_102_out, buffer_101_out);
  buf buffer_103 (buffer_103_out, buffer_104_out);
  buf buffer_104 (buffer_104_out, buffer_105_out);
  buf buffer_105 (buffer_105_out, buffer_106_out);
  buf buffer_106 (buffer_106_out, buffer_177_out);
  buf buffer_107 (buffer_107_out, buffer_37_out);
  buf buffer_108 (buffer_108_out, buffer_107_out);
  buf buffer_109 (buffer_109_out, buffer_108_out);
  buf buffer_110 (buffer_110_out, buffer_109_out);
  buf buffer_111 (buffer_111_out, buffer_112_out);
  buf buffer_112 (buffer_112_out, buffer_113_out);
  buf buffer_113 (buffer_113_out, buffer_114_out);
  buf buffer_114 (buffer_114_out, buffer_184_out);
  buf buffer_115 (buffer_115_out, buffer_42_out);
  buf buffer_116 (buffer_116_out, buffer_115_out);
  buf buffer_117 (buffer_117_out, buffer_116_out);
  buf buffer_118 (buffer_118_out, buffer_117_out);
  buf buffer_119 (buffer_119_out, buffer_120_out);
  buf buffer_120 (buffer_120_out, buffer_121_out);
  buf buffer_121 (buffer_121_out, buffer_122_out);
  buf buffer_122 (buffer_122_out, buffer_191_out);
  buf buffer_123 (buffer_123_out, buffer_47_out);
  buf buffer_124 (buffer_124_out, buffer_123_out);
  buf buffer_125 (buffer_125_out, buffer_124_out);
  buf buffer_126 (buffer_126_out, buffer_125_out);
  buf buffer_127 (buffer_127_out, buffer_128_out);
  buf buffer_128 (buffer_128_out, buffer_129_out);
  buf buffer_129 (buffer_129_out, buffer_130_out);
  buf buffer_130 (buffer_130_out, buffer_198_out);
  buf buffer_131 (buffer_131_out, buffer_54_out);
  buf buffer_132 (buffer_132_out, buffer_131_out);
  buf buffer_133 (buffer_133_out, buffer_132_out);
  buf buffer_134 (buffer_134_out, buffer_133_out);
  buf buffer_135 (buffer_135_out, buffer_136_out);
  buf buffer_136 (buffer_136_out, buffer_137_out);
  buf buffer_137 (buffer_137_out, buffer_134_out);
  buf buffer_138 (buffer_138_out, buffer_62_out);
  buf buffer_139 (buffer_139_out, buffer_138_out);
  buf buffer_140 (buffer_140_out, buffer_139_out);
  buf buffer_141 (buffer_141_out, buffer_140_out);
  buf buffer_142 (buffer_142_out, buffer_143_out);
  buf buffer_143 (buffer_143_out, buffer_144_out);
  buf buffer_144 (buffer_144_out, buffer_141_out);
  buf buffer_145 (buffer_145_out, buffer_70_out);
  buf buffer_146 (buffer_146_out, buffer_145_out);
  buf buffer_147 (buffer_147_out, buffer_146_out);
  buf buffer_148 (buffer_148_out, buffer_147_out);
  buf buffer_149 (buffer_149_out, buffer_150_out);
  buf buffer_150 (buffer_150_out, buffer_151_out);
  buf buffer_151 (buffer_151_out, buffer_148_out);
  buf buffer_152 (buffer_152_out, buffer_78_out);
  buf buffer_153 (buffer_153_out, buffer_152_out);
  buf buffer_154 (buffer_154_out, buffer_153_out);
  buf buffer_155 (buffer_155_out, buffer_154_out);
  buf buffer_156 (buffer_156_out, buffer_157_out);
  buf buffer_157 (buffer_157_out, buffer_158_out);
  buf buffer_158 (buffer_158_out, buffer_155_out);
  buf buffer_159 (buffer_159_out, buffer_86_out);
  buf buffer_160 (buffer_160_out, buffer_159_out);
  buf buffer_161 (buffer_161_out, buffer_160_out);
  buf buffer_162 (buffer_162_out, buffer_161_out);
  buf buffer_163 (buffer_163_out, buffer_164_out);
  buf buffer_164 (buffer_164_out, buffer_165_out);
  buf buffer_165 (buffer_165_out, buffer_162_out);
  buf buffer_166 (buffer_166_out, buffer_94_out);
  buf buffer_167 (buffer_167_out, buffer_166_out);
  buf buffer_168 (buffer_168_out, buffer_167_out);
  buf buffer_169 (buffer_169_out, buffer_168_out);
  buf buffer_170 (buffer_170_out, buffer_171_out);
  buf buffer_171 (buffer_171_out, buffer_172_out);
  buf buffer_172 (buffer_172_out, buffer_169_out);
  buf buffer_173 (buffer_173_out, buffer_102_out);
  buf buffer_174 (buffer_174_out, buffer_173_out);
  buf buffer_175 (buffer_175_out, buffer_174_out);
  buf buffer_176 (buffer_176_out, buffer_175_out);
  buf buffer_177 (buffer_177_out, buffer_178_out);
  buf buffer_178 (buffer_178_out, buffer_179_out);
  buf buffer_179 (buffer_179_out, buffer_176_out);
  buf buffer_180 (buffer_180_out, buffer_110_out);
  buf buffer_181 (buffer_181_out, buffer_180_out);
  buf buffer_182 (buffer_182_out, buffer_181_out);
  buf buffer_183 (buffer_183_out, buffer_182_out);
  buf buffer_184 (buffer_184_out, buffer_185_out);
  buf buffer_185 (buffer_185_out, buffer_186_out);
  buf buffer_186 (buffer_186_out, buffer_183_out);
  buf buffer_187 (buffer_187_out, buffer_118_out);
  buf buffer_188 (buffer_188_out, buffer_187_out);
  buf buffer_189 (buffer_189_out, buffer_188_out);
  buf buffer_190 (buffer_190_out, buffer_189_out);
  buf buffer_191 (buffer_191_out, buffer_192_out);
  buf buffer_192 (buffer_192_out, buffer_193_out);
  buf buffer_193 (buffer_193_out, buffer_190_out);
  buf buffer_194 (buffer_194_out, buffer_126_out);
  buf buffer_195 (buffer_195_out, buffer_194_out);
  buf buffer_196 (buffer_196_out, buffer_195_out);
  buf buffer_197 (buffer_197_out, buffer_196_out);
  buf buffer_198 (buffer_198_out, buffer_199_out);
  buf buffer_199 (buffer_199_out, buffer_200_out);
  buf buffer_200 (buffer_200_out, buffer_197_out);
endmodule

module micro_tick_delay_25 (
  input  in_1,
  output out_2
);

  wire buffer_1_out, buffer_2_out, buffer_3_out, buffer_4_out, buffer_6_out, buffer_7_out, buffer_8_out,
       buffer_9_out, buffer_10_out, buffer_11_out, buffer_12_out, buffer_13_out, buffer_14_out,
       buffer_15_out, buffer_16_out, buffer_17_out, buffer_18_out, buffer_19_out, buffer_20_out,
       buffer_21_out, buffer_22_out, buffer_23_out, buffer_24_out, buffer_25_out;

  buf buffer_1 (buffer_1_out, buffer_6_out);
  buf buffer_2 (buffer_2_out, buffer_1_out);
  buf buffer_3 (buffer_3_out, buffer_14_out);
  buf buffer_4 (buffer_4_out, buffer_3_out);
  buf buffer_5 (out_2, buffer_22_out);
  buf buffer_6 (buffer_6_out, buffer_8_out);
  buf buffer_7 (buffer_7_out, buffer_9_out);
  buf buffer_8 (buffer_8_out, buffer_7_out);
  buf buffer_9 (buffer_9_out, in_1);
  buf buffer_10 (buffer_10_out, buffer_2_out);
  buf buffer_11 (buffer_11_out, buffer_12_out);
  buf buffer_12 (buffer_12_out, buffer_10_out);
  buf buffer_13 (buffer_13_out, buffer_11_out);
  buf buffer_14 (buffer_14_out, buffer_16_out);
  buf buffer_15 (buffer_15_out, buffer_17_out);
  buf buffer_16 (buffer_16_out, buffer_15_out);
  buf buffer_17 (buffer_17_out, buffer_13_out);
  buf buffer_18 (buffer_18_out, buffer_4_out);
  buf buffer_19 (buffer_19_out, buffer_20_out);
  buf buffer_20 (buffer_20_out, buffer_18_out);
  buf buffer_21 (buffer_21_out, buffer_19_out);
  buf buffer_22 (buffer_22_out, buffer_24_out);
  buf buffer_23 (buffer_23_out, buffer_25_out);
  buf buffer_24 (buffer_24_out, buffer_23_out);
  buf buffer_25 (buffer_25_out, buffer_21_out);
endmodule
